// Logisim project cpu7400.circ as structural Verilog: 13 circuits, main circuit Computer
module Computer (
  input  reset
);

  wire and_1_out, clk, d_ff_1_q, decoder_1_out0, decoder_1_out1, selKeyboard, selRAM, selScreen, writeM;
  wire [6:0] keyboard_1_data;
  wire [14:0] addrM, cpu_1_pc;
  wire [15:0] hack_video_display_1_p6, inM, outM, rom_1_data;
  wire [15:15] keyboard_1_avail;

  Clock clock_1 (.out(clk));
  Decoder #(.select(2), .enable("false")) decoder_1 (
    .out0(decoder_1_out0), .out1(decoder_1_out1), .out2(selScreen), .out3(selKeyboard), .sel(addrM[14:13]));
  ROM #(.addrWidth(15), .dataWidth(16)) rom_1 (.addr(cpu_1_pc), .data(rom_1_data), .sel(1'b1));
  Memory memory_1 (.outM(outM), .clk(clk), .addrM(addrM), .load(writeM), .inM(inM), .selRAM(selRAM));
  or or_1 (selRAM, decoder_1_out0, decoder_1_out1);
  // Probe on inM
  CPU cpu_1 (
    .inM(inM), .instruction(rom_1_data), .reset(reset), .clk(clk), .outM(outM), .writeM(writeM),
    .addressM(addrM), .pc(cpu_1_pc));
  // Probe on outM
  // Probe on addrM
  // Probe on cpu_1_pc
  and and_1 (and_1_out, selScreen, writeM);
  D_Flip_Flop d_ff_1 (.clk(clk), .D(writeM), .Q(d_ff_1_q));  // open: Qn, preset, en, reset
  Keyboard keyboard_1 (
    .clk(d_ff_1_q), .re(selKeyboard), .clr(reset), .avail(keyboard_1_avail[15]), .data(keyboard_1_data));
  assign inM = and_1_out ? hack_video_display_1_p6 : 16'bz;  // Controlled_Buffer controlled_buffer_1
  // HACK_Video_Display hack_video_display_1: pin names not known; wires that end beside it: reset, clk, and_1_out, addrM[12:0], outM, hack_video_display_1_p6
  assign inM = selKeyboard ? {keyboard_1_avail[15], {8{1'b0}}, keyboard_1_data} : 16'bz;  // Controlled_Buffer controlled_buffer_2

  // Notes on the sheet:
  //   ROM
  //   contents of rom_1 (hex, n*v repeats v):
  //   64 ec10 10 e308 11 efc8 11 fc10 10 fc20 e308 10 fdc8 11 fc10 f098 6 e305 2 ec10 12 e308 13 e308 4000
  //   ec10 1010 e090 14 e308 10 ea88 11 efc8 13 fc10 15 e308 11 fc10 14 fc20 f548 10 fdc8 11 f098 37 e305
  //   14 fdc8 10 ea88 11 efc8 15 fc98 26 e305 12 fc10 13 f088 13 fc10 15 e308 11 fc10 14 fc20 f548 20 ec10
  //   14 f1d8 4000 e4d0 96 e304 15 fc98 43 e305 12 fc10 13 f088 13 fc10 15 e308 11 fc10 14 fc20 f548 10
  //   fc98 6b e303 14 fc88 f ec10 10 e308 10 fc10 64 e0a0 fc10 11 e308 15 fc98 5c e305 12 fc10 13 f088 13
  //   fc10 15 e308 11 fc10 14 fc20 f548 20 ec10 14 f098 6000 e4d0 96 e303 15 fc98 7e e305 12 fc10 13 f088
  //   22 ea87 96 ea87
  //   Keyboard
endmodule

module CPU (
  input  reset,
  input  clk,
  input  [15:0] inM,
  input  [15:0] instruction,
  output [15:0] outM,
  output writeM,
  output [14:0] addressM,
  output [14:0] pc
);

  wire and_2_out, and_3_out, and_4_out, isAinstruction, isJump__unused, isPositive__unused, loadA, loadD,
       loadPC, ng, not_2_out, not_3_out, PCinc, selInstrOrALU, zr;
  wire [15:0] mux16_1_out, outAorM, outDReg;
  wire [15:15] outAReg, outPC;

  Mux16 mux16_1 (.sel(selInstrOrALU), .a(instruction), .b(outM), .out(mux16_1_out));
  not not_1 (isAinstruction, instruction[15]);
  Register A (.load(loadA), .clk(clk), .a(mux16_1_out), .out_4({outAReg[15], addressM}));
  Register D (.load(loadD), .clk(clk), .a(outM), .out_4(outDReg));
  PC pc_1 (.load(loadPC), .inc(PCinc), .reset(reset), .clk(clk), .a({outAReg[15], addressM}), .out_6({outPC[15], pc}));
  Mux16 mux16_2 (.sel(instruction[12]), .a({outAReg[15], addressM}), .b(inM), .out(outAorM));
  not not_2 (not_2_out, zr);
  and and_1 (isPositive__unused, not_2_out, not_3_out);
  not not_3 (not_3_out, ng);
  and and_2 (and_2_out, isPositive__unused, instruction[0]);
  and and_3 (and_3_out, zr, instruction[1]);
  and and_4 (and_4_out, ng, instruction[2]);
  and and_5 (selInstrOrALU, instruction[5], instruction[15]);
  and and_6 (loadD, instruction[4], instruction[15]);
  and and_7 (writeM, instruction[15], instruction[3]);
  or or_1 (isJump__unused, and_2_out, and_3_out, and_4_out);
  or or_2 (loadA, isAinstruction, selInstrOrALU);
  and and_8 (loadPC, instruction[15], isJump__unused);
  not not_4 (PCinc, loadPC);
  ALU alu_1 (
    .x(outDReg), .y(outAorM), .zx(instruction[11]), .nx(instruction[10]), .zy(instruction[9]),
    .ny(instruction[8]), .f(instruction[7]), .no(instruction[6]), .out(outM), .zr(zr), .ng(ng));

  // Other names for the same wires on the sheet: destIsM = instruction[3]; destIsD = instruction[4];
  //   destIsA = instruction[5]; no = instruction[6]; f = instruction[7]; ny = instruction[8]; zy = instruction[9];
  //   nx = instruction[10]; zx = instruction[11]; aBit = instruction[12]; isCinstruction = instruction[15];
  //   outALU[15:0] = outM; outAReg[14:0] = addressM; outPC[14:0] = pc

  // Notes on the sheet:
  //   CONTROL LOGIC
endmodule

// RAM
module Memory (
  input  [15:0] outM,
  input  selRAM,
  input  clk,
  input  load,
  input  [14:0] addrM,
  output [15:0] inM
);

  wire selBank0, selBank1, selBank2, selBank3, selBank4, selBank5, selBank6, selBank7;
  wire [7:0] ram_1_data, ram_2_data, ram_3_data, ram_4_data, ram_5_data, ram_6_data, ram_7_data, ram_8_data,
       ram_9_data, ram_10_data, ram_11_data, ram_12_data, ram_13_data, ram_14_data, ram_15_data, ram_16_data;

  Decoder #(.select(3), .enable("false")) decoder_1 (
    .out0(selBank0), .out1(selBank1), .out2(selBank2), .out3(selBank3), .out4(selBank4), .out5(selBank5),
    .out6(selBank6), .out7(selBank7), .sel(addrM[13:11]));
  RAM #(.addrWidth(11), .bus("separate")) ram_1 (
    .addr(addrM[10:0]), .din(outM[15:8]), .data(ram_1_data), .str(load), .sel(selBank0), .clk(clk),
    .ld(1'b1), .clr(1'b0));
  assign inM[15:8] = selBank0 ? ram_1_data : 8'bz;  // Controlled_Buffer controlled_buffer_1
  assign inM[15:8] = selBank1 ? ram_2_data : 8'bz;  // Controlled_Buffer controlled_buffer_2
  RAM #(.addrWidth(11), .bus("separate")) ram_2 (
    .addr(addrM[10:0]), .din(outM[15:8]), .data(ram_2_data), .str(load), .sel(selBank1), .clk(clk),
    .ld(1'b1), .clr(1'b0));
  RAM #(.addrWidth(11), .bus("separate")) ram_3 (
    .addr(addrM[10:0]), .din(outM[15:8]), .data(ram_3_data), .str(load), .sel(selBank2), .clk(clk),
    .ld(1'b1), .clr(1'b0));
  assign inM[15:8] = selBank2 ? ram_3_data : 8'bz;  // Controlled_Buffer controlled_buffer_3
  assign inM[15:8] = selBank3 ? ram_4_data : 8'bz;  // Controlled_Buffer controlled_buffer_4
  RAM #(.addrWidth(11), .bus("separate")) ram_4 (
    .addr(addrM[10:0]), .din(outM[15:8]), .data(ram_4_data), .str(load), .sel(selBank3), .clk(clk),
    .ld(1'b1), .clr(1'b0));
  RAM #(.addrWidth(11), .bus("separate")) ram_5 (
    .addr(addrM[10:0]), .din(outM[15:8]), .data(ram_5_data), .str(load), .sel(selBank4), .clk(clk),
    .ld(1'b1), .clr(1'b0));
  assign inM[15:8] = selBank4 ? ram_5_data : 8'bz;  // Controlled_Buffer controlled_buffer_5
  assign inM[15:8] = selBank5 ? ram_6_data : 8'bz;  // Controlled_Buffer controlled_buffer_6
  RAM #(.addrWidth(11), .bus("separate")) ram_6 (
    .addr(addrM[10:0]), .din(outM[15:8]), .data(ram_6_data), .str(load), .sel(selBank5), .clk(clk),
    .ld(1'b1), .clr(1'b0));
  RAM #(.addrWidth(11), .bus("separate")) ram_7 (
    .addr(addrM[10:0]), .din(outM[15:8]), .data(ram_7_data), .str(load), .sel(selBank6), .clk(clk),
    .ld(1'b1), .clr(1'b0));
  assign inM[15:8] = selBank6 ? ram_7_data : 8'bz;  // Controlled_Buffer controlled_buffer_7
  RAM #(.addrWidth(11), .bus("separate")) ram_8 (
    .addr(addrM[10:0]), .din(outM[15:8]), .data(ram_8_data), .str(load), .sel(selBank7), .clk(clk),
    .ld(1'b1), .clr(1'b0));
  assign inM[15:8] = selBank7 ? ram_8_data : 8'bz;  // Controlled_Buffer controlled_buffer_8
  RAM #(.addrWidth(11), .bus("separate")) ram_9 (
    .addr(addrM[10:0]), .din(outM[7:0]), .data(ram_9_data), .str(load), .sel(selBank0), .clk(clk), .ld(1'b1),
    .clr(1'b0));
  assign inM[7:0] = selBank0 ? ram_9_data : 8'bz;  // Controlled_Buffer controlled_buffer_9
  assign inM[7:0] = selBank1 ? ram_10_data : 8'bz;  // Controlled_Buffer controlled_buffer_10
  RAM #(.addrWidth(11), .bus("separate")) ram_10 (
    .addr(addrM[10:0]), .din(outM[7:0]), .data(ram_10_data), .str(load), .sel(selBank1), .clk(clk),
    .ld(1'b1), .clr(1'b0));
  RAM #(.addrWidth(11), .bus("separate")) ram_11 (
    .addr(addrM[10:0]), .din(outM[7:0]), .data(ram_11_data), .str(load), .sel(selBank2), .clk(clk),
    .ld(1'b1), .clr(1'b0));
  assign inM[7:0] = selBank2 ? ram_11_data : 8'bz;  // Controlled_Buffer controlled_buffer_11
  assign inM[7:0] = selBank3 ? ram_12_data : 8'bz;  // Controlled_Buffer controlled_buffer_12
  RAM #(.addrWidth(11), .bus("separate")) ram_12 (
    .addr(addrM[10:0]), .din(outM[7:0]), .data(ram_12_data), .str(load), .sel(selBank3), .clk(clk),
    .ld(1'b1), .clr(1'b0));
  RAM #(.addrWidth(11), .bus("separate")) ram_13 (
    .addr(addrM[10:0]), .din(outM[7:0]), .data(ram_13_data), .str(load), .sel(selBank4), .clk(clk),
    .ld(1'b1), .clr(1'b0));
  assign inM[7:0] = selBank4 ? ram_13_data : 8'bz;  // Controlled_Buffer controlled_buffer_13
  RAM #(.addrWidth(11), .bus("separate")) ram_14 (
    .addr(addrM[10:0]), .din(outM[7:0]), .data(ram_14_data), .str(load), .sel(selBank5), .clk(clk),
    .ld(1'b1), .clr(1'b0));
  assign inM[7:0] = selBank5 ? ram_14_data : 8'bz;  // Controlled_Buffer controlled_buffer_14
  RAM #(.addrWidth(11), .bus("separate")) ram_15 (
    .addr(addrM[10:0]), .din(outM[7:0]), .data(ram_15_data), .str(load), .sel(selBank6), .clk(clk),
    .ld(1'b1), .clr(1'b0));
  assign inM[7:0] = selBank6 ? ram_15_data : 8'bz;  // Controlled_Buffer controlled_buffer_15
  RAM #(.addrWidth(11), .bus("separate")) ram_16 (
    .addr(addrM[10:0]), .din(outM[7:0]), .data(ram_16_data), .str(load), .sel(selBank7), .clk(clk),
    .ld(1'b1), .clr(1'b0));
  assign inM[7:0] = selBank7 ? ram_16_data : 8'bz;  // Controlled_Buffer controlled_buffer_16

  // Other names for the same wires on the sheet: writeM = load
endmodule

module ALU (
  input  [15:0] x,
  input  [15:0] y,
  input  zx,
  input  nx,
  input  zy,
  input  ny,
  input  f,
  input  no,
  output [15:0] out,
  output zr,
  output ng
);

  wire or8way_1_out, or8way_2_out;
  wire [15:0] add16_1_out_3, and16_1_out_3, bit_extender_1_out, bit_extender_2_out, bit_extender_3_out,
       mux16_1_out, mux16_2_out, mux16_3_out, xor16_1_out_3, xor16_2_out_3;

  assign bit_extender_1_out = {{15{nx}}, nx};  // Bit_Extender bit_extender_1
  Mux16 mux16_1 (.sel(zx), .a(x), .b({16{1'b0}}), .out(mux16_1_out));
  assign bit_extender_2_out = {{15{ny}}, ny};  // Bit_Extender bit_extender_2
  Mux16 mux16_2 (.sel(zy), .a(y), .b({16{1'b0}}), .out(mux16_2_out));
  XOR16 xor16_1 (.a(bit_extender_1_out), .b(mux16_1_out), .out_3(xor16_1_out_3));
  XOR16 xor16_2 (.a(bit_extender_2_out), .b(mux16_2_out), .out_3(xor16_2_out_3));
  And16 and16_1 (.a(xor16_1_out_3), .b(xor16_2_out_3), .out_3(and16_1_out_3));
  Add16 add16_1 (.a(xor16_1_out_3), .b(xor16_2_out_3), .out_3(add16_1_out_3));
  Mux16 mux16_3 (.sel(f), .a(and16_1_out_3), .b(add16_1_out_3), .out(mux16_3_out));
  assign bit_extender_3_out = {{15{no}}, no};  // Bit_Extender bit_extender_3
  XOR16 xor16_3 (.a(bit_extender_3_out), .b(mux16_3_out), .out_3({ng, out[14:0]}));
  Or8Way or8way_1 (.in(out[7:0]), .out(or8way_1_out));
  Or8Way or8way_2 (.in({ng, out[14:8]}), .out(or8way_2_out));
  nor nor_1 (zr, or8way_1_out, or8way_2_out);

  assign out[15] = ng;

  // Notes on the sheet:
  //   x input
  //   y input
endmodule

module PC (
  input  load,
  input  inc,
  input  reset,
  input  clk,
  input  [15:0] a,
  output [15:0] out_6
);

  wire load_t, n74163_1__15__tc, n74163_2__15__tc, n74163_3__15__tc, reset_t, tc3;

  not not_1 (load_t, load);
  not not_2 (reset_t, reset);
  _74163 u_74163_1 (
    ._1__nMR(reset_t), ._2__CP(clk), ._3__D0(a[0]), ._4__D1(a[1]), ._5__D2(a[2]), ._6__D3(a[3]),
    ._7__CEP(inc), ._8__GND(1'b0), ._16__Vcc(1'b1), ._15__TC(n74163_1__15__tc), ._14__Q0(out_6[0]),
    ._13__Q1(out_6[1]), ._12__Q2(out_6[2]), ._11__O3(out_6[3]), ._10__CET(inc), ._9__nPE(load_t));
  _74163 u_74163_2 (
    ._1__nMR(reset_t), ._2__CP(clk), ._3__D0(a[4]), ._4__D1(a[5]), ._5__D2(a[6]), ._6__D3(a[7]),
    ._8__GND(1'b0), ._16__Vcc(1'b1), ._15__TC(n74163_2__15__tc), ._14__Q0(out_6[4]), ._13__Q1(out_6[5]),
    ._12__Q2(out_6[6]), ._11__O3(out_6[7]), ._10__CET(n74163_1__15__tc), ._9__nPE(load_t));  // open: _7__CEP
  _74163 u_74163_3 (
    ._1__nMR(reset_t), ._2__CP(clk), ._3__D0(a[8]), ._4__D1(a[9]), ._5__D2(a[10]), ._6__D3(a[11]),
    ._8__GND(1'b0), ._16__Vcc(1'b1), ._15__TC(n74163_3__15__tc), ._14__Q0(out_6[8]), ._13__Q1(out_6[9]),
    ._12__Q2(out_6[10]), ._11__O3(out_6[11]), ._10__CET(n74163_2__15__tc), ._9__nPE(load_t));  // open: _7__CEP
  _74163 u_74163_4 (
    ._1__nMR(reset_t), ._2__CP(clk), ._3__D0(a[12]), ._4__D1(a[13]), ._5__D2(a[14]), ._6__D3(a[15]),
    ._8__GND(1'b0), ._16__Vcc(1'b1), ._15__TC(tc3), ._14__Q0(out_6[12]), ._13__Q1(out_6[13]),
    ._12__Q2(out_6[14]), ._11__O3(out_6[15]), ._10__CET(n74163_3__15__tc), ._9__nPE(load_t));  // open: _7__CEP

  // Other names for the same wires on the sheet: out0 = out_6[0]; out1 = out_6[1]; out2 = out_6[2]; out3 = out_6[3];
  //   out4 = out_6[4]; out5 = out_6[5]; out6 = out_6[6]; out7 = out_6[7]; out8 = out_6[8]; out9 = out_6[9];
  //   out10 = out_6[10]; out11 = out_6[11]; out12 = out_6[12]; out13 = out_6[13]; out14 = out_6[14];
  //   out15 = out_6[15]
endmodule

module Register (
  input  load,
  input  clk,
  input  [15:0] a,
  output [15:0] out_4
);

  wire clkAndLastLoad, d_ff_1_q, not_1_out;

  not not_1 (not_1_out, clk);
  D_Flip_Flop #(.trigger("high")) d_ff_1 (.clk(not_1_out), .D(load), .Q(d_ff_1_q));  // open: Qn, preset, en, reset
  and and_1 (clkAndLastLoad, d_ff_1_q, clk);
  IC_74273 ic_74273_1 (
    .CLK(clkAndLastLoad), .D1(a[0]), .D2(a[1]), .D3(a[2]), .D4(a[3]), .D5(a[4]), .D6(a[5]), .D7(a[6]),
    .D8(a[7]), .Y1(out_4[0]), .Y2(out_4[1]), .Y3(out_4[2]), .Y4(out_4[3]), .Y6(out_4[5]), .Y7(out_4[6]),
    .Y8(out_4[7]), .Y5(out_4[4]), .Vcc(1'b1), .GND(1'b0));  // open: CLR
  IC_74273 ic_74273_2 (
    .CLK(clkAndLastLoad), .D1(a[8]), .D2(a[9]), .D3(a[10]), .D4(a[11]), .D5(a[12]), .D6(a[13]), .D7(a[14]),
    .D8(a[15]), .Y1(out_4[8]), .Y2(out_4[9]), .Y3(out_4[10]), .Y4(out_4[11]), .Y6(out_4[13]), .Y7(out_4[14]),
    .Y8(out_4[15]), .Y5(out_4[12]), .Vcc(1'b1), .GND(1'b0));  // open: CLR

  // Other names for the same wires on the sheet: out0 = out_4[0]; out1 = out_4[1]; out2 = out_4[2]; out3 = out_4[3];
  //   out4 = out_4[4]; out5 = out_4[5]; out6 = out_4[6]; out7 = out_4[7]; out8 = out_4[8]; out9 = out_4[9];
  //   out10 = out_4[10]; out11 = out_4[11]; out12 = out_4[12]; out13 = out_4[13]; out14 = out_4[14];
  //   out15 = out_4[15]
endmodule

// Add
module Add16 (
  input  [15:0] a,
  input  [15:0] b,
  output [15:0] out_3
);

  wire n7483_1__14__cout, n7483_2__14__cout, n7483_3__14__cout, n7483_4__14__cout;

  _7483 u_7483_1 (
    ._1__A4(a[3]), ._2__S3(out_3[2]), ._3__A3(a[2]), ._4__B3(b[2]), ._5__Vcc(1'b1), ._6__S2(out_3[1]),
    ._7__B2(b[1]), ._8__A2(a[1]), ._16__B4(b[3]), ._15__S4(out_3[3]), ._14__Cout(n7483_1__14__cout),
    ._13__Cin(1'b0), ._12__GND(1'b0), ._11__B1(b[0]), ._10__A1(a[0]), ._9__S1(out_3[0]));
  _7483 u_7483_2 (
    ._1__A4(a[7]), ._2__S3(out_3[6]), ._3__A3(a[6]), ._4__B3(b[6]), ._5__Vcc(1'b1), ._6__S2(out_3[5]),
    ._7__B2(b[5]), ._8__A2(a[5]), ._16__B4(b[7]), ._15__S4(out_3[7]), ._14__Cout(n7483_2__14__cout),
    ._13__Cin(n7483_1__14__cout), ._12__GND(1'b0), ._11__B1(b[4]), ._10__A1(a[4]), ._9__S1(out_3[4]));
  _7483 u_7483_3 (
    ._1__A4(a[11]), ._2__S3(out_3[10]), ._3__A3(a[10]), ._4__B3(b[10]), ._5__Vcc(1'b1), ._6__S2(out_3[9]),
    ._7__B2(b[9]), ._8__A2(a[9]), ._16__B4(b[11]), ._15__S4(out_3[11]), ._14__Cout(n7483_3__14__cout),
    ._13__Cin(n7483_2__14__cout), ._12__GND(1'b0), ._11__B1(b[8]), ._10__A1(a[8]), ._9__S1(out_3[8]));
  _7483 u_7483_4 (
    ._1__A4(a[15]), ._2__S3(out_3[14]), ._3__A3(a[14]), ._4__B3(b[14]), ._5__Vcc(1'b1), ._6__S2(out_3[13]),
    ._7__B2(b[13]), ._8__A2(a[13]), ._16__B4(b[15]), ._15__S4(out_3[15]), ._14__Cout(n7483_4__14__cout),
    ._13__Cin(n7483_3__14__cout), ._12__GND(n7483_4__14__cout), ._11__B1(b[12]), ._10__A1(a[12]),
    ._9__S1(out_3[12]));
  // also tied to GND on the sheet: n7483_4__14__cout

  // Other names for the same wires on the sheet: out0 = out_3[0]; out1 = out_3[1]; out2 = out_3[2]; out3 = out_3[3];
  //   out4 = out_3[4]; out5 = out_3[5]; out6 = out_3[6]; out7 = out_3[7]; out8 = out_3[8]; out9 = out_3[9];
  //   out10 = out_3[10]; out11 = out_3[11]; out12 = out_3[12]; out13 = out_3[13]; out14 = out_3[14];
  //   out15 = out_3[15]
endmodule

module Mux4Way16 (
  input  [15:0] a,
  input  [15:0] b,
  input  [15:0] c,
  input  [15:0] d,
  input  [1:0] sel,
  output [15:0] out
);

  wire [15:0] mux16_1_out, mux16_2_out;

  Mux16 mux16_1 (.sel(sel[0]), .a(a), .b(b), .out(mux16_1_out));
  Mux16 mux16_2 (.sel(sel[0]), .a(c), .b(d), .out(mux16_2_out));
  Mux16 mux16_3 (.sel(sel[1]), .a(mux16_1_out), .b(mux16_2_out), .out(out));
endmodule

module DMux4Way (
  input  in,
  input  [1:0] sel,
  output a,
  output b,
  output c,
  output d
);

  Demultiplexer #(.select(2), .enable("false")) demultiplexer_1 (
    .out0(a), .out1(b), .out2(c), .out3(d), .in(in), .sel(sel));
endmodule

// Mux
module Mux16 (
  input  sel,
  input  [15:0] a,
  input  [15:0] b,
  output [15:0] out
);

  _74157 u_74157_1 (
    ._1__S(sel), ._2__A1(a[0]), ._3__B1(b[0]), ._4__Y1(out[0]), ._5__A2(a[1]), ._6__B2(b[1]),
    ._7__Y2(out[1]), ._8__GND(1'b0), ._16__Vcc(1'b1), ._15__G(1'b0), ._14__A4(a[3]), ._13__B4(b[3]),
    ._12__Y4(out[3]), ._11__A3(a[2]), ._10__B3(b[2]), ._9__Y3(out[2]));
  _74157 u_74157_2 (
    ._1__S(sel), ._2__A1(a[4]), ._3__B1(b[4]), ._4__Y1(out[4]), ._5__A2(a[5]), ._6__B2(b[5]),
    ._7__Y2(out[5]), ._8__GND(1'b0), ._16__Vcc(1'b1), ._15__G(1'b0), ._14__A4(a[7]), ._13__B4(b[7]),
    ._12__Y4(out[7]), ._11__A3(a[6]), ._10__B3(b[6]), ._9__Y3(out[6]));
  _74157 u_74157_3 (
    ._1__S(sel), ._2__A1(a[8]), ._3__B1(b[8]), ._4__Y1(out[8]), ._5__A2(a[9]), ._6__B2(b[9]),
    ._7__Y2(out[9]), ._8__GND(1'b0), ._16__Vcc(1'b1), ._15__G(1'b0), ._14__A4(a[11]), ._13__B4(b[11]),
    ._12__Y4(out[11]), ._11__A3(a[10]), ._10__B3(b[10]), ._9__Y3(out[10]));
  _74157 u_74157_4 (
    ._1__S(sel), ._2__A1(a[12]), ._3__B1(b[12]), ._4__Y1(out[12]), ._5__A2(a[13]), ._6__B2(b[13]),
    ._7__Y2(out[13]), ._8__GND(1'b0), ._16__Vcc(1'b1), ._15__G(1'b0), ._14__A4(a[15]), ._13__B4(b[15]),
    ._12__Y4(out[15]), ._11__A3(a[14]), ._10__B3(b[14]), ._9__Y3(out[14]));
endmodule

// And
module And16 (
  input  [15:0] a,
  input  [15:0] b,
  output [15:0] out_3
);

  _7408 u_7408_1 (
    ._1__1A(a[0]), ._2__1B(b[0]), ._3__1Y(out_3[0]), ._4__2A(a[1]), ._5__2B(b[1]), ._6__2Y(out_3[1]),
    ._7__GND(1'b0), ._14__Vcc(1'b1), ._13__4B(b[3]), ._12__4A(a[3]), ._11__4Y(out_3[3]), ._10__3B(b[2]),
    ._9__3A(a[2]), ._8__3Y(out_3[2]));
  _7408 u_7408_2 (
    ._1__1A(a[4]), ._2__1B(b[4]), ._3__1Y(out_3[4]), ._4__2A(a[5]), ._5__2B(b[5]), ._6__2Y(out_3[5]),
    ._7__GND(1'b0), ._14__Vcc(1'b1), ._13__4B(b[7]), ._12__4A(a[7]), ._11__4Y(out_3[7]), ._10__3B(b[6]),
    ._9__3A(a[6]), ._8__3Y(out_3[6]));
  _7408 u_7408_3 (
    ._1__1A(a[8]), ._2__1B(b[8]), ._3__1Y(out_3[8]), ._4__2A(a[9]), ._5__2B(b[9]), ._6__2Y(out_3[9]),
    ._7__GND(1'b0), ._14__Vcc(1'b1), ._13__4B(b[11]), ._12__4A(a[11]), ._11__4Y(out_3[11]), ._10__3B(b[10]),
    ._9__3A(a[10]), ._8__3Y(out_3[10]));
  _7408 u_7408_4 (
    ._1__1A(a[12]), ._2__1B(b[12]), ._3__1Y(out_3[12]), ._4__2A(a[13]), ._5__2B(b[13]), ._6__2Y(out_3[13]),
    ._7__GND(1'b0), ._14__Vcc(1'b1), ._13__4B(b[15]), ._12__4A(a[15]), ._11__4Y(out_3[15]), ._10__3B(b[14]),
    ._9__3A(a[14]), ._8__3Y(out_3[14]));

  // Other names for the same wires on the sheet: out0 = out_3[0]; out1 = out_3[1]; out2 = out_3[2]; out3 = out_3[3];
  //   out4 = out_3[4]; out5 = out_3[5]; out6 = out_3[6]; out7 = out_3[7]; out8 = out_3[8]; out9 = out_3[9];
  //   out10 = out_3[10]; out11 = out_3[11]; out12 = out_3[12]; out13 = out_3[13]; out14 = out_3[14];
  //   out15 = out_3[15]
endmodule

// Or
module Or8Way (
  input  [7:0] in,
  output out
);

  wire n7432_1__3__1y, n7432_1__6__2y, n7432_1__8__3y, n7432_1__11__4y, n7432_2__3__1y, n7432_2__11__4y;

  _7432 u_7432_1 (
    ._1__1A(in[0]), ._2__1B(in[1]), ._3__1Y(n7432_1__3__1y), ._4__2A(in[2]), ._5__2B(in[3]),
    ._6__2Y(n7432_1__6__2y), ._7__GND(1'b0), ._14__Vcc(1'b1), ._13__4B(in[7]), ._12__4A(in[6]),
    ._11__4Y(n7432_1__11__4y), ._10__3B(in[5]), ._9__3A(in[4]), ._8__3Y(n7432_1__8__3y));
  _7432 u_7432_2 (
    ._1__1A(n7432_1__6__2y), ._2__1B(n7432_1__3__1y), ._3__1Y(n7432_2__3__1y), ._4__2A(n7432_2__3__1y),
    ._5__2B(n7432_2__11__4y), ._6__2Y(out), ._7__GND(1'b0), ._14__Vcc(1'b1), ._13__4B(n7432_1__8__3y),
    ._12__4A(n7432_1__11__4y), ._11__4Y(n7432_2__11__4y));  // open: _10__3B, _9__3A, _8__3Y
endmodule

// XOR
module XOR16 (
  input  [15:0] a,
  input  [15:0] b,
  output [15:0] out_3
);

  _7486 u_7486_1 (
    ._1__1A(a[0]), ._2__1B(b[0]), ._3__1Y(out_3[0]), ._4__2A(a[1]), ._5__2B(b[1]), ._6__2Y(out_3[1]),
    ._7__GND(1'b0), ._14__Vcc(1'b1), ._13__4B(b[3]), ._12__4A(a[3]), ._11__4Y(out_3[3]), ._10__3B(b[2]),
    ._9__3A(a[2]), ._8__3Y(out_3[2]));
  _7486 u_7486_2 (
    ._1__1A(a[4]), ._2__1B(b[4]), ._3__1Y(out_3[4]), ._4__2A(a[5]), ._5__2B(b[5]), ._6__2Y(out_3[5]),
    ._7__GND(1'b0), ._14__Vcc(1'b1), ._13__4B(b[7]), ._12__4A(a[7]), ._11__4Y(out_3[7]), ._10__3B(b[6]),
    ._9__3A(a[6]), ._8__3Y(out_3[6]));
  _7486 u_7486_3 (
    ._1__1A(a[8]), ._2__1B(b[8]), ._3__1Y(out_3[8]), ._4__2A(a[9]), ._5__2B(b[9]), ._6__2Y(out_3[9]),
    ._7__GND(1'b0), ._14__Vcc(1'b1), ._13__4B(b[11]), ._12__4A(a[11]), ._11__4Y(out_3[11]), ._10__3B(b[10]),
    ._9__3A(a[10]), ._8__3Y(out_3[10]));
  _7486 u_7486_4 (
    ._1__1A(a[12]), ._2__1B(b[12]), ._3__1Y(out_3[12]), ._4__2A(a[13]), ._5__2B(b[13]), ._6__2Y(out_3[13]),
    ._7__GND(1'b0), ._14__Vcc(1'b1), ._13__4B(b[15]), ._12__4A(a[15]), ._11__4Y(out_3[15]), ._10__3B(b[14]),
    ._9__3A(a[14]), ._8__3Y(out_3[14]));

  // Other names for the same wires on the sheet: out0 = out_3[0]; out1 = out_3[1]; out2 = out_3[2]; out3 = out_3[3];
  //   out4 = out_3[4]; out5 = out_3[5]; out6 = out_3[6]; out7 = out_3[7]; out8 = out_3[8]; out9 = out_3[9];
  //   out10 = out_3[10]; out11 = out_3[11]; out12 = out_3[12]; out13 = out_3[13]; out14 = out_3[14];
  //   out15 = out_3[15]
endmodule
