// Logisim project simulation_v3.circ as structural Verilog: 13 circuits, main circuit main
module main (
  input  reset,
  output [14:0] pc,
  output [15:0] inM,
  output [15:0] instruction,
  output [15:0] outM,
  output [14:0] addressM
);

  wire clock_1_out, cpu_1_p20;

  Clock clock_1 (.out(clock_1_out));
  // CPU cpu_1: pin names not known; wires that end beside it: instruction, reset, clock_1_out, instruction, instruction, instruction, instruction, instruction, instruction, instruction, instruction, instruction, instruction, instruction, instruction, instruction, instruction, instruction, addressM, cpu_1_p20, inM, pc
  ROM #(.addrWidth(15), .dataWidth(16)) rom_1 (.addr(pc), .data(instruction));  // open: sel
  MEMORY memory_1 (.load(cpu_1_p20), .out(inM), .in(instruction), .CLK(clock_1_out), .address(addressM));

  assign outM = instruction;

  // Notes on the sheet:
  //   If the ROM instr. is a C-instruction
  //   then this register will hold the value
  //   to be written to memory.
  //   If the ROM instr. is a A-instruction 
  //   then this register will hold the address 
  //   in the next clock cycle.
  //   contents of rom_1 (hex, n*v repeats v):
  //   10 ea88 11 ea88 10 fc10 1 f4d0 12 e303 0 fc10 11 f088 10 fdc8 4 ea87 11 fc10 2 e308 12 ea87
endmodule

module CPU (
  input  in_1,
  input  in_2,
  input  in_3,
  input  in_4,
  input  in_5,
  input  in_6,
  input  in_7,
  input  in_8,
  input  in_9,
  input  in_10,
  input  in_11,
  input  in_12,
  input  in_13,
  input  in_14,
  input  in_15,
  input  in_16,
  input  [15:0] instruction,
  input  [15:0] inM,
  input  clk,
  input  reset,
  output [15:0] outM,
  output writeM,
  output [14:0] pc,
  output [14:0] addressM
);

  wire addressM_0, addressM_1, addressM_2, addressM_3, addressM_4, addressM_5, addressM_6, addressM_7,
       addressM_8, addressM_9, addressM_10, addressM_11, addressM_12, addressM_13, addressM_14, Ainstruction,
       ALUout_0, ALUout_1, ALUout_2, ALUout_3, ALUout_4, ALUout_5, ALUout_6, ALUout_7, ALUout_8, ALUout_9,
       ALUout_10, ALUout_11, ALUout_12, ALUout_13, ALUout_14, ALUout_15, ALUtoA, AMout_0, AMout_1, AMout_2,
       AMout_3, AMout_4, AMout_5, AMout_6, AMout_7, AMout_8, AMout_9, AMout_10, AMout_11, AMout_12, AMout_13,
       AMout_14, AMout_15, and_2_out, and_3_out, and_4_out, and_5_out, and_6_out, and_7_out, Aout_0, Aout_1,
       Aout_2, Aout_3, Aout_4, Aout_5, Aout_6, Aout_7, Aout_8, Aout_9, Aout_10, Aout_11, Aout_12, Aout_13,
       Aout_14, Aout_15, Aregin_0, Aregin_1, Aregin_2, Aregin_3, Aregin_4, Aregin_5, Aregin_6, Aregin_7,
       Aregin_8, Aregin_9, Aregin_10, Aregin_11, Aregin_12, Aregin_13, Aregin_14, Aregin_15, Cinstruction,
       CLK_t, Dout_0, Dout_1, Dout_2, Dout_3, Dout_4, Dout_5, Dout_6, Dout_7, Dout_8, Dout_9, Dout_10,
       Dout_11, Dout_12, Dout_13, Dout_14, Dout_15, GND, GND_t, GND_t_t, inM_0, inM_1, inM_2, inM_3, inM_4,
       inM_5, inM_6, inM_7, inM_8, inM_9, inM_10, inM_11, inM_12, inM_13, inM_14, inM_15, jeq, jgt, jle, jlt,
       jumpToA, loadA, loadD, NC, NC_t, NC_t_t, NC_t_t_t, NGout, not_1_out, not_2_out, not_3_out, not_4_out,
       not_5_out, or_1_out, or_2_out, or_3_out, or_4_out, or_5_out, or_6_out, or_7_out, or_8_out, or_9_out,
       or_10_out, or_11_out, or_12_out, or_13_out, or_14_out, or_15_out, or_16_out, or_17_out, or_18_out,
       or_19_out, or_20_out, or_21_out, or_22_out, or_23_out, or_24_out, or_25_out, or_26_out, or_27_out,
       or_28_out, or_29_out, or_30_out, or_31_out, or_32_out, or_33_out, or_34_out, outM_0, outM_1, outM_2,
       outM_3, outM_4, outM_5, outM_6, outM_7, outM_8, outM_9, outM_10, outM_11, outM_12, outM_13, outM_14,
       PCinc, PCload, positive, pull_resistor_1_node, pull_resistor_2_node, pull_resistor_3_node,
       pull_resistor_4_node, pull_resistor_5_node, pull_resistor_6_node, pull_resistor_7_node,
       pull_resistor_8_node, pull_resistor_9_node, pull_resistor_10_node, pull_resistor_11_node,
       pull_resistor_12_node, pull_resistor_13_node, pull_resistor_14_node, pull_resistor_15_node,
       pull_resistor_16_node, pull_resistor_17_node, pull_resistor_18_node, pull_resistor_19_node,
       pull_resistor_20_node, pull_resistor_21_node, pull_resistor_22_node, pull_resistor_23_node,
       pull_resistor_24_node, pull_resistor_25_node, pull_resistor_26_node, pull_resistor_27_node,
       pull_resistor_28_node, pull_resistor_29_node, pull_resistor_30_node, Vcc, Vcc_t, Vcc_t_t, Vcc_t_t_t,
       writeM_t, zeroOrNeg, ZRout;
  wire [3:0] multiplexer_4_out, multiplexer_8_out, multiplexer_12_out, multiplexer_16_out,
       multiplexer_20_out, multiplexer_24_out, multiplexer_28_out, multiplexer_32_out;
  wire [15:0] register_20_q;
  wire [15:15] pc_1_out, register_13_q;

  mux4 mux4_1 (
    .not_E(NC_t), .I_0a(Aout_0), .I_1a(inM_0), .I_0b(Aout_1), .I_1b(inM_1), .I_0c(Aout_2), .I_1c(inM_2),
    .I_0d(Aout_3), .I_1d(inM_3), .Z_a(AMout_0), .Z_b(AMout_1), .Z_c(AMout_2), .Z_d(AMout_3), .S(in_13),
    .Vcc(Vcc_t), .GND(GND));
  mux4 mux4_2 (
    .not_E(NC_t), .I_0a(Aout_4), .I_1a(inM_4), .I_0b(Aout_5), .I_1b(inM_5), .I_0c(Aout_6), .I_1c(inM_6),
    .I_0d(Aout_7), .I_1d(inM_7), .Z_a(AMout_4), .Z_b(AMout_5), .Z_c(AMout_6), .Z_d(AMout_7), .S(in_13),
    .Vcc(Vcc_t), .GND(GND));
  not6 not6_1 (
    ._1A(in_16), ._2A(Ainstruction), ._1Y(Ainstruction), ._2Y(Cinstruction));  // open: _3A, _4A, _5A, _6A, _3Y, _4Y, _5Y, _6Y, Vcc, GND
  mux4 mux4_3 (
    .not_E(NC), .I_0a(Aout_8), .I_1a(inM_8), .I_0b(Aout_9), .I_1b(inM_9), .I_0c(Aout_10), .I_1c(inM_10),
    .I_0d(Aout_11), .I_1d(inM_11), .Z_a(AMout_8), .Z_b(AMout_9), .Z_c(AMout_10), .Z_d(AMout_11), .S(in_13),
    .Vcc(Vcc), .GND(GND_t));
  mux4 mux4_4 (
    .not_E(NC_t_t), .I_0a(Aout_12), .I_1a(inM_12), .I_0b(Aout_13), .I_1b(inM_13), .I_0c(Aout_14),
    .I_1c(inM_14), .I_0d(Aout_15), .I_1d(inM_15), .Z_a(AMout_12), .Z_b(AMout_13), .Z_c(AMout_14),
    .Z_d(AMout_15), .S(in_13), .Vcc(Vcc_t_t), .GND(GND_t));
  and4 and4_1 (
    .Vcc(Vcc_t), .GND(GND), .A1(Cinstruction), .A2(Cinstruction), .B1(in_6), .B2(in_5), .S1(ALUtoA),
    .S2(loadD));  // open: A3, A4, B3, B4, S3, S4
  and and_1 (writeM, instruction[3], not_2_out);
  mux4 mux4_5 (
    .not_E(NC_t_t_t), .I_0a(in_1), .I_1a(ALUout_0), .I_0b(in_2), .I_1b(ALUout_1), .I_0c(in_3),
    .I_1c(ALUout_2), .I_0d(in_4), .I_1d(ALUout_3), .Z_a(Aregin_0), .Z_b(Aregin_1), .Z_c(Aregin_2),
    .Z_d(Aregin_3), .S(ALUtoA), .Vcc(Vcc_t_t_t), .GND(GND_t_t));
  mux4 mux4_6 (
    .not_E(NC_t_t_t), .I_0a(in_5), .I_1a(ALUout_4), .I_0b(in_6), .I_1b(ALUout_5), .I_0c(in_7),
    .I_1c(ALUout_6), .I_0d(in_8), .I_1d(ALUout_7), .Z_a(Aregin_4), .Z_b(Aregin_5), .Z_c(Aregin_6),
    .Z_d(Aregin_7), .S(ALUtoA), .Vcc(Vcc_t_t_t), .GND(GND_t_t));
  register8 register8_1 (
    .Vcc(Vcc_t_t_t), .GND(GND_t_t), .D0(ALUout_0), .D1(ALUout_1), .D2(ALUout_2), .D3(ALUout_3),
    .D4(ALUout_4), .D5(ALUout_5), .D6(ALUout_6), .D7(ALUout_7), .Q0(Dout_0), .Q1(Dout_1), .Q2(Dout_2),
    .Q3(Dout_3), .Q4(Dout_4), .Q5(Dout_5), .Q6(Dout_6), .Q7(Dout_7), .not_E(loadD), .CLK(CLK_t));
  register8 register8_2 (
    .Vcc(Vcc_t_t_t), .GND(GND_t_t), .D0(ALUout_8), .D1(ALUout_9), .D2(ALUout_10), .D3(ALUout_11),
    .D4(ALUout_12), .D5(ALUout_13), .D6(ALUout_14), .D7(ALUout_15), .Q0(Dout_8), .Q1(Dout_9), .Q2(Dout_10),
    .Q3(Dout_11), .Q4(Dout_12), .Q5(Dout_13), .Q6(Dout_14), .Q7(Dout_15), .not_E(loadD), .CLK(CLK_t));
  not not_1 (not_1_out, instruction[15]);
  not not_2 (not_2_out, not_1_out);
  or or_1 (or_1_out, not_1_out, and_2_out);
  and and_2 (and_2_out, not_2_out, instruction[6]);
  mux4 mux4_7 (
    .not_E(NC_t_t_t), .I_0a(in_9), .I_1a(ALUout_8), .I_0b(in_10), .I_1b(ALUout_9), .I_0c(in_11),
    .I_1c(ALUout_10), .I_0d(in_12), .I_1d(ALUout_11), .Z_a(Aregin_8), .Z_b(Aregin_9), .Z_c(Aregin_10),
    .Z_d(Aregin_11), .S(ALUtoA), .Vcc(Vcc_t_t_t), .GND(GND_t_t));
  mux4 mux4_8 (
    .not_E(NC_t_t_t), .I_0a(in_13), .I_1a(ALUout_12), .I_0b(in_14), .I_1b(ALUout_13), .I_0c(in_15),
    .I_1c(ALUout_14), .I_0d(in_16), .I_1d(ALUout_15), .Z_a(Aregin_12), .Z_b(Aregin_13), .Z_c(Aregin_14),
    .Z_d(Aregin_15), .S(ALUtoA), .Vcc(Vcc_t_t_t), .GND(GND_t_t));
  Pull_Resistor pull_resistor_1 (.node(pull_resistor_1_node));
  or4 or4_1 (
    .Vcc(Vcc_t_t_t), .GND(GND_t_t), .A1(pull_resistor_1_node), .B1(Aout_0), .A2(pull_resistor_3_node),
    .B2(Aout_1), .A3(pull_resistor_4_node), .B3(Aout_2), .A4(pull_resistor_2_node), .B4(Aout_3),
    .Y1(addressM_0), .Y2(addressM_1), .Y3(addressM_2), .Y4(addressM_3));
  Pull_Resistor pull_resistor_2 (.node(pull_resistor_2_node));
  Pull_Resistor pull_resistor_3 (.node(pull_resistor_3_node));
  Pull_Resistor pull_resistor_4 (.node(pull_resistor_4_node));
  Pull_Resistor pull_resistor_5 (.node(pull_resistor_5_node));
  or4 or4_2 (
    .Vcc(Vcc_t_t_t), .GND(GND_t_t), .A1(pull_resistor_5_node), .B1(Aout_4), .A2(pull_resistor_7_node),
    .B2(Aout_5), .A3(pull_resistor_8_node), .B3(Aout_6), .A4(pull_resistor_6_node), .B4(Aout_7),
    .Y1(addressM_4), .Y2(addressM_5), .Y3(addressM_6), .Y4(addressM_7));
  Pull_Resistor pull_resistor_6 (.node(pull_resistor_6_node));
  Pull_Resistor pull_resistor_7 (.node(pull_resistor_7_node));
  Pull_Resistor pull_resistor_8 (.node(pull_resistor_8_node));
  Pull_Resistor pull_resistor_9 (.node(pull_resistor_9_node));
  or4 or4_3 (
    .Vcc(Vcc_t_t_t), .GND(GND_t_t), .A1(pull_resistor_9_node), .B1(Aout_8), .A2(pull_resistor_11_node),
    .B2(Aout_9), .A3(pull_resistor_12_node), .B3(Aout_10), .A4(pull_resistor_10_node), .B4(Aout_11),
    .Y1(addressM_8), .Y2(addressM_9), .Y3(addressM_10), .Y4(addressM_11));
  Pull_Resistor pull_resistor_10 (.node(pull_resistor_10_node));
  Pull_Resistor pull_resistor_11 (.node(pull_resistor_11_node));
  Pull_Resistor pull_resistor_12 (.node(pull_resistor_12_node));
  Pull_Resistor pull_resistor_13 (.node(pull_resistor_13_node));
  or4 or4_4 (
    .Vcc(Vcc_t_t_t), .GND(GND_t_t), .A1(pull_resistor_13_node), .B1(Aout_12), .A2(pull_resistor_14_node),
    .B2(Aout_13), .A3(pull_resistor_15_node), .B3(Aout_14), .Y1(addressM_12), .Y2(addressM_13),
    .Y3(addressM_14));  // open: A4, B4, Y4
  Pull_Resistor pull_resistor_14 (.node(pull_resistor_14_node));
  Pull_Resistor pull_resistor_15 (.node(pull_resistor_15_node));
  Multiplexer #(.enable("false")) multiplexer_1 (
    .in0(instruction[3]), .in1(outM[3]), .out(multiplexer_4_out[3]), .sel(and_2_out));
  Multiplexer #(.enable("false")) multiplexer_2 (
    .in0(instruction[2]), .in1(outM[2]), .out(multiplexer_4_out[2]), .sel(and_2_out));
  Multiplexer #(.enable("false")) multiplexer_3 (
    .in0(instruction[1]), .in1(outM[1]), .out(multiplexer_4_out[1]), .sel(and_2_out));
  Multiplexer #(.enable("false")) multiplexer_4 (
    .in0(instruction[0]), .in1(outM[0]), .out(multiplexer_4_out[0]), .sel(and_2_out));
  Pull_Resistor pull_resistor_16 (.node(pull_resistor_16_node));
  Pull_Resistor pull_resistor_17 (.node(pull_resistor_17_node));
  Pull_Resistor pull_resistor_18 (.node(pull_resistor_18_node));
  Pull_Resistor pull_resistor_19 (.node(pull_resistor_19_node));
  Pull_Resistor pull_resistor_20 (.node(pull_resistor_20_node));
  Pull_Resistor pull_resistor_21 (.node(pull_resistor_21_node));
  Pull_Resistor pull_resistor_22 (.node(pull_resistor_22_node));
  Pull_Resistor pull_resistor_23 (.node(pull_resistor_23_node));
  or4 or4_5 (.A1(Ainstruction), .B1(ALUtoA), .Y1(loadA));  // open: Vcc, GND, A2, B2, A3, B3, A4, B4, Y2, Y3, Y4
  or4 or4_6 (
    .Vcc(Vcc_t_t_t), .GND(GND_t_t), .A1(pull_resistor_16_node), .B1(ALUout_0), .A2(pull_resistor_17_node),
    .B2(ALUout_1), .A3(pull_resistor_25_node), .B3(ALUout_2), .A4(pull_resistor_24_node), .B4(ALUout_3),
    .Y1(outM_0), .Y2(outM_1), .Y3(outM_2), .Y4(outM_3));
  Pull_Resistor pull_resistor_24 (.node(pull_resistor_24_node));
  Pull_Resistor pull_resistor_25 (.node(pull_resistor_25_node));
  or4 or4_7 (
    .Vcc(Vcc_t_t_t), .GND(GND_t_t), .A1(pull_resistor_18_node), .B1(ALUout_4), .A2(pull_resistor_19_node),
    .B2(ALUout_5), .A3(pull_resistor_27_node), .B3(ALUout_6), .A4(pull_resistor_26_node), .B4(ALUout_7),
    .Y1(outM_4), .Y2(outM_5), .Y3(outM_6), .Y4(outM_7));
  Pull_Resistor pull_resistor_26 (.node(pull_resistor_26_node));
  Pull_Resistor pull_resistor_27 (.node(pull_resistor_27_node));
  or4 or4_8 (
    .Vcc(Vcc_t_t_t), .GND(GND_t_t), .A1(pull_resistor_20_node), .B1(ALUout_8), .A2(pull_resistor_21_node),
    .B2(ALUout_9), .A3(pull_resistor_29_node), .B3(ALUout_10), .A4(pull_resistor_28_node), .B4(ALUout_11),
    .Y1(outM_8), .Y2(outM_9), .Y3(outM_10), .Y4(outM_11));
  Pull_Resistor pull_resistor_28 (.node(pull_resistor_28_node));
  Pull_Resistor pull_resistor_29 (.node(pull_resistor_29_node));
  or4 or4_9 (
    .Vcc(Vcc_t_t_t), .GND(GND_t_t), .A1(pull_resistor_22_node), .B1(ALUout_12), .A2(pull_resistor_23_node),
    .B2(ALUout_13), .A3(pull_resistor_30_node), .B3(ALUout_14), .Y1(outM_12), .Y2(outM_13), .Y3(outM_14));  // open: A4, B4, Y4
  Pull_Resistor pull_resistor_30 (.node(pull_resistor_30_node));
  Multiplexer #(.enable("false")) multiplexer_5 (
    .in0(instruction[7]), .in1(outM[7]), .out(multiplexer_8_out[3]), .sel(and_2_out));
  Multiplexer #(.enable("false")) multiplexer_6 (
    .in0(instruction[6]), .in1(outM[6]), .out(multiplexer_8_out[2]), .sel(and_2_out));
  Multiplexer #(.enable("false")) multiplexer_7 (
    .in0(instruction[5]), .in1(outM[5]), .out(multiplexer_8_out[1]), .sel(and_2_out));
  Multiplexer #(.enable("false")) multiplexer_8 (
    .in0(instruction[4]), .in1(outM[4]), .out(multiplexer_8_out[0]), .sel(and_2_out));
  and and_3 (and_3_out, not_2_out, instruction[4]);
  register8 register8_3 (
    .Vcc(Vcc_t_t_t), .GND(GND_t_t), .D0(Aregin_0), .D1(Aregin_1), .D2(Aregin_2), .D3(Aregin_3),
    .D4(Aregin_4), .D5(Aregin_5), .D6(Aregin_6), .D7(Aregin_7), .Q0(Aout_0), .Q1(Aout_1), .Q2(Aout_2),
    .Q3(Aout_3), .Q4(Aout_4), .Q5(Aout_5), .Q6(Aout_6), .Q7(Aout_7), .not_E(loadA), .CLK(CLK_t));
  and4 and4_2 (
    .Vcc(Vcc_t_t_t), .GND(GND_t_t), .A1(Cinstruction), .A2(ZRout), .A3(NGout), .B1(in_4), .B2(in_2),
    .B3(in_3), .S1(writeM_t), .S2(jeq), .S3(jlt));  // open: A4, B4, S4
  or4 or4_10 (
    .Vcc(Vcc_t_t_t), .GND(GND_t_t), .A1(ZRout), .B1(NGout), .Y1(zeroOrNeg));  // open: A2, B2, A3, B3, A4, B4, Y2, Y3, Y4
  not6 not6_2 (
    ._1A(zeroOrNeg), ._2A(PCload), ._1Y(positive), ._2Y(PCinc), .Vcc(Vcc_t_t_t), .GND(GND_t_t));  // open: _3A, _4A, _5A, _6A, _3Y, _4Y, _5Y, _6Y
  Multiplexer #(.enable("false")) multiplexer_9 (
    .in0(instruction[11]), .in1(outM[11]), .out(multiplexer_12_out[3]), .sel(and_2_out));
  Multiplexer #(.enable("false")) multiplexer_10 (
    .in0(instruction[10]), .in1(outM[10]), .out(multiplexer_12_out[2]), .sel(and_2_out));
  Multiplexer #(.enable("false")) multiplexer_11 (
    .in0(instruction[9]), .in1(outM[9]), .out(multiplexer_12_out[1]), .sel(and_2_out));
  Multiplexer #(.enable("false")) multiplexer_12 (
    .in0(instruction[8]), .in1(outM[8]), .out(multiplexer_12_out[0]), .sel(and_2_out));
  Multiplexer #(.enable("false")) multiplexer_13 (
    .in0(instruction[15]), .in1(outM[15]), .out(multiplexer_16_out[3]), .sel(and_2_out));
  Multiplexer #(.enable("false")) multiplexer_14 (
    .in0(instruction[14]), .in1(outM[14]), .out(multiplexer_16_out[2]), .sel(and_2_out));
  Multiplexer #(.enable("false")) multiplexer_15 (
    .in0(instruction[13]), .in1(outM[13]), .out(multiplexer_16_out[1]), .sel(and_2_out));
  Multiplexer #(.enable("false")) multiplexer_16 (
    .in0(instruction[12]), .in1(outM[12]), .out(multiplexer_16_out[0]), .sel(and_2_out));
  register8 register8_4 (
    .Vcc(Vcc_t_t_t), .GND(GND_t_t), .D0(Aregin_8), .D1(Aregin_9), .D2(Aregin_10), .D3(Aregin_11),
    .D4(Aregin_12), .D5(Aregin_13), .D6(Aregin_14), .D7(Aregin_15), .Q0(Aout_8), .Q1(Aout_9), .Q2(Aout_10),
    .Q3(Aout_11), .Q4(Aout_12), .Q5(Aout_13), .Q6(Aout_14), .Q7(Aout_15), .not_E(loadA), .CLK(CLK_t));
  and4 and4_3 (
    .Vcc(Vcc_t_t_t), .GND(GND_t_t), .A1(positive), .A2(Cinstruction), .B1(in_1), .B2(jumpToA), .S1(jgt),
    .S2(PCload));  // open: A3, A4, B3, B4, S3, S4
  or4 or4_11 (
    .Vcc(Vcc_t_t_t), .GND(GND_t_t), .A1(jeq), .B1(jlt), .A2(jle), .B2(jgt), .Y1(jle), .Y2(jumpToA));  // open: A3, B3, A4, B4, Y3, Y4
  Register #(.width(1)) register_1 (.D(multiplexer_4_out[3]), .en(or_1_out), .Q(addressM[3]), .clk(clk));  // open: clr
  Register #(.width(1)) register_2 (.D(multiplexer_4_out[2]), .en(or_1_out), .Q(addressM[2]), .clk(clk));  // open: clr
  Register #(.width(1)) register_3 (.D(multiplexer_4_out[1]), .en(or_1_out), .Q(addressM[1]), .clk(clk));  // open: clr
  Register #(.width(1)) register_4 (.D(multiplexer_4_out[0]), .en(or_1_out), .Q(addressM[0]), .clk(clk));  // open: clr
  Register #(.width(1)) register_5 (.D(multiplexer_8_out[3]), .en(or_1_out), .Q(addressM[7]), .clk(clk));  // open: clr
  Register #(.width(1)) register_6 (.D(multiplexer_8_out[2]), .en(or_1_out), .Q(addressM[6]), .clk(clk));  // open: clr
  Register #(.width(1)) register_7 (.D(multiplexer_8_out[1]), .en(or_1_out), .Q(addressM[5]), .clk(clk));  // open: clr
  Register #(.width(1)) register_8 (.D(multiplexer_8_out[0]), .en(or_1_out), .Q(addressM[4]), .clk(clk));  // open: clr
  Register #(.width(1)) register_9 (
    .D(multiplexer_12_out[3]), .en(or_1_out), .Q(addressM[11]), .clk(clk));  // open: clr
  Register #(.width(1)) register_10 (
    .D(multiplexer_12_out[2]), .en(or_1_out), .Q(addressM[10]), .clk(clk));  // open: clr
  Register #(.width(1)) register_11 (
    .D(multiplexer_12_out[1]), .en(or_1_out), .Q(addressM[9]), .clk(clk));  // open: clr
  Register #(.width(1)) register_12 (
    .D(multiplexer_12_out[0]), .en(or_1_out), .Q(addressM[8]), .clk(clk));  // open: clr
  Register #(.width(1)) register_13 (
    .D(multiplexer_16_out[3]), .en(or_1_out), .Q(register_13_q[15]), .clk(clk));  // open: clr
  Register #(.width(1)) register_14 (
    .D(multiplexer_16_out[2]), .en(or_1_out), .Q(addressM[14]), .clk(clk));  // open: clr
  Register #(.width(1)) register_15 (
    .D(multiplexer_16_out[1]), .en(or_1_out), .Q(addressM[13]), .clk(clk));  // open: clr
  Register #(.width(1)) register_16 (
    .D(multiplexer_16_out[0]), .en(or_1_out), .Q(addressM[12]), .clk(clk));  // open: clr
  Multiplexer #(.enable("false")) multiplexer_17 (
    .in0(addressM[3]), .in1(inM[3]), .out(multiplexer_20_out[3]), .sel(instruction[12]));
  Multiplexer #(.enable("false")) multiplexer_18 (
    .in0(addressM[2]), .in1(inM[2]), .out(multiplexer_20_out[2]), .sel(instruction[12]));
  Multiplexer #(.enable("false")) multiplexer_19 (
    .in0(addressM[1]), .in1(inM[1]), .out(multiplexer_20_out[1]), .sel(instruction[12]));
  Multiplexer #(.enable("false")) multiplexer_20 (
    .in0(addressM[0]), .in1(inM[0]), .out(multiplexer_20_out[0]), .sel(instruction[12]));
  Register #(.width(1)) register_17 (.D(outM[3]), .en(and_3_out), .Q(register_20_q[3]), .clk(clk));  // open: clr
  Register #(.width(1)) register_18 (.D(outM[2]), .en(and_3_out), .Q(register_20_q[2]), .clk(clk));  // open: clr
  Register #(.width(1)) register_19 (.D(outM[1]), .en(and_3_out), .Q(register_20_q[1]), .clk(clk));  // open: clr
  Register #(.width(1)) register_20 (.D(outM[0]), .en(and_3_out), .Q(register_20_q[0]), .clk(clk));  // open: clr
  Multiplexer #(.enable("false")) multiplexer_21 (
    .in0(addressM[7]), .in1(inM[7]), .out(multiplexer_24_out[3]), .sel(instruction[12]));
  Multiplexer #(.enable("false")) multiplexer_22 (
    .in0(addressM[6]), .in1(inM[6]), .out(multiplexer_24_out[2]), .sel(instruction[12]));
  Multiplexer #(.enable("false")) multiplexer_23 (
    .in0(addressM[5]), .in1(inM[5]), .out(multiplexer_24_out[1]), .sel(instruction[12]));
  Multiplexer #(.enable("false")) multiplexer_24 (
    .in0(addressM[4]), .in1(inM[4]), .out(multiplexer_24_out[0]), .sel(instruction[12]));
  Register #(.width(1)) register_21 (.D(outM[7]), .en(and_3_out), .Q(register_20_q[7]), .clk(clk));  // open: clr
  Register #(.width(1)) register_22 (.D(outM[6]), .en(and_3_out), .Q(register_20_q[6]), .clk(clk));  // open: clr
  Register #(.width(1)) register_23 (.D(outM[5]), .en(and_3_out), .Q(register_20_q[5]), .clk(clk));  // open: clr
  Register #(.width(1)) register_24 (.D(outM[4]), .en(and_3_out), .Q(register_20_q[4]), .clk(clk));  // open: clr
  Register #(.width(1)) register_25 (.D(outM[11]), .en(and_3_out), .Q(register_20_q[11]), .clk(clk));  // open: clr
  Register #(.width(1)) register_26 (.D(outM[10]), .en(and_3_out), .Q(register_20_q[10]), .clk(clk));  // open: clr
  Register #(.width(1)) register_27 (.D(outM[9]), .en(and_3_out), .Q(register_20_q[9]), .clk(clk));  // open: clr
  Register #(.width(1)) register_28 (.D(outM[8]), .en(and_3_out), .Q(register_20_q[8]), .clk(clk));  // open: clr
  Multiplexer #(.enable("false")) multiplexer_25 (
    .in0(addressM[11]), .in1(inM[11]), .out(multiplexer_28_out[3]), .sel(instruction[12]));
  Multiplexer #(.enable("false")) multiplexer_26 (
    .in0(addressM[10]), .in1(inM[10]), .out(multiplexer_28_out[2]), .sel(instruction[12]));
  Multiplexer #(.enable("false")) multiplexer_27 (
    .in0(addressM[9]), .in1(inM[9]), .out(multiplexer_28_out[1]), .sel(instruction[12]));
  Multiplexer #(.enable("false")) multiplexer_28 (
    .in0(addressM[8]), .in1(inM[8]), .out(multiplexer_28_out[0]), .sel(instruction[12]));
  Register #(.width(1)) register_29 (.D(outM[15]), .en(and_3_out), .Q(register_20_q[15]), .clk(clk));  // open: clr
  Register #(.width(1)) register_30 (.D(outM[14]), .en(and_3_out), .Q(register_20_q[14]), .clk(clk));  // open: clr
  Register #(.width(1)) register_31 (.D(outM[13]), .en(and_3_out), .Q(register_20_q[13]), .clk(clk));  // open: clr
  Register #(.width(1)) register_32 (.D(outM[12]), .en(and_3_out), .Q(register_20_q[12]), .clk(clk));  // open: clr
  Multiplexer #(.enable("false")) multiplexer_29 (
    .in0(register_13_q[15]), .in1(inM[15]), .out(multiplexer_32_out[3]), .sel(instruction[12]));
  Multiplexer #(.enable("false")) multiplexer_30 (
    .in0(addressM[14]), .in1(inM[14]), .out(multiplexer_32_out[2]), .sel(instruction[12]));
  Multiplexer #(.enable("false")) multiplexer_31 (
    .in0(addressM[13]), .in1(inM[13]), .out(multiplexer_32_out[1]), .sel(instruction[12]));
  Multiplexer #(.enable("false")) multiplexer_32 (
    .in0(addressM[12]), .in1(inM[12]), .out(multiplexer_32_out[0]), .sel(instruction[12]));
  PC pc_1 (
    .in({register_13_q[15], addressM}), .reset(reset), .load(and_5_out), .inc(not_5_out),
    .out({pc_1_out[15], pc}), .clk(clk));
  or or_2 (or_2_out, outM[15], outM[14]);
  ALU alu_1 (
    .x(register_20_q), .y({multiplexer_32_out, multiplexer_28_out, multiplexer_24_out, multiplexer_20_out}),
    .out(outM), .zx(instruction[11]), .zy(instruction[9]), .nx(instruction[10]), .ny(instruction[8]),
    .f(instruction[7]), .no(instruction[6]));
  or or_3 (or_3_out, outM[11], outM[10]);
  or or_4 (or_4_out, outM[13], outM[12]);
  or or_5 (or_5_out, or_2_out, or_4_out);
  or or_6 (or_6_out, or_3_out, or_10_out);
  or or_7 (or_7_out, or_5_out, or_6_out);
  or or_8 (or_8_out, outM[7], outM[6]);
  or or_9 (or_9_out, outM[5], outM[4]);
  or or_10 (or_10_out, outM[9], outM[8]);
  or or_11 (or_11_out, or_8_out, or_9_out);
  or or_12 (or_12_out, or_11_out, or_17_out);
  or or_13 (or_13_out, or_7_out, or_12_out);
  not not_3 (not_3_out, or_13_out);
  or or_14 (or_14_out, outM[1], outM[0]);
  or or_15 (or_15_out, outM[15], outM[14]);
  or or_16 (or_16_out, outM[3], outM[2]);
  or or_17 (or_17_out, or_16_out, or_14_out);
  or or_18 (or_18_out, or_31_out, not_3_out);
  not not_4 (not_4_out, or_18_out);
  and and_4 (and_4_out, not_4_out, instruction[0]);
  or or_19 (or_19_out, and_4_out, or_25_out);
  and and_5 (and_5_out, not_2_out, or_19_out);
  not not_5 (not_5_out, and_5_out);
  or or_20 (or_20_out, outM[13], outM[12]);
  or or_21 (or_21_out, outM[11], outM[10]);
  or or_22 (or_22_out, or_21_out, or_27_out);
  or or_23 (or_23_out, or_15_out, or_20_out);
  or or_24 (or_24_out, or_23_out, or_22_out);
  or or_25 (or_25_out, and_6_out, and_7_out);
  or or_26 (or_26_out, outM[7], outM[6]);
  or or_27 (or_27_out, outM[9], outM[8]);
  or or_28 (or_28_out, outM[5], outM[4]);
  or or_29 (or_29_out, or_26_out, or_28_out);
  or or_30 (or_30_out, or_29_out, or_34_out);
  or or_31 (or_31_out, or_24_out, or_30_out);
  or or_32 (or_32_out, outM[3], outM[2]);
  or or_33 (or_33_out, outM[1], outM[0]);
  or or_34 (or_34_out, or_32_out, or_33_out);
  and and_6 (and_6_out, or_31_out, instruction[2]);
  and and_7 (and_7_out, not_3_out, instruction[1]);

  // Other names for the same wires on the sheet: instruction_0 = in_1; instruction_1 = in_2; instruction_2 = in_3;
  //   instruction_3 = in_4; instruction_4 = in_5; instruction_5 = in_6; instruction_6 = in_7; instruction_7 = in_8;
  //   instruction_8 = in_9; instruction_9 = in_10; instruction_10 = in_11; instruction_11 = in_12;
  //   instruction_12 = in_13; instruction_13 = in_14; instruction_14 = in_15; instruction_15 = in_16

  // Notes on the sheet:
  //   A Register
  //   D Register
endmodule

module ALU (
  input  nx,
  input  zx,
  input  [15:0] x,
  input  f,
  input  no,
  input  ny,
  input  zy,
  input  [15:0] y,
  output [15:0] out
);

  wire adder_1_cout, adder_2_cout, adder_3_cout, adder_4_cout, adder_5_cout, adder_6_cout, adder_7_cout,
       adder_8_cout, adder_9_cout, adder_10_cout, adder_11_cout, adder_12_cout, adder_13_cout, adder_14_cout,
       adder_15_cout;
  wire [3:0] adder_1_out, adder_5_out, adder_9_out, adder_13_out, and_4_out, and_8_out, and_12_out,
       and_16_out, multiplexer_28_out, multiplexer_32_out, multiplexer_36_out, multiplexer_40_out,
       multiplexer_44_out, multiplexer_48_out, multiplexer_52_out, multiplexer_56_out, multiplexer_60_out,
       multiplexer_64_out, multiplexer_68_out, multiplexer_72_out, multiplexer_76_out, multiplexer_80_out;
  wire [11:0] multiplexer_4_out, multiplexer_8_out;
  wire [15:0] not_1_out, not_17_out, not_33_out, pull_resistor_1_node, pull_resistor_2_node;

  Pull_Resistor pull_resistor_1 (.node(pull_resistor_1_node));
  Pull_Resistor pull_resistor_2 (.node(pull_resistor_2_node));
  Multiplexer #(.enable("false")) multiplexer_1 (
    .in0(x[3]), .in1(pull_resistor_1_node[3]), .out(multiplexer_4_out[3]), .sel(zx));
  Multiplexer #(.enable("false")) multiplexer_2 (
    .in0(x[2]), .in1(pull_resistor_1_node[2]), .out(multiplexer_4_out[2]), .sel(zx));
  Multiplexer #(.enable("false")) multiplexer_3 (
    .in0(x[1]), .in1(pull_resistor_1_node[1]), .out(multiplexer_4_out[1]), .sel(zx));
  Multiplexer #(.enable("false")) multiplexer_4 (
    .in0(x[0]), .in1(pull_resistor_1_node[0]), .out(multiplexer_4_out[0]), .sel(zx));
  Multiplexer #(.enable("false")) multiplexer_5 (
    .in0(y[3]), .in1(pull_resistor_2_node[3]), .out(multiplexer_8_out[3]), .sel(zy));
  Multiplexer #(.enable("false")) multiplexer_6 (
    .in0(y[2]), .in1(pull_resistor_2_node[2]), .out(multiplexer_8_out[2]), .sel(zy));
  Multiplexer #(.enable("false")) multiplexer_7 (
    .in0(y[1]), .in1(pull_resistor_2_node[1]), .out(multiplexer_8_out[1]), .sel(zy));
  Multiplexer #(.enable("false")) multiplexer_8 (
    .in0(y[0]), .in1(pull_resistor_2_node[0]), .out(multiplexer_8_out[0]), .sel(zy));
  Multiplexer #(.enable("false")) multiplexer_9 (
    .in0(x[7]), .in1(pull_resistor_1_node[7]), .out(multiplexer_4_out[7]), .sel(zx));
  Multiplexer #(.enable("false")) multiplexer_10 (
    .in0(x[6]), .in1(pull_resistor_1_node[6]), .out(multiplexer_4_out[6]), .sel(zx));
  Multiplexer #(.enable("false")) multiplexer_11 (
    .in0(x[5]), .in1(pull_resistor_1_node[5]), .out(multiplexer_4_out[5]), .sel(zx));
  Multiplexer #(.enable("false")) multiplexer_12 (
    .in0(x[4]), .in1(pull_resistor_1_node[4]), .out(multiplexer_4_out[4]), .sel(zx));
  Multiplexer #(.enable("false")) multiplexer_13 (
    .in0(y[7]), .in1(pull_resistor_2_node[7]), .out(multiplexer_8_out[7]), .sel(zy));
  Multiplexer #(.enable("false")) multiplexer_14 (
    .in0(y[6]), .in1(pull_resistor_2_node[6]), .out(multiplexer_8_out[6]), .sel(zy));
  Multiplexer #(.enable("false")) multiplexer_15 (
    .in0(y[5]), .in1(pull_resistor_2_node[5]), .out(multiplexer_8_out[5]), .sel(zy));
  Multiplexer #(.enable("false")) multiplexer_16 (
    .in0(y[4]), .in1(pull_resistor_2_node[4]), .out(multiplexer_8_out[4]), .sel(zy));
  Multiplexer #(.enable("false")) multiplexer_17 (
    .in0(x[11]), .in1(pull_resistor_1_node[11]), .out(multiplexer_4_out[11]), .sel(zx));
  Multiplexer #(.enable("false")) multiplexer_18 (
    .in0(x[10]), .in1(pull_resistor_1_node[10]), .out(multiplexer_4_out[10]), .sel(zx));
  Multiplexer #(.enable("false")) multiplexer_19 (
    .in0(x[9]), .in1(pull_resistor_1_node[9]), .out(multiplexer_4_out[9]), .sel(zx));
  Multiplexer #(.enable("false")) multiplexer_20 (
    .in0(x[8]), .in1(pull_resistor_1_node[8]), .out(multiplexer_4_out[8]), .sel(zx));
  Multiplexer #(.enable("false")) multiplexer_21 (
    .in0(y[11]), .in1(pull_resistor_2_node[11]), .out(multiplexer_8_out[11]), .sel(zy));
  Multiplexer #(.enable("false")) multiplexer_22 (
    .in0(y[10]), .in1(pull_resistor_2_node[10]), .out(multiplexer_8_out[10]), .sel(zy));
  Multiplexer #(.enable("false")) multiplexer_23 (
    .in0(y[9]), .in1(pull_resistor_2_node[9]), .out(multiplexer_8_out[9]), .sel(zy));
  Multiplexer #(.enable("false")) multiplexer_24 (
    .in0(y[8]), .in1(pull_resistor_2_node[8]), .out(multiplexer_8_out[8]), .sel(zy));
  Multiplexer #(.enable("false")) multiplexer_25 (
    .in0(x[15]), .in1(pull_resistor_1_node[15]), .out(multiplexer_28_out[3]), .sel(zx));
  Multiplexer #(.enable("false")) multiplexer_26 (
    .in0(x[14]), .in1(pull_resistor_1_node[14]), .out(multiplexer_28_out[2]), .sel(zx));
  Multiplexer #(.enable("false")) multiplexer_27 (
    .in0(x[13]), .in1(pull_resistor_1_node[13]), .out(multiplexer_28_out[1]), .sel(zx));
  Multiplexer #(.enable("false")) multiplexer_28 (
    .in0(x[12]), .in1(pull_resistor_1_node[12]), .out(multiplexer_28_out[0]), .sel(zx));
  Multiplexer #(.enable("false")) multiplexer_29 (
    .in0(y[15]), .in1(pull_resistor_2_node[15]), .out(multiplexer_32_out[3]), .sel(zy));
  Multiplexer #(.enable("false")) multiplexer_30 (
    .in0(y[14]), .in1(pull_resistor_2_node[14]), .out(multiplexer_32_out[2]), .sel(zy));
  Multiplexer #(.enable("false")) multiplexer_31 (
    .in0(y[13]), .in1(pull_resistor_2_node[13]), .out(multiplexer_32_out[1]), .sel(zy));
  Multiplexer #(.enable("false")) multiplexer_32 (
    .in0(y[12]), .in1(pull_resistor_2_node[12]), .out(multiplexer_32_out[0]), .sel(zy));
  not not_1 (not_1_out[0], multiplexer_4_out[0]);
  not not_2 (not_1_out[1], multiplexer_4_out[1]);
  not not_3 (not_1_out[2], multiplexer_4_out[2]);
  not not_4 (not_1_out[3], multiplexer_4_out[3]);
  not not_5 (not_1_out[4], multiplexer_4_out[4]);
  not not_6 (not_1_out[5], multiplexer_4_out[5]);
  not not_7 (not_1_out[6], multiplexer_4_out[6]);
  not not_8 (not_1_out[7], multiplexer_4_out[7]);
  not not_9 (not_1_out[8], multiplexer_4_out[8]);
  not not_10 (not_1_out[9], multiplexer_4_out[9]);
  not not_11 (not_1_out[10], multiplexer_4_out[10]);
  not not_12 (not_1_out[11], multiplexer_4_out[11]);
  not not_13 (not_1_out[12], multiplexer_28_out[0]);
  not not_14 (not_1_out[13], multiplexer_28_out[1]);
  not not_15 (not_1_out[14], multiplexer_28_out[2]);
  not not_16 (not_1_out[15], multiplexer_28_out[3]);
  not not_17 (not_17_out[0], multiplexer_8_out[0]);
  not not_18 (not_17_out[1], multiplexer_8_out[1]);
  not not_19 (not_17_out[2], multiplexer_8_out[2]);
  not not_20 (not_17_out[3], multiplexer_8_out[3]);
  not not_21 (not_17_out[4], multiplexer_8_out[4]);
  not not_22 (not_17_out[5], multiplexer_8_out[5]);
  not not_23 (not_17_out[6], multiplexer_8_out[6]);
  not not_24 (not_17_out[7], multiplexer_8_out[7]);
  not not_25 (not_17_out[8], multiplexer_8_out[8]);
  not not_26 (not_17_out[9], multiplexer_8_out[9]);
  not not_27 (not_17_out[10], multiplexer_8_out[10]);
  not not_28 (not_17_out[11], multiplexer_8_out[11]);
  not not_29 (not_17_out[12], multiplexer_32_out[0]);
  not not_30 (not_17_out[13], multiplexer_32_out[1]);
  not not_31 (not_17_out[14], multiplexer_32_out[2]);
  not not_32 (not_17_out[15], multiplexer_32_out[3]);
  Multiplexer #(.enable("false")) multiplexer_33 (
    .in0(multiplexer_4_out[3]), .in1(not_1_out[3]), .out(multiplexer_36_out[3]), .sel(nx));
  Multiplexer #(.enable("false")) multiplexer_34 (
    .in0(multiplexer_4_out[2]), .in1(not_1_out[2]), .out(multiplexer_36_out[2]), .sel(nx));
  Multiplexer #(.enable("false")) multiplexer_35 (
    .in0(multiplexer_4_out[1]), .in1(not_1_out[1]), .out(multiplexer_36_out[1]), .sel(nx));
  Multiplexer #(.enable("false")) multiplexer_36 (
    .in0(multiplexer_4_out[0]), .in1(not_1_out[0]), .out(multiplexer_36_out[0]), .sel(nx));
  Multiplexer #(.enable("false")) multiplexer_37 (
    .in0(multiplexer_8_out[3]), .in1(not_17_out[3]), .out(multiplexer_40_out[3]), .sel(ny));
  Multiplexer #(.enable("false")) multiplexer_38 (
    .in0(multiplexer_8_out[2]), .in1(not_17_out[2]), .out(multiplexer_40_out[2]), .sel(ny));
  Multiplexer #(.enable("false")) multiplexer_39 (
    .in0(multiplexer_8_out[1]), .in1(not_17_out[1]), .out(multiplexer_40_out[1]), .sel(ny));
  Multiplexer #(.enable("false")) multiplexer_40 (
    .in0(multiplexer_8_out[0]), .in1(not_17_out[0]), .out(multiplexer_40_out[0]), .sel(ny));
  Multiplexer #(.enable("false")) multiplexer_41 (
    .in0(multiplexer_4_out[7]), .in1(not_1_out[7]), .out(multiplexer_44_out[3]), .sel(nx));
  Multiplexer #(.enable("false")) multiplexer_42 (
    .in0(multiplexer_4_out[6]), .in1(not_1_out[6]), .out(multiplexer_44_out[2]), .sel(nx));
  Multiplexer #(.enable("false")) multiplexer_43 (
    .in0(multiplexer_4_out[5]), .in1(not_1_out[5]), .out(multiplexer_44_out[1]), .sel(nx));
  Multiplexer #(.enable("false")) multiplexer_44 (
    .in0(multiplexer_4_out[4]), .in1(not_1_out[4]), .out(multiplexer_44_out[0]), .sel(nx));
  Multiplexer #(.enable("false")) multiplexer_45 (
    .in0(multiplexer_8_out[7]), .in1(not_17_out[7]), .out(multiplexer_48_out[3]), .sel(ny));
  Multiplexer #(.enable("false")) multiplexer_46 (
    .in0(multiplexer_8_out[6]), .in1(not_17_out[6]), .out(multiplexer_48_out[2]), .sel(ny));
  Multiplexer #(.enable("false")) multiplexer_47 (
    .in0(multiplexer_8_out[5]), .in1(not_17_out[5]), .out(multiplexer_48_out[1]), .sel(ny));
  Multiplexer #(.enable("false")) multiplexer_48 (
    .in0(multiplexer_8_out[4]), .in1(not_17_out[4]), .out(multiplexer_48_out[0]), .sel(ny));
  Multiplexer #(.enable("false")) multiplexer_49 (
    .in0(multiplexer_4_out[11]), .in1(not_1_out[11]), .out(multiplexer_52_out[3]), .sel(nx));
  Multiplexer #(.enable("false")) multiplexer_50 (
    .in0(multiplexer_4_out[10]), .in1(not_1_out[10]), .out(multiplexer_52_out[2]), .sel(nx));
  Multiplexer #(.enable("false")) multiplexer_51 (
    .in0(multiplexer_4_out[9]), .in1(not_1_out[9]), .out(multiplexer_52_out[1]), .sel(nx));
  Multiplexer #(.enable("false")) multiplexer_52 (
    .in0(multiplexer_4_out[8]), .in1(not_1_out[8]), .out(multiplexer_52_out[0]), .sel(nx));
  Multiplexer #(.enable("false")) multiplexer_53 (
    .in0(multiplexer_8_out[11]), .in1(not_17_out[11]), .out(multiplexer_56_out[3]), .sel(ny));
  Multiplexer #(.enable("false")) multiplexer_54 (
    .in0(multiplexer_8_out[10]), .in1(not_17_out[10]), .out(multiplexer_56_out[2]), .sel(ny));
  Multiplexer #(.enable("false")) multiplexer_55 (
    .in0(multiplexer_8_out[9]), .in1(not_17_out[9]), .out(multiplexer_56_out[1]), .sel(ny));
  Multiplexer #(.enable("false")) multiplexer_56 (
    .in0(multiplexer_8_out[8]), .in1(not_17_out[8]), .out(multiplexer_56_out[0]), .sel(ny));
  Multiplexer #(.enable("false")) multiplexer_57 (
    .in0(multiplexer_28_out[3]), .in1(not_1_out[15]), .out(multiplexer_60_out[3]), .sel(nx));
  Multiplexer #(.enable("false")) multiplexer_58 (
    .in0(multiplexer_28_out[2]), .in1(not_1_out[14]), .out(multiplexer_60_out[2]), .sel(nx));
  Multiplexer #(.enable("false")) multiplexer_59 (
    .in0(multiplexer_28_out[1]), .in1(not_1_out[13]), .out(multiplexer_60_out[1]), .sel(nx));
  Multiplexer #(.enable("false")) multiplexer_60 (
    .in0(multiplexer_28_out[0]), .in1(not_1_out[12]), .out(multiplexer_60_out[0]), .sel(nx));
  Multiplexer #(.enable("false")) multiplexer_61 (
    .in0(multiplexer_32_out[3]), .in1(not_17_out[15]), .out(multiplexer_64_out[3]), .sel(ny));
  Multiplexer #(.enable("false")) multiplexer_62 (
    .in0(multiplexer_32_out[2]), .in1(not_17_out[14]), .out(multiplexer_64_out[2]), .sel(ny));
  Multiplexer #(.enable("false")) multiplexer_63 (
    .in0(multiplexer_32_out[1]), .in1(not_17_out[13]), .out(multiplexer_64_out[1]), .sel(ny));
  Multiplexer #(.enable("false")) multiplexer_64 (
    .in0(multiplexer_32_out[0]), .in1(not_17_out[12]), .out(multiplexer_64_out[0]), .sel(ny));
  and and_1 (and_4_out[3], multiplexer_36_out[3], multiplexer_40_out[3]);
  and and_2 (and_4_out[2], multiplexer_36_out[2], multiplexer_40_out[2]);
  and and_3 (and_4_out[1], multiplexer_36_out[1], multiplexer_40_out[1]);
  and and_4 (and_4_out[0], multiplexer_36_out[0], multiplexer_40_out[0]);
  Adder #(.width(1)) adder_1 (
    .a(multiplexer_36_out[0]), .b(multiplexer_40_out[0]), .out(adder_1_out[0]), .cout(adder_1_cout));  // open: cin
  Adder #(.width(1)) adder_2 (
    .a(multiplexer_36_out[1]), .b(multiplexer_40_out[1]), .out(adder_1_out[1]), .cin(adder_1_cout),
    .cout(adder_2_cout));
  Adder #(.width(1)) adder_3 (
    .a(multiplexer_36_out[2]), .b(multiplexer_40_out[2]), .out(adder_1_out[2]), .cin(adder_2_cout),
    .cout(adder_3_cout));
  Adder #(.width(1)) adder_4 (
    .a(multiplexer_36_out[3]), .b(multiplexer_40_out[3]), .out(adder_1_out[3]), .cin(adder_3_cout),
    .cout(adder_4_cout));
  and and_5 (and_8_out[3], multiplexer_44_out[3], multiplexer_48_out[3]);
  and and_6 (and_8_out[2], multiplexer_44_out[2], multiplexer_48_out[2]);
  and and_7 (and_8_out[1], multiplexer_44_out[1], multiplexer_48_out[1]);
  and and_8 (and_8_out[0], multiplexer_44_out[0], multiplexer_48_out[0]);
  Adder #(.width(1)) adder_5 (
    .a(multiplexer_44_out[0]), .b(multiplexer_48_out[0]), .out(adder_5_out[0]), .cin(adder_4_cout),
    .cout(adder_5_cout));
  Adder #(.width(1)) adder_6 (
    .a(multiplexer_44_out[1]), .b(multiplexer_48_out[1]), .out(adder_5_out[1]), .cin(adder_5_cout),
    .cout(adder_6_cout));
  Adder #(.width(1)) adder_7 (
    .a(multiplexer_44_out[2]), .b(multiplexer_48_out[2]), .out(adder_5_out[2]), .cin(adder_6_cout),
    .cout(adder_7_cout));
  Adder #(.width(1)) adder_8 (
    .a(multiplexer_44_out[3]), .b(multiplexer_48_out[3]), .out(adder_5_out[3]), .cin(adder_7_cout),
    .cout(adder_8_cout));
  and and_9 (and_12_out[3], multiplexer_52_out[3], multiplexer_56_out[3]);
  and and_10 (and_12_out[2], multiplexer_52_out[2], multiplexer_56_out[2]);
  and and_11 (and_12_out[1], multiplexer_52_out[1], multiplexer_56_out[1]);
  and and_12 (and_12_out[0], multiplexer_52_out[0], multiplexer_56_out[0]);
  Adder #(.width(1)) adder_9 (
    .a(multiplexer_52_out[0]), .b(multiplexer_56_out[0]), .out(adder_9_out[0]), .cin(adder_8_cout),
    .cout(adder_9_cout));
  Adder #(.width(1)) adder_10 (
    .a(multiplexer_52_out[1]), .b(multiplexer_56_out[1]), .out(adder_9_out[1]), .cin(adder_9_cout),
    .cout(adder_10_cout));
  Adder #(.width(1)) adder_11 (
    .a(multiplexer_52_out[2]), .b(multiplexer_56_out[2]), .out(adder_9_out[2]), .cin(adder_10_cout),
    .cout(adder_11_cout));
  Adder #(.width(1)) adder_12 (
    .a(multiplexer_52_out[3]), .b(multiplexer_56_out[3]), .out(adder_9_out[3]), .cin(adder_11_cout),
    .cout(adder_12_cout));
  and and_13 (and_16_out[3], multiplexer_60_out[3], multiplexer_64_out[3]);
  and and_14 (and_16_out[2], multiplexer_60_out[2], multiplexer_64_out[2]);
  and and_15 (and_16_out[1], multiplexer_60_out[1], multiplexer_64_out[1]);
  and and_16 (and_16_out[0], multiplexer_60_out[0], multiplexer_64_out[0]);
  Adder #(.width(1)) adder_13 (
    .a(multiplexer_60_out[0]), .b(multiplexer_64_out[0]), .out(adder_13_out[0]), .cin(adder_12_cout),
    .cout(adder_13_cout));
  Adder #(.width(1)) adder_14 (
    .a(multiplexer_60_out[1]), .b(multiplexer_64_out[1]), .out(adder_13_out[1]), .cin(adder_13_cout),
    .cout(adder_14_cout));
  Adder #(.width(1)) adder_15 (
    .a(multiplexer_60_out[2]), .b(multiplexer_64_out[2]), .out(adder_13_out[2]), .cin(adder_14_cout),
    .cout(adder_15_cout));
  Adder #(.width(1)) adder_16 (
    .a(multiplexer_60_out[3]), .b(multiplexer_64_out[3]), .out(adder_13_out[3]), .cin(adder_15_cout));  // open: cout
  Multiplexer #(.enable("false")) multiplexer_65 (
    .in0(and_4_out[3]), .in1(adder_1_out[3]), .out(multiplexer_68_out[3]), .sel(f));
  Multiplexer #(.enable("false")) multiplexer_66 (
    .in0(and_4_out[2]), .in1(adder_1_out[2]), .out(multiplexer_68_out[2]), .sel(f));
  Multiplexer #(.enable("false")) multiplexer_67 (
    .in0(and_4_out[1]), .in1(adder_1_out[1]), .out(multiplexer_68_out[1]), .sel(f));
  Multiplexer #(.enable("false")) multiplexer_68 (
    .in0(and_4_out[0]), .in1(adder_1_out[0]), .out(multiplexer_68_out[0]), .sel(f));
  Multiplexer #(.enable("false")) multiplexer_69 (
    .in0(and_8_out[3]), .in1(adder_5_out[3]), .out(multiplexer_72_out[3]), .sel(f));
  Multiplexer #(.enable("false")) multiplexer_70 (
    .in0(and_8_out[2]), .in1(adder_5_out[2]), .out(multiplexer_72_out[2]), .sel(f));
  Multiplexer #(.enable("false")) multiplexer_71 (
    .in0(and_8_out[1]), .in1(adder_5_out[1]), .out(multiplexer_72_out[1]), .sel(f));
  Multiplexer #(.enable("false")) multiplexer_72 (
    .in0(and_8_out[0]), .in1(adder_5_out[0]), .out(multiplexer_72_out[0]), .sel(f));
  Multiplexer #(.enable("false")) multiplexer_73 (
    .in0(and_12_out[3]), .in1(adder_9_out[3]), .out(multiplexer_76_out[3]), .sel(f));
  Multiplexer #(.enable("false")) multiplexer_74 (
    .in0(and_12_out[2]), .in1(adder_9_out[2]), .out(multiplexer_76_out[2]), .sel(f));
  Multiplexer #(.enable("false")) multiplexer_75 (
    .in0(and_12_out[1]), .in1(adder_9_out[1]), .out(multiplexer_76_out[1]), .sel(f));
  Multiplexer #(.enable("false")) multiplexer_76 (
    .in0(and_12_out[0]), .in1(adder_9_out[0]), .out(multiplexer_76_out[0]), .sel(f));
  Multiplexer #(.enable("false")) multiplexer_77 (
    .in0(and_16_out[3]), .in1(adder_13_out[3]), .out(multiplexer_80_out[3]), .sel(f));
  Multiplexer #(.enable("false")) multiplexer_78 (
    .in0(and_16_out[2]), .in1(adder_13_out[2]), .out(multiplexer_80_out[2]), .sel(f));
  Multiplexer #(.enable("false")) multiplexer_79 (
    .in0(and_16_out[1]), .in1(adder_13_out[1]), .out(multiplexer_80_out[1]), .sel(f));
  Multiplexer #(.enable("false")) multiplexer_80 (
    .in0(and_16_out[0]), .in1(adder_13_out[0]), .out(multiplexer_80_out[0]), .sel(f));
  not not_33 (not_33_out[0], multiplexer_68_out[0]);
  not not_34 (not_33_out[1], multiplexer_68_out[1]);
  not not_35 (not_33_out[2], multiplexer_68_out[2]);
  not not_36 (not_33_out[3], multiplexer_68_out[3]);
  not not_37 (not_33_out[4], multiplexer_72_out[0]);
  not not_38 (not_33_out[5], multiplexer_72_out[1]);
  not not_39 (not_33_out[6], multiplexer_72_out[2]);
  not not_40 (not_33_out[7], multiplexer_72_out[3]);
  not not_41 (not_33_out[8], multiplexer_76_out[0]);
  not not_42 (not_33_out[9], multiplexer_76_out[1]);
  not not_43 (not_33_out[10], multiplexer_76_out[2]);
  not not_44 (not_33_out[11], multiplexer_76_out[3]);
  not not_45 (not_33_out[12], multiplexer_80_out[0]);
  not not_46 (not_33_out[13], multiplexer_80_out[1]);
  not not_47 (not_33_out[14], multiplexer_80_out[2]);
  not not_48 (not_33_out[15], multiplexer_80_out[3]);
  Multiplexer #(.enable("false")) multiplexer_81 (
    .in0(multiplexer_68_out[3]), .in1(not_33_out[3]), .out(out[3]), .sel(no));
  Multiplexer #(.enable("false")) multiplexer_82 (
    .in0(multiplexer_68_out[2]), .in1(not_33_out[2]), .out(out[2]), .sel(no));
  Multiplexer #(.enable("false")) multiplexer_83 (
    .in0(multiplexer_68_out[1]), .in1(not_33_out[1]), .out(out[1]), .sel(no));
  Multiplexer #(.enable("false")) multiplexer_84 (
    .in0(multiplexer_68_out[0]), .in1(not_33_out[0]), .out(out[0]), .sel(no));
  Multiplexer #(.enable("false")) multiplexer_85 (
    .in0(multiplexer_72_out[3]), .in1(not_33_out[7]), .out(out[7]), .sel(no));
  Multiplexer #(.enable("false")) multiplexer_86 (
    .in0(multiplexer_72_out[2]), .in1(not_33_out[6]), .out(out[6]), .sel(no));
  Multiplexer #(.enable("false")) multiplexer_87 (
    .in0(multiplexer_72_out[1]), .in1(not_33_out[5]), .out(out[5]), .sel(no));
  Multiplexer #(.enable("false")) multiplexer_88 (
    .in0(multiplexer_72_out[0]), .in1(not_33_out[4]), .out(out[4]), .sel(no));
  Multiplexer #(.enable("false")) multiplexer_89 (
    .in0(multiplexer_76_out[3]), .in1(not_33_out[11]), .out(out[11]), .sel(no));
  Multiplexer #(.enable("false")) multiplexer_90 (
    .in0(multiplexer_76_out[2]), .in1(not_33_out[10]), .out(out[10]), .sel(no));
  Multiplexer #(.enable("false")) multiplexer_91 (
    .in0(multiplexer_76_out[1]), .in1(not_33_out[9]), .out(out[9]), .sel(no));
  Multiplexer #(.enable("false")) multiplexer_92 (
    .in0(multiplexer_76_out[0]), .in1(not_33_out[8]), .out(out[8]), .sel(no));
  Multiplexer #(.enable("false")) multiplexer_93 (
    .in0(multiplexer_80_out[3]), .in1(not_33_out[15]), .out(out[15]), .sel(no));
  Multiplexer #(.enable("false")) multiplexer_94 (
    .in0(multiplexer_80_out[2]), .in1(not_33_out[14]), .out(out[14]), .sel(no));
  Multiplexer #(.enable("false")) multiplexer_95 (
    .in0(multiplexer_80_out[1]), .in1(not_33_out[13]), .out(out[13]), .sel(no));
  Multiplexer #(.enable("false")) multiplexer_96 (
    .in0(multiplexer_80_out[0]), .in1(not_33_out[12]), .out(out[12]), .sel(no));
endmodule

module PC (
  input  [15:0] in,
  input  reset,
  input  load,
  input  inc,
  input  clk,
  output [15:0] out
);

  wire adder_1_cout, adder_2_cout, adder_3_cout, adder_4_cout, adder_5_cout, adder_6_cout, adder_7_cout,
       adder_8_cout, adder_9_cout, adder_10_cout, adder_11_cout, adder_12_cout, adder_13_cout, adder_14_cout,
       adder_15_cout, or_1_out, or_2_out;
  wire [3:0] adder_13_out, multiplexer_4_out, multiplexer_8_out, multiplexer_12_out, multiplexer_16_out,
       multiplexer_20_out, multiplexer_24_out, multiplexer_28_out, multiplexer_32_out;
  wire [11:0] adder_1_out;
  wire [15:0] pull_resistor_1_node, pull_resistor_3_node;

  Pull_Resistor #(.pull(1)) pull_resistor_1 (.node(pull_resistor_1_node[0]));
  Pull_Resistor pull_resistor_2 (.node(pull_resistor_1_node[15]));
  Adder #(.width(1)) adder_1 (
    .a(out[0]), .b(pull_resistor_1_node[0]), .out(adder_1_out[0]), .cout(adder_1_cout));  // open: cin
  Adder #(.width(1)) adder_2 (
    .a(out[1]), .b(pull_resistor_1_node[15]), .out(adder_1_out[1]), .cin(adder_1_cout), .cout(adder_2_cout));
  Adder #(.width(1)) adder_3 (
    .a(out[2]), .b(pull_resistor_1_node[15]), .out(adder_1_out[2]), .cin(adder_2_cout), .cout(adder_3_cout));
  Adder #(.width(1)) adder_4 (
    .a(out[3]), .b(pull_resistor_1_node[15]), .out(adder_1_out[3]), .cin(adder_3_cout), .cout(adder_4_cout));
  Adder #(.width(1)) adder_5 (
    .a(out[4]), .b(pull_resistor_1_node[15]), .out(adder_1_out[4]), .cin(adder_4_cout), .cout(adder_5_cout));
  Adder #(.width(1)) adder_6 (
    .a(out[5]), .b(pull_resistor_1_node[15]), .out(adder_1_out[5]), .cin(adder_5_cout), .cout(adder_6_cout));
  Adder #(.width(1)) adder_7 (
    .a(out[6]), .b(pull_resistor_1_node[15]), .out(adder_1_out[6]), .cin(adder_6_cout), .cout(adder_7_cout));
  Adder #(.width(1)) adder_8 (
    .a(out[7]), .b(pull_resistor_1_node[15]), .out(adder_1_out[7]), .cin(adder_7_cout), .cout(adder_8_cout));
  Adder #(.width(1)) adder_9 (
    .a(out[8]), .b(pull_resistor_1_node[15]), .out(adder_1_out[8]), .cin(adder_8_cout), .cout(adder_9_cout));
  Adder #(.width(1)) adder_10 (
    .a(out[9]), .b(pull_resistor_1_node[15]), .out(adder_1_out[9]), .cin(adder_9_cout), .cout(adder_10_cout));
  Adder #(.width(1)) adder_11 (
    .a(out[10]), .b(pull_resistor_1_node[15]), .out(adder_1_out[10]), .cin(adder_10_cout),
    .cout(adder_11_cout));
  Adder #(.width(1)) adder_12 (
    .a(out[11]), .b(pull_resistor_1_node[15]), .out(adder_1_out[11]), .cin(adder_11_cout),
    .cout(adder_12_cout));
  Adder #(.width(1)) adder_13 (
    .a(out[12]), .b(pull_resistor_1_node[15]), .out(adder_13_out[0]), .cin(adder_12_cout),
    .cout(adder_13_cout));
  Adder #(.width(1)) adder_14 (
    .a(out[13]), .b(pull_resistor_1_node[15]), .out(adder_13_out[1]), .cin(adder_13_cout),
    .cout(adder_14_cout));
  Adder #(.width(1)) adder_15 (
    .a(out[14]), .b(pull_resistor_1_node[15]), .out(adder_13_out[2]), .cin(adder_14_cout),
    .cout(adder_15_cout));
  Adder #(.width(1)) adder_16 (
    .a(out[15]), .b(pull_resistor_1_node[15]), .out(adder_13_out[3]), .cin(adder_15_cout));  // open: cout
  Multiplexer #(.enable("false")) multiplexer_1 (
    .in0(adder_1_out[3]), .in1(in[3]), .out(multiplexer_4_out[3]), .sel(load));
  Multiplexer #(.enable("false")) multiplexer_2 (
    .in0(adder_1_out[2]), .in1(in[2]), .out(multiplexer_4_out[2]), .sel(load));
  Multiplexer #(.enable("false")) multiplexer_3 (
    .in0(adder_1_out[1]), .in1(in[1]), .out(multiplexer_4_out[1]), .sel(load));
  Multiplexer #(.enable("false")) multiplexer_4 (
    .in0(adder_1_out[0]), .in1(in[0]), .out(multiplexer_4_out[0]), .sel(load));
  Multiplexer #(.enable("false")) multiplexer_5 (
    .in0(adder_1_out[7]), .in1(in[7]), .out(multiplexer_8_out[3]), .sel(load));
  Multiplexer #(.enable("false")) multiplexer_6 (
    .in0(adder_1_out[6]), .in1(in[6]), .out(multiplexer_8_out[2]), .sel(load));
  Multiplexer #(.enable("false")) multiplexer_7 (
    .in0(adder_1_out[5]), .in1(in[5]), .out(multiplexer_8_out[1]), .sel(load));
  Multiplexer #(.enable("false")) multiplexer_8 (
    .in0(adder_1_out[4]), .in1(in[4]), .out(multiplexer_8_out[0]), .sel(load));
  Multiplexer #(.enable("false")) multiplexer_9 (
    .in0(adder_1_out[11]), .in1(in[11]), .out(multiplexer_12_out[3]), .sel(load));
  Multiplexer #(.enable("false")) multiplexer_10 (
    .in0(adder_1_out[10]), .in1(in[10]), .out(multiplexer_12_out[2]), .sel(load));
  Multiplexer #(.enable("false")) multiplexer_11 (
    .in0(adder_1_out[9]), .in1(in[9]), .out(multiplexer_12_out[1]), .sel(load));
  Multiplexer #(.enable("false")) multiplexer_12 (
    .in0(adder_1_out[8]), .in1(in[8]), .out(multiplexer_12_out[0]), .sel(load));
  Multiplexer #(.enable("false")) multiplexer_13 (
    .in0(adder_13_out[3]), .in1(in[15]), .out(multiplexer_16_out[3]), .sel(load));
  Multiplexer #(.enable("false")) multiplexer_14 (
    .in0(adder_13_out[2]), .in1(in[14]), .out(multiplexer_16_out[2]), .sel(load));
  Multiplexer #(.enable("false")) multiplexer_15 (
    .in0(adder_13_out[1]), .in1(in[13]), .out(multiplexer_16_out[1]), .sel(load));
  Multiplexer #(.enable("false")) multiplexer_16 (
    .in0(adder_13_out[0]), .in1(in[12]), .out(multiplexer_16_out[0]), .sel(load));
  Pull_Resistor pull_resistor_3 (.node(pull_resistor_3_node));
  Multiplexer #(.enable("false")) multiplexer_17 (
    .in0(multiplexer_4_out[3]), .in1(pull_resistor_3_node[3]), .out(multiplexer_20_out[3]), .sel(reset));
  Multiplexer #(.enable("false")) multiplexer_18 (
    .in0(multiplexer_4_out[2]), .in1(pull_resistor_3_node[2]), .out(multiplexer_20_out[2]), .sel(reset));
  Multiplexer #(.enable("false")) multiplexer_19 (
    .in0(multiplexer_4_out[1]), .in1(pull_resistor_3_node[1]), .out(multiplexer_20_out[1]), .sel(reset));
  Multiplexer #(.enable("false")) multiplexer_20 (
    .in0(multiplexer_4_out[0]), .in1(pull_resistor_3_node[0]), .out(multiplexer_20_out[0]), .sel(reset));
  or or_1 (or_1_out, load, inc);
  Multiplexer #(.enable("false")) multiplexer_21 (
    .in0(multiplexer_8_out[3]), .in1(pull_resistor_3_node[7]), .out(multiplexer_24_out[3]), .sel(reset));
  Multiplexer #(.enable("false")) multiplexer_22 (
    .in0(multiplexer_8_out[2]), .in1(pull_resistor_3_node[6]), .out(multiplexer_24_out[2]), .sel(reset));
  Multiplexer #(.enable("false")) multiplexer_23 (
    .in0(multiplexer_8_out[1]), .in1(pull_resistor_3_node[5]), .out(multiplexer_24_out[1]), .sel(reset));
  Multiplexer #(.enable("false")) multiplexer_24 (
    .in0(multiplexer_8_out[0]), .in1(pull_resistor_3_node[4]), .out(multiplexer_24_out[0]), .sel(reset));
  or or_2 (or_2_out, reset, or_1_out);
  Multiplexer #(.enable("false")) multiplexer_25 (
    .in0(multiplexer_12_out[3]), .in1(pull_resistor_3_node[11]), .out(multiplexer_28_out[3]), .sel(reset));
  Multiplexer #(.enable("false")) multiplexer_26 (
    .in0(multiplexer_12_out[2]), .in1(pull_resistor_3_node[10]), .out(multiplexer_28_out[2]), .sel(reset));
  Multiplexer #(.enable("false")) multiplexer_27 (
    .in0(multiplexer_12_out[1]), .in1(pull_resistor_3_node[9]), .out(multiplexer_28_out[1]), .sel(reset));
  Multiplexer #(.enable("false")) multiplexer_28 (
    .in0(multiplexer_12_out[0]), .in1(pull_resistor_3_node[8]), .out(multiplexer_28_out[0]), .sel(reset));
  Multiplexer #(.enable("false")) multiplexer_29 (
    .in0(multiplexer_16_out[3]), .in1(pull_resistor_3_node[15]), .out(multiplexer_32_out[3]), .sel(reset));
  Multiplexer #(.enable("false")) multiplexer_30 (
    .in0(multiplexer_16_out[2]), .in1(pull_resistor_3_node[14]), .out(multiplexer_32_out[2]), .sel(reset));
  Multiplexer #(.enable("false")) multiplexer_31 (
    .in0(multiplexer_16_out[1]), .in1(pull_resistor_3_node[13]), .out(multiplexer_32_out[1]), .sel(reset));
  Multiplexer #(.enable("false")) multiplexer_32 (
    .in0(multiplexer_16_out[0]), .in1(pull_resistor_3_node[12]), .out(multiplexer_32_out[0]), .sel(reset));
  Register #(.width(1)) register_1 (.D(multiplexer_20_out[3]), .en(or_2_out), .Q(out[3]), .clk(clk));  // open: clr
  Register #(.width(1)) register_2 (.D(multiplexer_20_out[2]), .en(or_2_out), .Q(out[2]), .clk(clk));  // open: clr
  Register #(.width(1)) register_3 (.D(multiplexer_20_out[1]), .en(or_2_out), .Q(out[1]), .clk(clk));  // open: clr
  Register #(.width(1)) register_4 (.D(multiplexer_20_out[0]), .en(or_2_out), .Q(out[0]), .clk(clk));  // open: clr
  Register #(.width(1)) register_5 (.D(multiplexer_24_out[3]), .en(or_2_out), .Q(out[7]), .clk(clk));  // open: clr
  Register #(.width(1)) register_6 (.D(multiplexer_24_out[2]), .en(or_2_out), .Q(out[6]), .clk(clk));  // open: clr
  Register #(.width(1)) register_7 (.D(multiplexer_24_out[1]), .en(or_2_out), .Q(out[5]), .clk(clk));  // open: clr
  Register #(.width(1)) register_8 (.D(multiplexer_24_out[0]), .en(or_2_out), .Q(out[4]), .clk(clk));  // open: clr
  Register #(.width(1)) register_9 (.D(multiplexer_28_out[3]), .en(or_2_out), .Q(out[11]), .clk(clk));  // open: clr
  Register #(.width(1)) register_10 (.D(multiplexer_28_out[2]), .en(or_2_out), .Q(out[10]), .clk(clk));  // open: clr
  Register #(.width(1)) register_11 (.D(multiplexer_28_out[1]), .en(or_2_out), .Q(out[9]), .clk(clk));  // open: clr
  Register #(.width(1)) register_12 (.D(multiplexer_28_out[0]), .en(or_2_out), .Q(out[8]), .clk(clk));  // open: clr
  Register #(.width(1)) register_13 (.D(multiplexer_32_out[3]), .en(or_2_out), .Q(out[15]), .clk(clk));  // open: clr
  Register #(.width(1)) register_14 (.D(multiplexer_32_out[2]), .en(or_2_out), .Q(out[14]), .clk(clk));  // open: clr
  Register #(.width(1)) register_15 (.D(multiplexer_32_out[1]), .en(or_2_out), .Q(out[13]), .clk(clk));  // open: clr
  Register #(.width(1)) register_16 (.D(multiplexer_32_out[0]), .en(or_2_out), .Q(out[12]), .clk(clk));  // open: clr
endmodule

module MEMORY (
  input  [14:0] address,
  input  CLK,
  input  [15:0] in,
  input  load,
  output [15:0] out
);

  wire demultiplexer_1_out0, demultiplexer_1_out1, demultiplexer_2_out0, demultiplexer_2_out1,
       demultiplexer_3_out0, demultiplexer_3_out1, not_1_out, not_2_out, or_1_out;
  wire [15:0] multiplexer_1_out, multiplexer_2_out, pull_resistor_2_node, ram_1_data, ram_2_data;

  Demultiplexer #(.enable("false")) demultiplexer_1 (
    .out0(demultiplexer_1_out0), .out1(demultiplexer_1_out1), .in(demultiplexer_2_out0), .sel(address[14]));
  Demultiplexer #(.enable("false")) demultiplexer_2 (
    .out0(demultiplexer_2_out0), .out1(demultiplexer_2_out1), .in(load), .sel(address[13]));
  Demultiplexer #(.enable("false")) demultiplexer_3 (
    .out0(demultiplexer_3_out0), .out1(demultiplexer_3_out1), .in(demultiplexer_2_out1), .sel(address[14]));
  Pull_Resistor pull_resistor_1 (.node(demultiplexer_3_out1));
  or or_1 (or_1_out, demultiplexer_1_out0, demultiplexer_3_out0);
  not not_1 (not_1_out, or_1_out);
  not not_2 (not_2_out, demultiplexer_1_out1);
  RAM #(.addrWidth(14), .dataWidth(16), .bus("separate")) ram_1 (
    .addr(address[13:0]), .din(in), .data(ram_1_data), .str(or_1_out), .clk(CLK), .ld(not_1_out));  // open: sel, clr
  RAM #(.addrWidth(13), .dataWidth(16), .bus("separate")) ram_2 (
    .addr(address[12:0]), .din(in), .data(ram_2_data), .str(demultiplexer_1_out1), .clk(CLK), .ld(not_2_out));  // open: sel, clr
  Multiplexer #(.width(16), .enable("false")) multiplexer_1 (
    .in0(ram_1_data), .in1(ram_1_data), .out(multiplexer_1_out), .sel(address[13]));
  Multiplexer #(.width(16), .enable("false")) multiplexer_2 (
    .in0(ram_2_data), .in1(pull_resistor_2_node), .out(multiplexer_2_out), .sel(address[13]));
  Pull_Resistor pull_resistor_2 (.node(pull_resistor_2_node));
  Multiplexer #(.width(16), .enable("false")) multiplexer_3 (
    .in0(multiplexer_1_out), .in1(multiplexer_2_out), .out(out), .sel(address[14]));

  // Notes on the sheet:
  //   Main Memory 16K RAM
  //   Screen 8K RAM
endmodule

module mux16 (
);

  wire GND, GND_t, M1_A_0, M1_A_1, M1_A_2, M1_A_3, M1_A_4, M1_A_5, M1_A_6, M1_A_7, M1_A_8, M1_A_9, M1_A_10,
       M1_A_11, M1_A_12, M1_A_13, M1_A_14, M1_A_15, M1_B_0, M1_B_1, M1_B_2, M1_B_3, M1_B_4, M1_B_5, M1_B_6,
       M1_B_7, M1_B_8, M1_B_9, M1_B_10, M1_B_11, M1_B_12, M1_B_13, M1_B_14, M1_B_15, M1_SEL, M1_SEL_t,
       M1_Z_0, M1_Z_1, M1_Z_2, M1_Z_3, M1_Z_4, M1_Z_5, M1_Z_6, M1_Z_7, M1_Z_8, M1_Z_9, M1_Z_10, M1_Z_11,
       M1_Z_12, M1_Z_13, M1_Z_14, M1_Z_15, NC, NC_t, NC_t_t, Vcc, Vcc_t, Vcc_t_t;

  mux4 mux4_1 (
    .not_E(NC_t), .I_0a(M1_A_0), .I_1a(M1_B_0), .I_0b(M1_A_1), .I_1b(M1_B_1), .I_0c(M1_A_2), .I_1c(M1_B_2),
    .I_0d(M1_A_3), .I_1d(M1_B_3), .Z_a(M1_Z_0), .Z_b(M1_Z_1), .Z_c(M1_Z_2), .Z_d(M1_Z_3), .S(M1_SEL),
    .Vcc(Vcc_t), .GND(GND));
  mux4 mux4_2 (
    .not_E(NC_t), .I_0a(M1_A_4), .I_1a(M1_B_4), .I_0b(M1_A_5), .I_1b(M1_B_5), .I_0c(M1_A_6), .I_1c(M1_B_6),
    .I_0d(M1_A_7), .I_1d(M1_B_7), .Z_a(M1_Z_4), .Z_b(M1_Z_5), .Z_c(M1_Z_6), .Z_d(M1_Z_7), .S(M1_SEL),
    .Vcc(Vcc_t), .GND(GND));
  mux4 mux4_3 (
    .not_E(NC), .I_0a(M1_A_8), .I_1a(M1_B_8), .I_0b(M1_A_9), .I_1b(M1_B_9), .I_0c(M1_A_10), .I_1c(M1_B_10),
    .I_0d(M1_A_11), .I_1d(M1_B_11), .Z_a(M1_Z_8), .Z_b(M1_Z_9), .Z_c(M1_Z_10), .Z_d(M1_Z_11), .S(M1_SEL_t),
    .Vcc(Vcc), .GND(GND_t));
  mux4 mux4_4 (
    .not_E(NC_t_t), .I_0a(M1_A_12), .I_1a(M1_B_12), .I_0b(M1_A_13), .I_1b(M1_B_13), .I_0c(M1_A_14),
    .I_1c(M1_B_14), .I_0d(M1_A_15), .I_1d(M1_B_15), .Z_a(M1_Z_12), .Z_b(M1_Z_13), .Z_c(M1_Z_14),
    .Z_d(M1_Z_15), .S(M1_SEL_t), .Vcc(Vcc_t_t), .GND(GND_t));
endmodule

// 74F157A
module mux4 (
  input  not_E,
  input  Vcc,
  input  GND,
  input  S,
  input  I_0a,
  input  I_1a,
  input  I_0b,
  input  I_1b,
  input  I_0c,
  input  I_1c,
  input  I_0d,
  input  I_1d,
  output Z_a,
  output Z_b,
  output Z_c,
  output Z_d
);

  Pull_Resistor pull_resistor_1 (.node(not_E));
  Pull_Resistor #(.pull(1)) pull_resistor_2 (.node(Vcc));
  Pull_Resistor pull_resistor_3 (.node(GND));
  Multiplexer #(.enable("false")) multiplexer_1 (.in0(I_0a), .in1(I_1a), .out(Z_a), .sel(S));
  Multiplexer #(.enable("false")) multiplexer_2 (.in0(I_0b), .in1(I_1b), .out(Z_b), .sel(S));
  Multiplexer #(.enable("false")) multiplexer_3 (.in0(I_0c), .in1(I_1c), .out(Z_c), .sel(S));
  Multiplexer #(.enable("false")) multiplexer_4 (.in0(I_0d), .in1(I_1d), .out(Z_d), .sel(S));
endmodule

// 74LS377 (REG)
module register16 (
);

  wire CLK, D_0, D_1, D_2, D_3, D_4, D_5, D_6, D_7, D_8, D_9, D_10, D_11, D_12, D_13, D_14, D_15, GND, not_E,
       Q_0, Q_1, Q_2, Q_3, Q_4, Q_5, Q_6, Q_7, Q_8, Q_9, Q_10, Q_11, Q_12, Q_13, Q_14, Q_15, Vcc;

  register8 register8_1 (
    .Vcc(Vcc), .GND(GND), .D0(D_0), .D1(D_1), .D2(D_2), .D3(D_3), .D4(D_4), .D5(D_5), .D6(D_6), .D7(D_7),
    .Q0(Q_0), .Q1(Q_1), .Q2(Q_2), .Q3(Q_3), .Q4(Q_4), .Q5(Q_5), .Q6(Q_6), .Q7(Q_7), .not_E(not_E), .CLK(CLK));
  register8 register8_2 (
    .Vcc(Vcc), .GND(GND), .D0(D_8), .D1(D_9), .D2(D_10), .D3(D_11), .D4(D_12), .D5(D_13), .D6(D_14),
    .D7(D_15), .Q0(Q_8), .Q1(Q_9), .Q2(Q_10), .Q3(Q_11), .Q4(Q_12), .Q5(Q_13), .Q6(Q_14), .Q7(Q_15),
    .not_E(not_E), .CLK(CLK));
endmodule

// 74LS377 (REG)
module register8 (
  input  Vcc,
  input  GND,
  input  D0,
  input  D1,
  input  D2,
  input  D3,
  input  D4,
  input  D5,
  input  D6,
  input  D7,
  input  not_E,
  input  CLK,
  output Q0,
  output Q1,
  output Q2,
  output Q3,
  output Q4,
  output Q5,
  output Q6,
  output Q7
);

  Pull_Resistor #(.pull(1)) pull_resistor_1 (.node(Vcc));
  Pull_Resistor pull_resistor_2 (.node(GND));
  Register register_1 (
    .D({D7, D6, D5, D4, D3, D2, D1, D0}), .en(not_E), .Q({Q7, Q6, Q5, Q4, Q3, Q2, Q1, Q0}), .clk(CLK));  // open: clr

  // Notes on the sheet:
  //   if not_E == LOW, then output = D
endmodule

// 74LS283 (ADD)
module add4 (
  input  Vcc,
  input  GND,
  input  A1,
  input  A2,
  input  A3,
  input  C0,
  input  A4,
  input  B1,
  input  B2,
  input  B3,
  input  B4,
  output S1,
  output S2,
  output S3,
  output S4,
  output C4
);

  Pull_Resistor #(.pull(1)) pull_resistor_1 (.node(Vcc));
  Pull_Resistor pull_resistor_2 (.node(GND));
  Adder #(.width(4)) adder_1 (.a({A4, A3, A2, A1}), .b({B4, B3, B2, B1}), .out({S4, S3, S2, S1}), .cin(C0), .cout(C4));
endmodule

// DM7408 (AND)
module and4 (
  input  Vcc,
  input  GND,
  input  A1,
  input  A2,
  input  A3,
  input  A4,
  input  B1,
  input  B2,
  input  B3,
  input  B4,
  output S1,
  output S2,
  output S3,
  output S4
);

  Pull_Resistor #(.pull(1)) pull_resistor_1 (.node(Vcc));
  Pull_Resistor pull_resistor_2 (.node(GND));
  assign {S4, S3, S2, S1} = {A4, A3, A2, A1} & {B4, B3, B2, B1};  // AND_Gate and_1, 4 bits wide
endmodule

// SN7404 (NOT)
module not6 (
  input  Vcc,
  input  GND,
  input  _1A,
  input  _2A,
  input  _3A,
  input  _4A,
  input  _5A,
  input  _6A,
  output _1Y,
  output _2Y,
  output _3Y,
  output _4Y,
  output _5Y,
  output _6Y
);

  Pull_Resistor #(.pull(1)) pull_resistor_1 (.node(Vcc));
  Pull_Resistor pull_resistor_2 (.node(GND));
  not not_1 (_1Y, _1A);
  not not_2 (_2Y, _2A);
  not not_3 (_3Y, _3A);
  not not_4 (_4Y, _4A);
  not not_5 (_5Y, _5A);
  not not_6 (_6Y, _6A);
endmodule

// SN7432 (OR)
module or4 (
  input  Vcc,
  input  GND,
  input  A1,
  input  B1,
  input  A2,
  input  B2,
  input  A3,
  input  B3,
  input  A4,
  input  B4,
  output Y1,
  output Y2,
  output Y3,
  output Y4
);

  Pull_Resistor #(.pull(1)) pull_resistor_1 (.node(Vcc));
  Pull_Resistor pull_resistor_2 (.node(GND));
  or or_1 (Y1, A1, B1);
  or or_2 (Y2, A2, B2);
  or or_3 (Y3, A3, B3);
  or or_4 (Y4, A4, B4);
endmodule
