// Logisim project simulation.circ as structural Verilog
module ALU (
);

  wire mux_4_74lvc257_1__1y, mux_4_74lvc257_1__2y, mux_4_74lvc257_1__3y, mux_4_74lvc257_1__4y,
       mux_4_74lvc257_2__1y, mux_4_74lvc257_2__2y, mux_4_74lvc257_2__3y, mux_4_74lvc257_2__4y,
       mux_4_74lvc257_3__1y, mux_4_74lvc257_3__2y, mux_4_74lvc257_3__3y, mux_4_74lvc257_3__4y,
       mux_4_74lvc257_4__1y, mux_4_74lvc257_4__2y, mux_4_74lvc257_4__3y, mux_4_74lvc257_4__4y,
       pull_resistor_1_node, undriven, undriven_2, undriven_3;

  QUAD_AND_7408 quad_and_7408_1 ();  // open: A1, B1, A2, B2, A3, B3, A4, B4, Y1, Y2, Y3, Y4
  QUAD_OR_7432 quad_or_7432_1 ();  // open: A1, B1, A2, B2, A3, B3, A4, B4, Y1, Y2, Y3, Y4
  FULL_ADDER_74283 full_adder_74283_1 ();  // open: in_1, in_2, in_3, in_5, in_6, in_7, in_8, in_9, out_10, out_11, out_12, out_13, C4, C0
  REGISTER_8BIT_74377 register_8bit_74377_1 ();  // open: D0, D1, D2, D3, D4, D5, D6, D7, out_11, out_12, out_13, out_14, out_15, out_16, out_17, out_18, E, CP
  REGISTER_8BIT_74377 register_8bit_74377_2 ();  // open: D0, D1, D2, D3, D4, D5, D6, D7, out_11, out_12, out_13, out_14, out_15, out_16, out_17, out_18, E, CP
  HEX_INVERTER_7404 hex_inverter_7404_1 ();  // open: _1A, _2A, _3A, _4A, _5A, _6A, _1Y, _2Y, _3Y, _4Y, _5Y, _6Y
  QUAD_AND_7408 quad_and_7408_2 ();  // open: A1, B1, A2, B2, A3, B3, A4, B4, Y1, Y2, Y3, Y4
  QUAD_OR_7432 quad_or_7432_2 ();  // open: A1, B1, A2, B2, A3, B3, A4, B4, Y1, Y2, Y3, Y4
  FULL_ADDER_74283 full_adder_74283_2 ();  // open: in_1, in_2, in_3, in_5, in_6, in_7, in_8, in_9, out_10, out_11, out_12, out_13, C4, C0
  REGISTER_8BIT_74377 register_8bit_74377_3 ();  // open: D0, D1, D2, D3, D4, D5, D6, D7, out_11, out_12, out_13, out_14, out_15, out_16, out_17, out_18, E, CP
  REGISTER_8BIT_74377 register_8bit_74377_4 ();  // open: D0, D1, D2, D3, D4, D5, D6, D7, out_11, out_12, out_13, out_14, out_15, out_16, out_17, out_18, E, CP
  HEX_INVERTER_7404 hex_inverter_7404_2 ();  // open: _1A, _2A, _3A, _4A, _5A, _6A, _1Y, _2Y, _3Y, _4Y, _5Y, _6Y
  QUAD_AND_7408 quad_and_7408_3 ();  // open: A1, B1, A2, B2, A3, B3, A4, B4, Y1, Y2, Y3, Y4
  QUAD_OR_7432 quad_or_7432_3 ();  // open: A1, B1, A2, B2, A3, B3, A4, B4, Y1, Y2, Y3, Y4
  FULL_ADDER_74283 full_adder_74283_3 ();  // open: in_1, in_2, in_3, in_5, in_6, in_7, in_8, in_9, out_10, out_11, out_12, out_13, C4, C0
  HEX_INVERTER_7404 hex_inverter_7404_3 ();  // open: _1A, _2A, _3A, _4A, _5A, _6A, _1Y, _2Y, _3Y, _4Y, _5Y, _6Y
  QUAD_AND_7408 quad_and_7408_4 ();  // open: A1, B1, A2, B2, A3, B3, A4, B4, Y1, Y2, Y3, Y4
  QUAD_OR_7432 quad_or_7432_4 ();  // open: A1, B1, A2, B2, A3, B3, A4, B4, Y1, Y2, Y3, Y4
  REGISTER_8BIT_74377 register_8bit_74377_5 ();  // open: D0, D1, D2, D3, D4, D5, D6, D7, out_11, out_12, out_13, out_14, out_15, out_16, out_17, out_18, E, CP
  REGISTER_8BIT_74377 register_8bit_74377_6 ();  // open: D0, D1, D2, D3, D4, D5, D6, D7, out_11, out_12, out_13, out_14, out_15, out_16, out_17, out_18, E, CP
  FULL_ADDER_74283 full_adder_74283_4 ();  // open: in_1, in_2, in_3, in_5, in_6, in_7, in_8, in_9, out_10, out_11, out_12, out_13, C4, C0
  MUX_4_74LVC257 mux_4_74lvc257_1 (
    ._1Y(mux_4_74lvc257_1__1y), .A_B(undriven_2), ._2Y(mux_4_74lvc257_1__2y), ._3Y(mux_4_74lvc257_1__3y),
    ._4Y(mux_4_74lvc257_1__4y), .OE(pull_resistor_1_node));  // open: _1A, _1B, _2A, _2B, _3A, _3B, _4A, _4B
  MUX_4_74LVC257 mux_4_74lvc257_2 (
    ._1Y(mux_4_74lvc257_2__1y), .A_B(undriven_2), ._2Y(mux_4_74lvc257_2__2y), ._3Y(mux_4_74lvc257_2__3y),
    ._4Y(mux_4_74lvc257_2__4y), .OE(pull_resistor_1_node));  // open: _1A, _1B, _2A, _2B, _3A, _3B, _4A, _4B
  MUX_4_74LVC257 mux_4_74lvc257_3 (
    ._1Y(mux_4_74lvc257_3__1y), .A_B(undriven_2), ._2Y(mux_4_74lvc257_3__2y), ._3Y(mux_4_74lvc257_3__3y),
    ._4Y(mux_4_74lvc257_3__4y), .OE(pull_resistor_1_node));  // open: _1A, _1B, _2A, _2B, _3A, _3B, _4A, _4B
  MUX_4_74LVC257 mux_4_74lvc257_4 (
    ._1A(undriven), ._1B(undriven_3), ._1Y(mux_4_74lvc257_4__1y), .A_B(undriven_2),
    ._2Y(mux_4_74lvc257_4__2y), ._3Y(mux_4_74lvc257_4__3y), ._4A(undriven_3), ._4Y(mux_4_74lvc257_4__4y),
    .OE(pull_resistor_1_node));  // open: _2A, _2B, _3A, _3B, _4B
  Pull_Resistor pull_resistor_1 (.node(pull_resistor_1_node));
  HEX_INVERTER_7404 hex_inverter_7404_4 ();  // open: _1A, _2A, _3A, _4A, _5A, _6A, _1Y, _2Y, _3Y, _4Y, _5Y, _6Y
  HEX_INVERTER_7404 hex_inverter_7404_5 ();  // open: _1A, _2A, _3A, _4A, _5A, _6A, _1Y, _2Y, _3Y, _4Y, _5Y, _6Y
  MUX_4_74LVC257 mux_4_74lvc257_5 ();  // open: _1A, _1B, _1Y, A_B, _2A, _2Y, _2B, _3A, _3Y, _3B, _4A, _4Y, _4B, OE
  MUX_4_74LVC257 mux_4_74lvc257_6 ();  // open: _1A, _1B, _1Y, A_B, _2A, _2Y, _2B, _3A, _3Y, _3B, _4A, _4Y, _4B, OE
  HEX_INVERTER_7404 hex_inverter_7404_6 ();  // open: _1A, _2A, _3A, _4A, _5A, _6A, _1Y, _2Y, _3Y, _4Y, _5Y, _6Y
  HEX_INVERTER_7404 hex_inverter_7404_7 ();  // open: _1A, _2A, _3A, _4A, _5A, _6A, _1Y, _2Y, _3Y, _4Y, _5Y, _6Y
  MUX_4_74LVC257 mux_4_74lvc257_7 ();  // open: _1A, _1B, _1Y, A_B, _2A, _2Y, _2B, _3A, _3Y, _3B, _4A, _4Y, _4B, OE
  MUX_4_74LVC257 mux_4_74lvc257_8 ();  // open: _1A, _1B, _1Y, A_B, _2A, _2Y, _2B, _3A, _3Y, _3B, _4A, _4Y, _4B, OE
  MUX_4_74LVC257 mux_4_74lvc257_9 ();  // open: _1A, _1B, _1Y, A_B, _2A, _2Y, _2B, _3A, _3Y, _3B, _4A, _4Y, _4B, OE
  MUX_4_74LVC257 mux_4_74lvc257_10 ();  // open: _1A, _1B, _1Y, A_B, _2A, _2Y, _2B, _3A, _3Y, _3B, _4A, _4Y, _4B, OE
  HEX_INVERTER_7404 hex_inverter_7404_8 ();  // open: _1A, _2A, _3A, _4A, _5A, _6A, _1Y, _2Y, _3Y, _4Y, _5Y, _6Y
  HEX_INVERTER_7404 hex_inverter_7404_9 ();  // open: _1A, _2A, _3A, _4A, _5A, _6A, _1Y, _2Y, _3Y, _4Y, _5Y, _6Y
  MUX_4_74LVC257 mux_4_74lvc257_11 ();  // open: _1A, _1B, _1Y, A_B, _2A, _2Y, _2B, _3A, _3Y, _3B, _4A, _4Y, _4B, OE
  MUX_4_74LVC257 mux_4_74lvc257_12 ();  // open: _1A, _1B, _1Y, A_B, _2A, _2Y, _2B, _3A, _3Y, _3B, _4A, _4Y, _4B, OE

  // Notes on the sheet:
  //   7404 = NOT
  //   7408 = AND
  //   74LS32 = OR
  //   74LVC257 = MUX
  //   74LS283 = FULL ADDER
endmodule

// 7404
module HEX_INVERTER_7404 (
  input  _1A,
  input  _2A,
  input  _3A,
  input  _4A,
  input  _5A,
  input  _6A,
  output _1Y,
  output _2Y,
  output _3Y,
  output _4Y,
  output _5Y,
  output _6Y
);

  not not_1 (_1Y, _1A);
  not not_2 (_2Y, _2A);
  not not_3 (_3Y, _3A);
  not not_4 (_4Y, _4A);
  not not_5 (_5Y, _5A);
  not not_6 (_6Y, _6A);
endmodule

// 7408
module QUAD_AND_7408 (
  input  A1,
  input  B1,
  input  A2,
  input  B2,
  input  A3,
  input  B3,
  input  A4,
  input  B4,
  output Y1,
  output Y2,
  output Y3,
  output Y4
);

  and and_1 (Y1, A1, B1);
  and and_2 (Y2, A2, B2);
  and and_3 (Y3, A3, B3);
  and and_4 (Y4, A4, B4);
endmodule

// 74LS32
module QUAD_OR_7432 (
  input  A1,
  input  B1,
  input  A2,
  input  B2,
  input  A3,
  input  B3,
  input  A4,
  input  B4,
  output Y1,
  output Y2,
  output Y3,
  output Y4
);

  or or_1 (Y1, A1, B1);
  or or_2 (Y2, A2, B2);
  or or_3 (Y3, A3, B3);
  or or_4 (Y4, A4, B4);
endmodule

// 74LVC257
module MUX_4_74LVC257 (
  input  A_B,
  input  OE,
  input  _1A,
  input  _1B,
  input  _2A,
  input  _2B,
  input  _3A,
  input  _3B,
  input  _4A,
  input  _4B,
  output _1Y,
  output _2Y,
  output _3Y,
  output _4Y
);

  wire not_1_out;

  Multiplexer multiplexer_1 (.in0(_1A), .in1(_1B), .out(_1Y), .sel(A_B), .en(not_1_out));
  Multiplexer multiplexer_2 (.in0(_2A), .in1(_2B), .out(_2Y), .sel(A_B), .en(not_1_out));
  Multiplexer multiplexer_3 (.in0(_3A), .in1(_3B), .out(_3Y), .sel(A_B), .en(not_1_out));
  Multiplexer multiplexer_4 (.in0(_4A), .in1(_4B), .out(_4Y), .sel(A_B), .en(not_1_out));
  not not_1 (not_1_out, OE);
endmodule

// 74LS283
module FULL_ADDER_74283 (
  input  in_1,
  input  in_2,
  input  in_3,
  input  C0,
  input  in_5,
  input  in_6,
  input  in_7,
  input  in_8,
  input  in_9,
  output out_10,
  output out_11,
  output out_12,
  output out_13,
  output C4
);

  Adder #(.width(4)) adder_1 (
    .a({in_5, in_3, in_2, in_1}), .b({in_9, in_8, in_7, in_6}), .out({out_13, out_12, out_11, out_10}),
    .cin(C0), .cout(C4));
endmodule

// 74LS377
module REGISTER_8BIT_74377 (
  input  D0,
  input  D1,
  input  D2,
  input  D3,
  input  D4,
  input  D5,
  input  D6,
  input  D7,
  input  E,
  input  CP,
  output out_11,
  output out_12,
  output out_13,
  output out_14,
  output out_15,
  output out_16,
  output out_17,
  output out_18
);

  Register register_1 (
    .D({D7, D6, D5, D4, D3, D2, D1, D0}), .en(E),
    .Q({out_18, out_17, out_16, out_15, out_14, out_13, out_12, out_11}), .clk(CP));  // open: clr
endmodule
