// Logisim project simulation_v0.circ as structural Verilog
module COMPUTER (
  input  reset,
  output [15:0] instruction,
  output [14:0] pc,
  output [15:0] inM,
  output [15:0] outM,
  output [14:0] addressM
);

  wire CLK_out, cpu_1_writem;

  Clock CLK (.out(CLK_out));
  CPU cpu_1 (
    .outM(outM), .addressM(addressM), .pc(pc), .inM(inM), .reset(reset), .writeM(cpu_1_writem),
    .CLK(CLK_out), .instruction(instruction));
  MEMORY memory_1 (.load(cpu_1_writem), .out(inM), .in(outM), .CLK(CLK_out), .address(addressM));
  ROM #(.addrWidth(15), .dataWidth(16)) rom_1 (.addr(pc), .data(instruction));  // open: sel

  // Notes on the sheet:
  //   to be written to memory.
  //   CPU
  //   If the ROM instr. is a C-instruction
  //   then this register will hold the value
  //   MEMORY
  //   ROM32K
  //   in the next clock cycle.
  //   contents of rom_1 (hex, n*v repeats v):
  //   10 ea88 11 ea88 10 fc10 1 f4d0 12 e303 0 fc10 11 f088 10 fdc8 4 ea87 11 fc10 2 e308 12 ea87
  //   If the ROM instr. is a A-instruction 
  //   then this register will hold the address 
endmodule

module CPU (
  input  [15:0] instruction,
  input  reset,
  input  [15:0] inM,
  input  CLK,
  output [15:0] outM,
  output writeM,
  output [14:0] addressM,
  output [14:0] pc
);

  wire alu_1_ng, alu_1_zr, and_1_out, and_3_out, and_4_out, and_5_out, and_6_out, and_7_out, not_1_out,
       not_2_out, not_3_out, not_4_out, or_1_out, or_2_out, or_3_out, or_4_out;
  wire [15:0] D_q, multiplexer_1_out, multiplexer_2_out;
  wire [15:15] A_q, pc_1_out;

  not not_1 (not_1_out, instruction[15]);
  not not_2 (not_2_out, not_1_out);
  and and_1 (and_1_out, not_2_out, instruction[5]);
  or or_1 (or_1_out, not_1_out, and_1_out);
  and and_2 (writeM, not_2_out, instruction[3]);
  Multiplexer #(.width(16), .enable("false")) multiplexer_1 (
    .in0(instruction), .in1(outM), .out(multiplexer_1_out), .sel(and_1_out));
  Register #(.width(16)) A (.D(multiplexer_1_out), .en(or_1_out), .Q({A_q[15], addressM}), .clk(CLK));  // open: clr
  and and_3 (and_3_out, not_2_out, instruction[4]);
  Register #(.width(16)) D (.D(outM), .en(and_3_out), .Q(D_q), .clk(CLK));  // open: clr
  Multiplexer #(.width(16), .enable("false")) multiplexer_2 (
    .in0({A_q[15], addressM}), .in1(inM), .out(multiplexer_2_out), .sel(instruction[12]));
  ALU alu_1 (
    .out(outM), .zr(alu_1_zr), .ng(alu_1_ng), .x(D_q), .y(multiplexer_2_out), .zx(instruction[11]),
    .zy(instruction[9]), .nx(instruction[10]), .ny(instruction[8]), .f(instruction[7]), .no(instruction[6]));
  and and_4 (and_4_out, instruction[1], alu_1_zr);
  and and_5 (and_5_out, instruction[2], alu_1_ng);
  not not_3 (not_3_out, or_2_out);
  or or_2 (or_2_out, alu_1_zr, alu_1_ng);
  or or_3 (or_3_out, and_4_out, and_5_out);
  and and_6 (and_6_out, instruction[0], not_3_out);
  or or_4 (or_4_out, or_3_out, and_6_out);
  and and_7 (and_7_out, or_4_out, not_2_out);
  not not_4 (not_4_out, and_7_out);
  PC pc_1 (
    .in({A_q[15], addressM}), .reset(reset), .inc(not_4_out), .load(and_7_out), .out({pc_1_out[15], pc}),
    .CLK(CLK));

  // Notes on the sheet:
  //   load A if A-instr
  //   or dest. if C-instr
  //   sel A out or M in
  //   zr & jump if = 0
  //   ng & jump if < 0
  //   zr OR ng
  //   (!ng OR !zr) & jump if > 0
endmodule

module MEMORY (
  input  [14:0] address,
  input  CLK,
  input  [15:0] in,
  input  load,
  output [15:0] out
);

  wire demultiplexer_1_out0, demultiplexer_1_out1, demultiplexer_2_out0, demultiplexer_2_out1,
       demultiplexer_3_out0, demultiplexer_3_out1, not_1_out, not_2_out, or_1_out;
  wire [15:0] multiplexer_1_out, multiplexer_2_out, pull_resistor_2_node, ram_1_data, ram_2_data;

  Demultiplexer #(.enable("false")) demultiplexer_1 (
    .out0(demultiplexer_1_out0), .out1(demultiplexer_1_out1), .in(demultiplexer_2_out0), .sel(address[14]));
  Demultiplexer #(.enable("false")) demultiplexer_2 (
    .out0(demultiplexer_2_out0), .out1(demultiplexer_2_out1), .in(load), .sel(address[13]));
  Demultiplexer #(.enable("false")) demultiplexer_3 (
    .out0(demultiplexer_3_out0), .out1(demultiplexer_3_out1), .in(demultiplexer_2_out1), .sel(address[14]));
  Pull_Resistor pull_resistor_1 (.node(demultiplexer_3_out1));
  or or_1 (or_1_out, demultiplexer_1_out0, demultiplexer_3_out0);
  not not_1 (not_1_out, or_1_out);
  not not_2 (not_2_out, demultiplexer_1_out1);
  RAM #(.addrWidth(14), .dataWidth(16), .bus("separate")) ram_1 (
    .addr(address[13:0]), .din(in), .data(ram_1_data), .str(or_1_out), .clk(CLK), .ld(not_1_out));  // open: sel, clr
  RAM #(.addrWidth(13), .dataWidth(16), .bus("separate")) ram_2 (
    .addr(address[12:0]), .din(in), .data(ram_2_data), .str(demultiplexer_1_out1), .clk(CLK), .ld(not_2_out));  // open: sel, clr
  Multiplexer #(.width(16), .enable("false")) multiplexer_1 (
    .in0(ram_1_data), .in1(ram_1_data), .out(multiplexer_1_out), .sel(address[13]));
  Multiplexer #(.width(16), .enable("false")) multiplexer_2 (
    .in0(ram_2_data), .in1(pull_resistor_2_node), .out(multiplexer_2_out), .sel(address[13]));
  Pull_Resistor pull_resistor_2 (.node(pull_resistor_2_node));
  Multiplexer #(.width(16), .enable("false")) multiplexer_3 (
    .in0(multiplexer_1_out), .in1(multiplexer_2_out), .out(out), .sel(address[14]));

  // Notes on the sheet:
  //   Main Memory 16K RAM
  //   Screen 8K RAM
endmodule

module ALU (
  input  zx,
  input  nx,
  input  f,
  input  no,
  input  [15:0] x,
  input  zy,
  input  ny,
  input  [15:0] y,
  output [15:0] out,
  output zr,
  output ng
);

  wire or_1_out, or_2_out, or_3_out, or_4_out, or_5_out, or_6_out, or_7_out, or_8_out, or_9_out, or_10_out,
       or_11_out, or_12_out, or_13_out, or_14_out, or_15_out, or_16_out, or_17_out, or_18_out, or_19_out,
       or_20_out, or_21_out, or_22_out, or_23_out, or_24_out, or_25_out, or_26_out, or_27_out, or_28_out,
       or_29_out;
  wire [15:0] adder_1_out, and_1_out, multiplexer_1_out, multiplexer_2_out, multiplexer_3_out,
       multiplexer_4_out, multiplexer_5_out, not_1_out, not_2_out, not_3_out, pull_resistor_1_node,
       pull_resistor_2_node;

  Pull_Resistor pull_resistor_1 (.node(pull_resistor_1_node));
  Pull_Resistor pull_resistor_2 (.node(pull_resistor_2_node));
  Multiplexer #(.width(16), .enable("false")) multiplexer_1 (
    .in0(x), .in1(pull_resistor_1_node), .out(multiplexer_1_out), .sel(zx));
  Multiplexer #(.width(16), .enable("false")) multiplexer_2 (
    .in0(y), .in1(pull_resistor_2_node), .out(multiplexer_2_out), .sel(zy));
  Multiplexer #(.width(16), .enable("false")) multiplexer_3 (
    .in0(multiplexer_1_out), .in1(not_1_out), .out(multiplexer_3_out), .sel(nx));
  assign not_1_out = ~multiplexer_1_out;  // NOT_Gate not_1, 16 bits wide
  Multiplexer #(.width(16), .enable("false")) multiplexer_4 (
    .in0(multiplexer_2_out), .in1(not_2_out), .out(multiplexer_4_out), .sel(ny));
  assign not_2_out = ~multiplexer_2_out;  // NOT_Gate not_2, 16 bits wide
  assign and_1_out = multiplexer_3_out & multiplexer_4_out;  // AND_Gate and_1, 16 bits wide
  Adder #(.width(16)) adder_1 (.a(multiplexer_3_out), .b(multiplexer_4_out), .out(adder_1_out));  // open: cin, cout
  Multiplexer #(.width(16), .enable("false")) multiplexer_5 (
    .in0(and_1_out), .in1(adder_1_out), .out(multiplexer_5_out), .sel(f));
  Multiplexer #(.width(16), .enable("false")) multiplexer_6 (
    .in0(multiplexer_5_out), .in1(not_3_out), .out(out), .sel(no));
  assign not_3_out = ~multiplexer_5_out;  // NOT_Gate not_3, 16 bits wide
  or or_1 (or_1_out, out[0], out[1]);
  or or_2 (or_2_out, out[2], out[3]);
  or or_3 (or_3_out, out[4], out[5]);
  or or_4 (or_4_out, out[6], out[7]);
  or or_5 (or_5_out, out[8], out[9]);
  or or_6 (or_6_out, out[10], out[11]);
  or or_7 (or_7_out, out[12], out[13]);
  or or_8 (or_8_out, out[14], out[15]);
  or or_9 (or_9_out, out[0], out[1]);
  or or_10 (or_10_out, out[2], out[3]);
  or or_11 (or_11_out, out[4], out[5]);
  or or_12 (or_12_out, out[6], out[7]);
  or or_13 (or_13_out, out[8], out[9]);
  or or_14 (or_14_out, out[10], out[11]);
  or or_15 (or_15_out, out[12], out[13]);
  or or_16 (or_16_out, out[14], out[15]);
  or or_17 (or_17_out, or_1_out, or_2_out);
  or or_18 (or_18_out, or_17_out, or_19_out);
  or or_19 (or_19_out, or_3_out, or_4_out);
  or or_20 (or_20_out, or_5_out, or_6_out);
  or or_21 (or_21_out, or_20_out, or_22_out);
  or or_22 (or_22_out, or_7_out, or_8_out);
  or or_23 (or_23_out, or_9_out, or_10_out);
  or or_24 (or_24_out, or_23_out, or_25_out);
  or or_25 (or_25_out, or_11_out, or_12_out);
  or or_26 (or_26_out, or_13_out, or_14_out);
  or or_27 (or_27_out, or_26_out, or_28_out);
  or or_28 (or_28_out, or_15_out, or_16_out);
  or or_29 (or_29_out, or_18_out, or_21_out);
  or or_30 (ng, or_24_out, or_27_out);
  not not_4 (zr, or_29_out);
endmodule

module PC (
  input  reset,
  input  inc,
  input  load,
  input  [15:0] in,
  input  CLK,
  output [15:0] out
);

  wire or_1_out, or_2_out;
  wire [15:0] adder_1_out, multiplexer_1_out, multiplexer_2_out, pull_resistor_1_node;

  Pull_Resistor #(.pull(1)) pull_resistor_1 (.node(pull_resistor_1_node[0]));
  Pull_Resistor pull_resistor_2 (.node(pull_resistor_1_node[15]));
  Adder #(.width(16)) adder_1 (
    .a(out), .b({{15{pull_resistor_1_node[15]}}, pull_resistor_1_node[0]}), .out(adder_1_out));  // open: cin, cout
  Multiplexer #(.width(16), .enable("false")) multiplexer_1 (
    .in0(adder_1_out), .in1(in), .out(multiplexer_1_out), .sel(load));
  or or_1 (or_1_out, load, inc);
  Multiplexer #(.width(16), .enable("false")) multiplexer_2 (
    .in0(multiplexer_1_out), .out(multiplexer_2_out), .sel(reset));  // open: in1
  or or_2 (or_2_out, or_1_out, reset);
  Register #(.width(16)) register_1 (.D(multiplexer_2_out), .en(or_2_out), .Q(out), .clk(CLK));  // open: clr
endmodule
