// Logisim project simulation_v2.circ as structural Verilog: 9 circuits, main circuit main
module main (
  input  reset,
  output [14:0] pc,
  output [15:0] inM,
  output [15:0] instruction,
  output [15:0] outM,
  output [14:0] addressM
);

  wire clock_1_out, cpu_1_writem;

  Clock clock_1 (.out(clock_1_out));
  CPU cpu_1 (
    .addressM(addressM), .pc(pc), .instruction(instruction), .inM(inM), .reset(reset), .clk(clock_1_out),
    .writeM(cpu_1_writem), .outM(outM));
  ROM #(.addrWidth(15), .dataWidth(16)) rom_1 (.addr(pc), .data(instruction));  // open: sel
  MEMORY memory_1 (.load(cpu_1_writem), .out(inM), .in(outM), .CLK(clock_1_out), .address(addressM));

  // Notes on the sheet:
  //   If the ROM instr. is a C-instruction
  //   then this register will hold the value
  //   to be written to memory.
  //   If the ROM instr. is a A-instruction 
  //   then this register will hold the address 
  //   in the next clock cycle.
  //   contents of rom_1 (hex, n*v repeats v):
  //   10 ea88 11 ea88 10 fc10 1 f4d0 12 e303 0 fc10 11 f088 10 fdc8 4 ea87 11 fc10 2 e308 12 ea87
endmodule

module CPU (
  input  [15:0] instruction,
  input  [15:0] inM,
  input  clk,
  input  reset,
  output [15:0] outM,
  output writeM,
  output [14:0] pc,
  output [14:0] addressM
);

  wire and_2_out, and_3_out, and_4_out, and_5_out, and_6_out, and_7_out, not_1_out, not_2_out, not_3_out,
       not_4_out, not_5_out, or_1_out, or_2_out, or_3_out, or_4_out, or_5_out, or_6_out, or_7_out, or_8_out,
       or_9_out, or_10_out, or_11_out, or_12_out, or_13_out, or_14_out, or_15_out, or_16_out, or_17_out,
       or_18_out, or_19_out, or_20_out, or_21_out, or_22_out, or_23_out, or_24_out, or_25_out, or_26_out,
       or_27_out, or_28_out, or_29_out, or_30_out, or_31_out, or_32_out, or_33_out, or_34_out;
  wire [3:0] multiplexer_4_out, multiplexer_8_out, multiplexer_12_out, multiplexer_16_out,
       multiplexer_20_out, multiplexer_24_out, multiplexer_28_out, multiplexer_32_out;
  wire [15:0] register_20_q;
  wire [15:15] pc_1_out, register_13_q;

  and and_1 (writeM, instruction[3], not_2_out);
  not not_1 (not_1_out, instruction[15]);
  not not_2 (not_2_out, not_1_out);
  and and_2 (and_2_out, not_2_out, instruction[6]);
  or or_1 (or_1_out, not_1_out, and_2_out);
  Multiplexer #(.enable("false")) multiplexer_1 (
    .in0(instruction[3]), .in1(outM[3]), .out(multiplexer_4_out[3]), .sel(and_2_out));
  Multiplexer #(.enable("false")) multiplexer_2 (
    .in0(instruction[2]), .in1(outM[2]), .out(multiplexer_4_out[2]), .sel(and_2_out));
  Multiplexer #(.enable("false")) multiplexer_3 (
    .in0(instruction[1]), .in1(outM[1]), .out(multiplexer_4_out[1]), .sel(and_2_out));
  Multiplexer #(.enable("false")) multiplexer_4 (
    .in0(instruction[0]), .in1(outM[0]), .out(multiplexer_4_out[0]), .sel(and_2_out));
  Multiplexer #(.enable("false")) multiplexer_5 (
    .in0(instruction[7]), .in1(outM[7]), .out(multiplexer_8_out[3]), .sel(and_2_out));
  Multiplexer #(.enable("false")) multiplexer_6 (
    .in0(instruction[6]), .in1(outM[6]), .out(multiplexer_8_out[2]), .sel(and_2_out));
  Multiplexer #(.enable("false")) multiplexer_7 (
    .in0(instruction[5]), .in1(outM[5]), .out(multiplexer_8_out[1]), .sel(and_2_out));
  Multiplexer #(.enable("false")) multiplexer_8 (
    .in0(instruction[4]), .in1(outM[4]), .out(multiplexer_8_out[0]), .sel(and_2_out));
  and and_3 (and_3_out, not_2_out, instruction[4]);
  Multiplexer #(.enable("false")) multiplexer_9 (
    .in0(instruction[11]), .in1(outM[11]), .out(multiplexer_12_out[3]), .sel(and_2_out));
  Multiplexer #(.enable("false")) multiplexer_10 (
    .in0(instruction[10]), .in1(outM[10]), .out(multiplexer_12_out[2]), .sel(and_2_out));
  Multiplexer #(.enable("false")) multiplexer_11 (
    .in0(instruction[9]), .in1(outM[9]), .out(multiplexer_12_out[1]), .sel(and_2_out));
  Multiplexer #(.enable("false")) multiplexer_12 (
    .in0(instruction[8]), .in1(outM[8]), .out(multiplexer_12_out[0]), .sel(and_2_out));
  Multiplexer #(.enable("false")) multiplexer_13 (
    .in0(instruction[15]), .in1(outM[15]), .out(multiplexer_16_out[3]), .sel(and_2_out));
  Multiplexer #(.enable("false")) multiplexer_14 (
    .in0(instruction[14]), .in1(outM[14]), .out(multiplexer_16_out[2]), .sel(and_2_out));
  Multiplexer #(.enable("false")) multiplexer_15 (
    .in0(instruction[13]), .in1(outM[13]), .out(multiplexer_16_out[1]), .sel(and_2_out));
  Multiplexer #(.enable("false")) multiplexer_16 (
    .in0(instruction[12]), .in1(outM[12]), .out(multiplexer_16_out[0]), .sel(and_2_out));
  Register #(.width(1)) register_1 (.D(multiplexer_4_out[3]), .en(or_1_out), .Q(addressM[3]), .clk(clk));  // open: clr
  Register #(.width(1)) register_2 (.D(multiplexer_4_out[2]), .en(or_1_out), .Q(addressM[2]), .clk(clk));  // open: clr
  Register #(.width(1)) register_3 (.D(multiplexer_4_out[1]), .en(or_1_out), .Q(addressM[1]), .clk(clk));  // open: clr
  Register #(.width(1)) register_4 (.D(multiplexer_4_out[0]), .en(or_1_out), .Q(addressM[0]), .clk(clk));  // open: clr
  Register #(.width(1)) register_5 (.D(multiplexer_8_out[3]), .en(or_1_out), .Q(addressM[7]), .clk(clk));  // open: clr
  Register #(.width(1)) register_6 (.D(multiplexer_8_out[2]), .en(or_1_out), .Q(addressM[6]), .clk(clk));  // open: clr
  Register #(.width(1)) register_7 (.D(multiplexer_8_out[1]), .en(or_1_out), .Q(addressM[5]), .clk(clk));  // open: clr
  Register #(.width(1)) register_8 (.D(multiplexer_8_out[0]), .en(or_1_out), .Q(addressM[4]), .clk(clk));  // open: clr
  Register #(.width(1)) register_9 (
    .D(multiplexer_12_out[3]), .en(or_1_out), .Q(addressM[11]), .clk(clk));  // open: clr
  Register #(.width(1)) register_10 (
    .D(multiplexer_12_out[2]), .en(or_1_out), .Q(addressM[10]), .clk(clk));  // open: clr
  Register #(.width(1)) register_11 (
    .D(multiplexer_12_out[1]), .en(or_1_out), .Q(addressM[9]), .clk(clk));  // open: clr
  Register #(.width(1)) register_12 (
    .D(multiplexer_12_out[0]), .en(or_1_out), .Q(addressM[8]), .clk(clk));  // open: clr
  Register #(.width(1)) register_13 (
    .D(multiplexer_16_out[3]), .en(or_1_out), .Q(register_13_q[15]), .clk(clk));  // open: clr
  Register #(.width(1)) register_14 (
    .D(multiplexer_16_out[2]), .en(or_1_out), .Q(addressM[14]), .clk(clk));  // open: clr
  Register #(.width(1)) register_15 (
    .D(multiplexer_16_out[1]), .en(or_1_out), .Q(addressM[13]), .clk(clk));  // open: clr
  Register #(.width(1)) register_16 (
    .D(multiplexer_16_out[0]), .en(or_1_out), .Q(addressM[12]), .clk(clk));  // open: clr
  Multiplexer #(.enable("false")) multiplexer_17 (
    .in0(addressM[3]), .in1(inM[3]), .out(multiplexer_20_out[3]), .sel(instruction[12]));
  Multiplexer #(.enable("false")) multiplexer_18 (
    .in0(addressM[2]), .in1(inM[2]), .out(multiplexer_20_out[2]), .sel(instruction[12]));
  Multiplexer #(.enable("false")) multiplexer_19 (
    .in0(addressM[1]), .in1(inM[1]), .out(multiplexer_20_out[1]), .sel(instruction[12]));
  Multiplexer #(.enable("false")) multiplexer_20 (
    .in0(addressM[0]), .in1(inM[0]), .out(multiplexer_20_out[0]), .sel(instruction[12]));
  Register #(.width(1)) register_17 (.D(outM[3]), .en(and_3_out), .Q(register_20_q[3]), .clk(clk));  // open: clr
  Register #(.width(1)) register_18 (.D(outM[2]), .en(and_3_out), .Q(register_20_q[2]), .clk(clk));  // open: clr
  Register #(.width(1)) register_19 (.D(outM[1]), .en(and_3_out), .Q(register_20_q[1]), .clk(clk));  // open: clr
  Register #(.width(1)) register_20 (.D(outM[0]), .en(and_3_out), .Q(register_20_q[0]), .clk(clk));  // open: clr
  Multiplexer #(.enable("false")) multiplexer_21 (
    .in0(addressM[7]), .in1(inM[7]), .out(multiplexer_24_out[3]), .sel(instruction[12]));
  Multiplexer #(.enable("false")) multiplexer_22 (
    .in0(addressM[6]), .in1(inM[6]), .out(multiplexer_24_out[2]), .sel(instruction[12]));
  Multiplexer #(.enable("false")) multiplexer_23 (
    .in0(addressM[5]), .in1(inM[5]), .out(multiplexer_24_out[1]), .sel(instruction[12]));
  Multiplexer #(.enable("false")) multiplexer_24 (
    .in0(addressM[4]), .in1(inM[4]), .out(multiplexer_24_out[0]), .sel(instruction[12]));
  Register #(.width(1)) register_21 (.D(outM[7]), .en(and_3_out), .Q(register_20_q[7]), .clk(clk));  // open: clr
  Register #(.width(1)) register_22 (.D(outM[6]), .en(and_3_out), .Q(register_20_q[6]), .clk(clk));  // open: clr
  Register #(.width(1)) register_23 (.D(outM[5]), .en(and_3_out), .Q(register_20_q[5]), .clk(clk));  // open: clr
  Register #(.width(1)) register_24 (.D(outM[4]), .en(and_3_out), .Q(register_20_q[4]), .clk(clk));  // open: clr
  Register #(.width(1)) register_25 (.D(outM[11]), .en(and_3_out), .Q(register_20_q[11]), .clk(clk));  // open: clr
  Register #(.width(1)) register_26 (.D(outM[10]), .en(and_3_out), .Q(register_20_q[10]), .clk(clk));  // open: clr
  Register #(.width(1)) register_27 (.D(outM[9]), .en(and_3_out), .Q(register_20_q[9]), .clk(clk));  // open: clr
  Register #(.width(1)) register_28 (.D(outM[8]), .en(and_3_out), .Q(register_20_q[8]), .clk(clk));  // open: clr
  Multiplexer #(.enable("false")) multiplexer_25 (
    .in0(addressM[11]), .in1(inM[11]), .out(multiplexer_28_out[3]), .sel(instruction[12]));
  Multiplexer #(.enable("false")) multiplexer_26 (
    .in0(addressM[10]), .in1(inM[10]), .out(multiplexer_28_out[2]), .sel(instruction[12]));
  Multiplexer #(.enable("false")) multiplexer_27 (
    .in0(addressM[9]), .in1(inM[9]), .out(multiplexer_28_out[1]), .sel(instruction[12]));
  Multiplexer #(.enable("false")) multiplexer_28 (
    .in0(addressM[8]), .in1(inM[8]), .out(multiplexer_28_out[0]), .sel(instruction[12]));
  Register #(.width(1)) register_29 (.D(outM[15]), .en(and_3_out), .Q(register_20_q[15]), .clk(clk));  // open: clr
  Register #(.width(1)) register_30 (.D(outM[14]), .en(and_3_out), .Q(register_20_q[14]), .clk(clk));  // open: clr
  Register #(.width(1)) register_31 (.D(outM[13]), .en(and_3_out), .Q(register_20_q[13]), .clk(clk));  // open: clr
  Register #(.width(1)) register_32 (.D(outM[12]), .en(and_3_out), .Q(register_20_q[12]), .clk(clk));  // open: clr
  Multiplexer #(.enable("false")) multiplexer_29 (
    .in0(register_13_q[15]), .in1(inM[15]), .out(multiplexer_32_out[3]), .sel(instruction[12]));
  Multiplexer #(.enable("false")) multiplexer_30 (
    .in0(addressM[14]), .in1(inM[14]), .out(multiplexer_32_out[2]), .sel(instruction[12]));
  Multiplexer #(.enable("false")) multiplexer_31 (
    .in0(addressM[13]), .in1(inM[13]), .out(multiplexer_32_out[1]), .sel(instruction[12]));
  Multiplexer #(.enable("false")) multiplexer_32 (
    .in0(addressM[12]), .in1(inM[12]), .out(multiplexer_32_out[0]), .sel(instruction[12]));
  PC pc_1 (
    .in({register_13_q[15], addressM}), .reset(reset), .load(and_5_out), .inc(not_5_out),
    .out({pc_1_out[15], pc}), .clk(clk));
  or or_2 (or_2_out, outM[13], outM[12]);
  or or_3 (or_3_out, outM[15], outM[14]);
  or or_4 (or_4_out, or_3_out, or_2_out);
  ALU alu_1 (
    .x(register_20_q), .y({multiplexer_32_out, multiplexer_28_out, multiplexer_24_out, multiplexer_20_out}),
    .out(outM), .zx(instruction[11]), .zy(instruction[9]), .nx(instruction[10]), .ny(instruction[8]),
    .f(instruction[7]), .no(instruction[6]));
  or or_5 (or_5_out, outM[11], outM[10]);
  or or_6 (or_6_out, outM[9], outM[8]);
  or or_7 (or_7_out, outM[7], outM[6]);
  or or_8 (or_8_out, or_5_out, or_6_out);
  or or_9 (or_9_out, or_4_out, or_8_out);
  or or_10 (or_10_out, or_9_out, or_15_out);
  not not_3 (not_3_out, or_10_out);
  or or_11 (or_11_out, outM[3], outM[2]);
  or or_12 (or_12_out, outM[5], outM[4]);
  or or_13 (or_13_out, or_11_out, or_18_out);
  or or_14 (or_14_out, or_7_out, or_12_out);
  or or_15 (or_15_out, or_14_out, or_13_out);
  or or_16 (or_16_out, or_28_out, not_3_out);
  not not_4 (not_4_out, or_16_out);
  and and_4 (and_4_out, not_4_out, instruction[0]);
  or or_17 (or_17_out, outM[15], outM[14]);
  or or_18 (or_18_out, outM[1], outM[0]);
  or or_19 (or_19_out, outM[13], outM[12]);
  or or_20 (or_20_out, or_17_out, or_19_out);
  or or_21 (or_21_out, and_6_out, and_7_out);
  or or_22 (or_22_out, and_4_out, or_21_out);
  and and_5 (and_5_out, not_2_out, or_22_out);
  not not_5 (not_5_out, and_5_out);
  or or_23 (or_23_out, outM[7], outM[6]);
  or or_24 (or_24_out, outM[9], outM[8]);
  or or_25 (or_25_out, outM[11], outM[10]);
  or or_26 (or_26_out, or_25_out, or_24_out);
  or or_27 (or_27_out, or_20_out, or_26_out);
  or or_28 (or_28_out, or_27_out, or_33_out);
  or or_29 (or_29_out, outM[5], outM[4]);
  or or_30 (or_30_out, outM[3], outM[2]);
  or or_31 (or_31_out, or_23_out, or_29_out);
  or or_32 (or_32_out, or_30_out, or_34_out);
  or or_33 (or_33_out, or_31_out, or_32_out);
  or or_34 (or_34_out, outM[1], outM[0]);
  and and_6 (and_6_out, or_28_out, instruction[2]);
  and and_7 (and_7_out, not_3_out, instruction[1]);

  // Notes on the sheet:
  //   A Register
  //   D Register
endmodule

module ALU (
  input  nx,
  input  zx,
  input  [15:0] x,
  input  f,
  input  no,
  input  ny,
  input  zy,
  input  [15:0] y,
  output [15:0] out
);

  wire adder_1_cout, adder_2_cout, adder_3_cout, adder_4_cout, adder_5_cout, adder_6_cout, adder_7_cout,
       adder_8_cout, adder_9_cout, adder_10_cout, adder_11_cout, adder_12_cout, adder_13_cout, adder_14_cout,
       adder_15_cout;
  wire [3:0] adder_1_out, adder_5_out, adder_9_out, adder_13_out, and_4_out, and_8_out, and_12_out,
       and_16_out, multiplexer_28_out, multiplexer_32_out, multiplexer_36_out, multiplexer_40_out,
       multiplexer_44_out, multiplexer_48_out, multiplexer_52_out, multiplexer_56_out, multiplexer_60_out,
       multiplexer_64_out, multiplexer_68_out, multiplexer_72_out, multiplexer_76_out, multiplexer_80_out;
  wire [11:0] multiplexer_4_out, multiplexer_8_out;
  wire [15:0] not_1_out, not_17_out, not_33_out, pull_resistor_1_node, pull_resistor_2_node;

  Pull_Resistor pull_resistor_1 (.node(pull_resistor_1_node));
  Pull_Resistor pull_resistor_2 (.node(pull_resistor_2_node));
  Multiplexer #(.enable("false")) multiplexer_1 (
    .in0(x[3]), .in1(pull_resistor_1_node[3]), .out(multiplexer_4_out[3]), .sel(zx));
  Multiplexer #(.enable("false")) multiplexer_2 (
    .in0(x[2]), .in1(pull_resistor_1_node[2]), .out(multiplexer_4_out[2]), .sel(zx));
  Multiplexer #(.enable("false")) multiplexer_3 (
    .in0(x[1]), .in1(pull_resistor_1_node[1]), .out(multiplexer_4_out[1]), .sel(zx));
  Multiplexer #(.enable("false")) multiplexer_4 (
    .in0(x[0]), .in1(pull_resistor_1_node[0]), .out(multiplexer_4_out[0]), .sel(zx));
  Multiplexer #(.enable("false")) multiplexer_5 (
    .in0(y[3]), .in1(pull_resistor_2_node[3]), .out(multiplexer_8_out[3]), .sel(zy));
  Multiplexer #(.enable("false")) multiplexer_6 (
    .in0(y[2]), .in1(pull_resistor_2_node[2]), .out(multiplexer_8_out[2]), .sel(zy));
  Multiplexer #(.enable("false")) multiplexer_7 (
    .in0(y[1]), .in1(pull_resistor_2_node[1]), .out(multiplexer_8_out[1]), .sel(zy));
  Multiplexer #(.enable("false")) multiplexer_8 (
    .in0(y[0]), .in1(pull_resistor_2_node[0]), .out(multiplexer_8_out[0]), .sel(zy));
  Multiplexer #(.enable("false")) multiplexer_9 (
    .in0(x[7]), .in1(pull_resistor_1_node[7]), .out(multiplexer_4_out[7]), .sel(zx));
  Multiplexer #(.enable("false")) multiplexer_10 (
    .in0(x[6]), .in1(pull_resistor_1_node[6]), .out(multiplexer_4_out[6]), .sel(zx));
  Multiplexer #(.enable("false")) multiplexer_11 (
    .in0(x[5]), .in1(pull_resistor_1_node[5]), .out(multiplexer_4_out[5]), .sel(zx));
  Multiplexer #(.enable("false")) multiplexer_12 (
    .in0(x[4]), .in1(pull_resistor_1_node[4]), .out(multiplexer_4_out[4]), .sel(zx));
  Multiplexer #(.enable("false")) multiplexer_13 (
    .in0(y[7]), .in1(pull_resistor_2_node[7]), .out(multiplexer_8_out[7]), .sel(zy));
  Multiplexer #(.enable("false")) multiplexer_14 (
    .in0(y[6]), .in1(pull_resistor_2_node[6]), .out(multiplexer_8_out[6]), .sel(zy));
  Multiplexer #(.enable("false")) multiplexer_15 (
    .in0(y[5]), .in1(pull_resistor_2_node[5]), .out(multiplexer_8_out[5]), .sel(zy));
  Multiplexer #(.enable("false")) multiplexer_16 (
    .in0(y[4]), .in1(pull_resistor_2_node[4]), .out(multiplexer_8_out[4]), .sel(zy));
  Multiplexer #(.enable("false")) multiplexer_17 (
    .in0(x[11]), .in1(pull_resistor_1_node[11]), .out(multiplexer_4_out[11]), .sel(zx));
  Multiplexer #(.enable("false")) multiplexer_18 (
    .in0(x[10]), .in1(pull_resistor_1_node[10]), .out(multiplexer_4_out[10]), .sel(zx));
  Multiplexer #(.enable("false")) multiplexer_19 (
    .in0(x[9]), .in1(pull_resistor_1_node[9]), .out(multiplexer_4_out[9]), .sel(zx));
  Multiplexer #(.enable("false")) multiplexer_20 (
    .in0(x[8]), .in1(pull_resistor_1_node[8]), .out(multiplexer_4_out[8]), .sel(zx));
  Multiplexer #(.enable("false")) multiplexer_21 (
    .in0(y[11]), .in1(pull_resistor_2_node[11]), .out(multiplexer_8_out[11]), .sel(zy));
  Multiplexer #(.enable("false")) multiplexer_22 (
    .in0(y[10]), .in1(pull_resistor_2_node[10]), .out(multiplexer_8_out[10]), .sel(zy));
  Multiplexer #(.enable("false")) multiplexer_23 (
    .in0(y[9]), .in1(pull_resistor_2_node[9]), .out(multiplexer_8_out[9]), .sel(zy));
  Multiplexer #(.enable("false")) multiplexer_24 (
    .in0(y[8]), .in1(pull_resistor_2_node[8]), .out(multiplexer_8_out[8]), .sel(zy));
  Multiplexer #(.enable("false")) multiplexer_25 (
    .in0(x[15]), .in1(pull_resistor_1_node[15]), .out(multiplexer_28_out[3]), .sel(zx));
  Multiplexer #(.enable("false")) multiplexer_26 (
    .in0(x[14]), .in1(pull_resistor_1_node[14]), .out(multiplexer_28_out[2]), .sel(zx));
  Multiplexer #(.enable("false")) multiplexer_27 (
    .in0(x[13]), .in1(pull_resistor_1_node[13]), .out(multiplexer_28_out[1]), .sel(zx));
  Multiplexer #(.enable("false")) multiplexer_28 (
    .in0(x[12]), .in1(pull_resistor_1_node[12]), .out(multiplexer_28_out[0]), .sel(zx));
  Multiplexer #(.enable("false")) multiplexer_29 (
    .in0(y[15]), .in1(pull_resistor_2_node[15]), .out(multiplexer_32_out[3]), .sel(zy));
  Multiplexer #(.enable("false")) multiplexer_30 (
    .in0(y[14]), .in1(pull_resistor_2_node[14]), .out(multiplexer_32_out[2]), .sel(zy));
  Multiplexer #(.enable("false")) multiplexer_31 (
    .in0(y[13]), .in1(pull_resistor_2_node[13]), .out(multiplexer_32_out[1]), .sel(zy));
  Multiplexer #(.enable("false")) multiplexer_32 (
    .in0(y[12]), .in1(pull_resistor_2_node[12]), .out(multiplexer_32_out[0]), .sel(zy));
  not not_1 (not_1_out[0], multiplexer_4_out[0]);
  not not_2 (not_1_out[1], multiplexer_4_out[1]);
  not not_3 (not_1_out[2], multiplexer_4_out[2]);
  not not_4 (not_1_out[3], multiplexer_4_out[3]);
  not not_5 (not_1_out[4], multiplexer_4_out[4]);
  not not_6 (not_1_out[5], multiplexer_4_out[5]);
  not not_7 (not_1_out[6], multiplexer_4_out[6]);
  not not_8 (not_1_out[7], multiplexer_4_out[7]);
  not not_9 (not_1_out[8], multiplexer_4_out[8]);
  not not_10 (not_1_out[9], multiplexer_4_out[9]);
  not not_11 (not_1_out[10], multiplexer_4_out[10]);
  not not_12 (not_1_out[11], multiplexer_4_out[11]);
  not not_13 (not_1_out[12], multiplexer_28_out[0]);
  not not_14 (not_1_out[13], multiplexer_28_out[1]);
  not not_15 (not_1_out[14], multiplexer_28_out[2]);
  not not_16 (not_1_out[15], multiplexer_28_out[3]);
  not not_17 (not_17_out[0], multiplexer_8_out[0]);
  not not_18 (not_17_out[1], multiplexer_8_out[1]);
  not not_19 (not_17_out[2], multiplexer_8_out[2]);
  not not_20 (not_17_out[3], multiplexer_8_out[3]);
  not not_21 (not_17_out[4], multiplexer_8_out[4]);
  not not_22 (not_17_out[5], multiplexer_8_out[5]);
  not not_23 (not_17_out[6], multiplexer_8_out[6]);
  not not_24 (not_17_out[7], multiplexer_8_out[7]);
  not not_25 (not_17_out[8], multiplexer_8_out[8]);
  not not_26 (not_17_out[9], multiplexer_8_out[9]);
  not not_27 (not_17_out[10], multiplexer_8_out[10]);
  not not_28 (not_17_out[11], multiplexer_8_out[11]);
  not not_29 (not_17_out[12], multiplexer_32_out[0]);
  not not_30 (not_17_out[13], multiplexer_32_out[1]);
  not not_31 (not_17_out[14], multiplexer_32_out[2]);
  not not_32 (not_17_out[15], multiplexer_32_out[3]);
  Multiplexer #(.enable("false")) multiplexer_33 (
    .in0(multiplexer_4_out[3]), .in1(not_1_out[3]), .out(multiplexer_36_out[3]), .sel(nx));
  Multiplexer #(.enable("false")) multiplexer_34 (
    .in0(multiplexer_4_out[2]), .in1(not_1_out[2]), .out(multiplexer_36_out[2]), .sel(nx));
  Multiplexer #(.enable("false")) multiplexer_35 (
    .in0(multiplexer_4_out[1]), .in1(not_1_out[1]), .out(multiplexer_36_out[1]), .sel(nx));
  Multiplexer #(.enable("false")) multiplexer_36 (
    .in0(multiplexer_4_out[0]), .in1(not_1_out[0]), .out(multiplexer_36_out[0]), .sel(nx));
  Multiplexer #(.enable("false")) multiplexer_37 (
    .in0(multiplexer_8_out[3]), .in1(not_17_out[3]), .out(multiplexer_40_out[3]), .sel(ny));
  Multiplexer #(.enable("false")) multiplexer_38 (
    .in0(multiplexer_8_out[2]), .in1(not_17_out[2]), .out(multiplexer_40_out[2]), .sel(ny));
  Multiplexer #(.enable("false")) multiplexer_39 (
    .in0(multiplexer_8_out[1]), .in1(not_17_out[1]), .out(multiplexer_40_out[1]), .sel(ny));
  Multiplexer #(.enable("false")) multiplexer_40 (
    .in0(multiplexer_8_out[0]), .in1(not_17_out[0]), .out(multiplexer_40_out[0]), .sel(ny));
  Multiplexer #(.enable("false")) multiplexer_41 (
    .in0(multiplexer_4_out[7]), .in1(not_1_out[7]), .out(multiplexer_44_out[3]), .sel(nx));
  Multiplexer #(.enable("false")) multiplexer_42 (
    .in0(multiplexer_4_out[6]), .in1(not_1_out[6]), .out(multiplexer_44_out[2]), .sel(nx));
  Multiplexer #(.enable("false")) multiplexer_43 (
    .in0(multiplexer_4_out[5]), .in1(not_1_out[5]), .out(multiplexer_44_out[1]), .sel(nx));
  Multiplexer #(.enable("false")) multiplexer_44 (
    .in0(multiplexer_4_out[4]), .in1(not_1_out[4]), .out(multiplexer_44_out[0]), .sel(nx));
  Multiplexer #(.enable("false")) multiplexer_45 (
    .in0(multiplexer_8_out[7]), .in1(not_17_out[7]), .out(multiplexer_48_out[3]), .sel(ny));
  Multiplexer #(.enable("false")) multiplexer_46 (
    .in0(multiplexer_8_out[6]), .in1(not_17_out[6]), .out(multiplexer_48_out[2]), .sel(ny));
  Multiplexer #(.enable("false")) multiplexer_47 (
    .in0(multiplexer_8_out[5]), .in1(not_17_out[5]), .out(multiplexer_48_out[1]), .sel(ny));
  Multiplexer #(.enable("false")) multiplexer_48 (
    .in0(multiplexer_8_out[4]), .in1(not_17_out[4]), .out(multiplexer_48_out[0]), .sel(ny));
  Multiplexer #(.enable("false")) multiplexer_49 (
    .in0(multiplexer_4_out[11]), .in1(not_1_out[11]), .out(multiplexer_52_out[3]), .sel(nx));
  Multiplexer #(.enable("false")) multiplexer_50 (
    .in0(multiplexer_4_out[10]), .in1(not_1_out[10]), .out(multiplexer_52_out[2]), .sel(nx));
  Multiplexer #(.enable("false")) multiplexer_51 (
    .in0(multiplexer_4_out[9]), .in1(not_1_out[9]), .out(multiplexer_52_out[1]), .sel(nx));
  Multiplexer #(.enable("false")) multiplexer_52 (
    .in0(multiplexer_4_out[8]), .in1(not_1_out[8]), .out(multiplexer_52_out[0]), .sel(nx));
  Multiplexer #(.enable("false")) multiplexer_53 (
    .in0(multiplexer_8_out[11]), .in1(not_17_out[11]), .out(multiplexer_56_out[3]), .sel(ny));
  Multiplexer #(.enable("false")) multiplexer_54 (
    .in0(multiplexer_8_out[10]), .in1(not_17_out[10]), .out(multiplexer_56_out[2]), .sel(ny));
  Multiplexer #(.enable("false")) multiplexer_55 (
    .in0(multiplexer_8_out[9]), .in1(not_17_out[9]), .out(multiplexer_56_out[1]), .sel(ny));
  Multiplexer #(.enable("false")) multiplexer_56 (
    .in0(multiplexer_8_out[8]), .in1(not_17_out[8]), .out(multiplexer_56_out[0]), .sel(ny));
  Multiplexer #(.enable("false")) multiplexer_57 (
    .in0(multiplexer_28_out[3]), .in1(not_1_out[15]), .out(multiplexer_60_out[3]), .sel(nx));
  Multiplexer #(.enable("false")) multiplexer_58 (
    .in0(multiplexer_28_out[2]), .in1(not_1_out[14]), .out(multiplexer_60_out[2]), .sel(nx));
  Multiplexer #(.enable("false")) multiplexer_59 (
    .in0(multiplexer_28_out[1]), .in1(not_1_out[13]), .out(multiplexer_60_out[1]), .sel(nx));
  Multiplexer #(.enable("false")) multiplexer_60 (
    .in0(multiplexer_28_out[0]), .in1(not_1_out[12]), .out(multiplexer_60_out[0]), .sel(nx));
  Multiplexer #(.enable("false")) multiplexer_61 (
    .in0(multiplexer_32_out[3]), .in1(not_17_out[15]), .out(multiplexer_64_out[3]), .sel(ny));
  Multiplexer #(.enable("false")) multiplexer_62 (
    .in0(multiplexer_32_out[2]), .in1(not_17_out[14]), .out(multiplexer_64_out[2]), .sel(ny));
  Multiplexer #(.enable("false")) multiplexer_63 (
    .in0(multiplexer_32_out[1]), .in1(not_17_out[13]), .out(multiplexer_64_out[1]), .sel(ny));
  Multiplexer #(.enable("false")) multiplexer_64 (
    .in0(multiplexer_32_out[0]), .in1(not_17_out[12]), .out(multiplexer_64_out[0]), .sel(ny));
  and and_1 (and_4_out[3], multiplexer_36_out[3], multiplexer_40_out[3]);
  and and_2 (and_4_out[2], multiplexer_36_out[2], multiplexer_40_out[2]);
  and and_3 (and_4_out[1], multiplexer_36_out[1], multiplexer_40_out[1]);
  and and_4 (and_4_out[0], multiplexer_36_out[0], multiplexer_40_out[0]);
  Adder #(.width(1)) adder_1 (
    .a(multiplexer_36_out[0]), .b(multiplexer_40_out[0]), .out(adder_1_out[0]), .cout(adder_1_cout));  // open: cin
  Adder #(.width(1)) adder_2 (
    .a(multiplexer_36_out[1]), .b(multiplexer_40_out[1]), .out(adder_1_out[1]), .cin(adder_1_cout),
    .cout(adder_2_cout));
  Adder #(.width(1)) adder_3 (
    .a(multiplexer_36_out[2]), .b(multiplexer_40_out[2]), .out(adder_1_out[2]), .cin(adder_2_cout),
    .cout(adder_3_cout));
  Adder #(.width(1)) adder_4 (
    .a(multiplexer_36_out[3]), .b(multiplexer_40_out[3]), .out(adder_1_out[3]), .cin(adder_3_cout),
    .cout(adder_4_cout));
  and and_5 (and_8_out[3], multiplexer_44_out[3], multiplexer_48_out[3]);
  and and_6 (and_8_out[2], multiplexer_44_out[2], multiplexer_48_out[2]);
  and and_7 (and_8_out[1], multiplexer_44_out[1], multiplexer_48_out[1]);
  and and_8 (and_8_out[0], multiplexer_44_out[0], multiplexer_48_out[0]);
  Adder #(.width(1)) adder_5 (
    .a(multiplexer_44_out[0]), .b(multiplexer_48_out[0]), .out(adder_5_out[0]), .cin(adder_4_cout),
    .cout(adder_5_cout));
  Adder #(.width(1)) adder_6 (
    .a(multiplexer_44_out[1]), .b(multiplexer_48_out[1]), .out(adder_5_out[1]), .cin(adder_5_cout),
    .cout(adder_6_cout));
  Adder #(.width(1)) adder_7 (
    .a(multiplexer_44_out[2]), .b(multiplexer_48_out[2]), .out(adder_5_out[2]), .cin(adder_6_cout),
    .cout(adder_7_cout));
  Adder #(.width(1)) adder_8 (
    .a(multiplexer_44_out[3]), .b(multiplexer_48_out[3]), .out(adder_5_out[3]), .cin(adder_7_cout),
    .cout(adder_8_cout));
  and and_9 (and_12_out[3], multiplexer_52_out[3], multiplexer_56_out[3]);
  and and_10 (and_12_out[2], multiplexer_52_out[2], multiplexer_56_out[2]);
  and and_11 (and_12_out[1], multiplexer_52_out[1], multiplexer_56_out[1]);
  and and_12 (and_12_out[0], multiplexer_52_out[0], multiplexer_56_out[0]);
  Adder #(.width(1)) adder_9 (
    .a(multiplexer_52_out[0]), .b(multiplexer_56_out[0]), .out(adder_9_out[0]), .cin(adder_8_cout),
    .cout(adder_9_cout));
  Adder #(.width(1)) adder_10 (
    .a(multiplexer_52_out[1]), .b(multiplexer_56_out[1]), .out(adder_9_out[1]), .cin(adder_9_cout),
    .cout(adder_10_cout));
  Adder #(.width(1)) adder_11 (
    .a(multiplexer_52_out[2]), .b(multiplexer_56_out[2]), .out(adder_9_out[2]), .cin(adder_10_cout),
    .cout(adder_11_cout));
  Adder #(.width(1)) adder_12 (
    .a(multiplexer_52_out[3]), .b(multiplexer_56_out[3]), .out(adder_9_out[3]), .cin(adder_11_cout),
    .cout(adder_12_cout));
  and and_13 (and_16_out[3], multiplexer_60_out[3], multiplexer_64_out[3]);
  and and_14 (and_16_out[2], multiplexer_60_out[2], multiplexer_64_out[2]);
  and and_15 (and_16_out[1], multiplexer_60_out[1], multiplexer_64_out[1]);
  and and_16 (and_16_out[0], multiplexer_60_out[0], multiplexer_64_out[0]);
  Adder #(.width(1)) adder_13 (
    .a(multiplexer_60_out[0]), .b(multiplexer_64_out[0]), .out(adder_13_out[0]), .cin(adder_12_cout),
    .cout(adder_13_cout));
  Adder #(.width(1)) adder_14 (
    .a(multiplexer_60_out[1]), .b(multiplexer_64_out[1]), .out(adder_13_out[1]), .cin(adder_13_cout),
    .cout(adder_14_cout));
  Adder #(.width(1)) adder_15 (
    .a(multiplexer_60_out[2]), .b(multiplexer_64_out[2]), .out(adder_13_out[2]), .cin(adder_14_cout),
    .cout(adder_15_cout));
  Adder #(.width(1)) adder_16 (
    .a(multiplexer_60_out[3]), .b(multiplexer_64_out[3]), .out(adder_13_out[3]), .cin(adder_15_cout));  // open: cout
  Multiplexer #(.enable("false")) multiplexer_65 (
    .in0(and_4_out[3]), .in1(adder_1_out[3]), .out(multiplexer_68_out[3]), .sel(f));
  Multiplexer #(.enable("false")) multiplexer_66 (
    .in0(and_4_out[2]), .in1(adder_1_out[2]), .out(multiplexer_68_out[2]), .sel(f));
  Multiplexer #(.enable("false")) multiplexer_67 (
    .in0(and_4_out[1]), .in1(adder_1_out[1]), .out(multiplexer_68_out[1]), .sel(f));
  Multiplexer #(.enable("false")) multiplexer_68 (
    .in0(and_4_out[0]), .in1(adder_1_out[0]), .out(multiplexer_68_out[0]), .sel(f));
  Multiplexer #(.enable("false")) multiplexer_69 (
    .in0(and_8_out[3]), .in1(adder_5_out[3]), .out(multiplexer_72_out[3]), .sel(f));
  Multiplexer #(.enable("false")) multiplexer_70 (
    .in0(and_8_out[2]), .in1(adder_5_out[2]), .out(multiplexer_72_out[2]), .sel(f));
  Multiplexer #(.enable("false")) multiplexer_71 (
    .in0(and_8_out[1]), .in1(adder_5_out[1]), .out(multiplexer_72_out[1]), .sel(f));
  Multiplexer #(.enable("false")) multiplexer_72 (
    .in0(and_8_out[0]), .in1(adder_5_out[0]), .out(multiplexer_72_out[0]), .sel(f));
  Multiplexer #(.enable("false")) multiplexer_73 (
    .in0(and_12_out[3]), .in1(adder_9_out[3]), .out(multiplexer_76_out[3]), .sel(f));
  Multiplexer #(.enable("false")) multiplexer_74 (
    .in0(and_12_out[2]), .in1(adder_9_out[2]), .out(multiplexer_76_out[2]), .sel(f));
  Multiplexer #(.enable("false")) multiplexer_75 (
    .in0(and_12_out[1]), .in1(adder_9_out[1]), .out(multiplexer_76_out[1]), .sel(f));
  Multiplexer #(.enable("false")) multiplexer_76 (
    .in0(and_12_out[0]), .in1(adder_9_out[0]), .out(multiplexer_76_out[0]), .sel(f));
  Multiplexer #(.enable("false")) multiplexer_77 (
    .in0(and_16_out[3]), .in1(adder_13_out[3]), .out(multiplexer_80_out[3]), .sel(f));
  Multiplexer #(.enable("false")) multiplexer_78 (
    .in0(and_16_out[2]), .in1(adder_13_out[2]), .out(multiplexer_80_out[2]), .sel(f));
  Multiplexer #(.enable("false")) multiplexer_79 (
    .in0(and_16_out[1]), .in1(adder_13_out[1]), .out(multiplexer_80_out[1]), .sel(f));
  Multiplexer #(.enable("false")) multiplexer_80 (
    .in0(and_16_out[0]), .in1(adder_13_out[0]), .out(multiplexer_80_out[0]), .sel(f));
  not not_33 (not_33_out[0], multiplexer_68_out[0]);
  not not_34 (not_33_out[1], multiplexer_68_out[1]);
  not not_35 (not_33_out[2], multiplexer_68_out[2]);
  not not_36 (not_33_out[3], multiplexer_68_out[3]);
  not not_37 (not_33_out[4], multiplexer_72_out[0]);
  not not_38 (not_33_out[5], multiplexer_72_out[1]);
  not not_39 (not_33_out[6], multiplexer_72_out[2]);
  not not_40 (not_33_out[7], multiplexer_72_out[3]);
  not not_41 (not_33_out[8], multiplexer_76_out[0]);
  not not_42 (not_33_out[9], multiplexer_76_out[1]);
  not not_43 (not_33_out[10], multiplexer_76_out[2]);
  not not_44 (not_33_out[11], multiplexer_76_out[3]);
  not not_45 (not_33_out[12], multiplexer_80_out[0]);
  not not_46 (not_33_out[13], multiplexer_80_out[1]);
  not not_47 (not_33_out[14], multiplexer_80_out[2]);
  not not_48 (not_33_out[15], multiplexer_80_out[3]);
  Multiplexer #(.enable("false")) multiplexer_81 (
    .in0(multiplexer_68_out[3]), .in1(not_33_out[3]), .out(out[3]), .sel(no));
  Multiplexer #(.enable("false")) multiplexer_82 (
    .in0(multiplexer_68_out[2]), .in1(not_33_out[2]), .out(out[2]), .sel(no));
  Multiplexer #(.enable("false")) multiplexer_83 (
    .in0(multiplexer_68_out[1]), .in1(not_33_out[1]), .out(out[1]), .sel(no));
  Multiplexer #(.enable("false")) multiplexer_84 (
    .in0(multiplexer_68_out[0]), .in1(not_33_out[0]), .out(out[0]), .sel(no));
  Multiplexer #(.enable("false")) multiplexer_85 (
    .in0(multiplexer_72_out[3]), .in1(not_33_out[7]), .out(out[7]), .sel(no));
  Multiplexer #(.enable("false")) multiplexer_86 (
    .in0(multiplexer_72_out[2]), .in1(not_33_out[6]), .out(out[6]), .sel(no));
  Multiplexer #(.enable("false")) multiplexer_87 (
    .in0(multiplexer_72_out[1]), .in1(not_33_out[5]), .out(out[5]), .sel(no));
  Multiplexer #(.enable("false")) multiplexer_88 (
    .in0(multiplexer_72_out[0]), .in1(not_33_out[4]), .out(out[4]), .sel(no));
  Multiplexer #(.enable("false")) multiplexer_89 (
    .in0(multiplexer_76_out[3]), .in1(not_33_out[11]), .out(out[11]), .sel(no));
  Multiplexer #(.enable("false")) multiplexer_90 (
    .in0(multiplexer_76_out[2]), .in1(not_33_out[10]), .out(out[10]), .sel(no));
  Multiplexer #(.enable("false")) multiplexer_91 (
    .in0(multiplexer_76_out[1]), .in1(not_33_out[9]), .out(out[9]), .sel(no));
  Multiplexer #(.enable("false")) multiplexer_92 (
    .in0(multiplexer_76_out[0]), .in1(not_33_out[8]), .out(out[8]), .sel(no));
  Multiplexer #(.enable("false")) multiplexer_93 (
    .in0(multiplexer_80_out[3]), .in1(not_33_out[15]), .out(out[15]), .sel(no));
  Multiplexer #(.enable("false")) multiplexer_94 (
    .in0(multiplexer_80_out[2]), .in1(not_33_out[14]), .out(out[14]), .sel(no));
  Multiplexer #(.enable("false")) multiplexer_95 (
    .in0(multiplexer_80_out[1]), .in1(not_33_out[13]), .out(out[13]), .sel(no));
  Multiplexer #(.enable("false")) multiplexer_96 (
    .in0(multiplexer_80_out[0]), .in1(not_33_out[12]), .out(out[12]), .sel(no));
endmodule

module PC (
  input  [15:0] in,
  input  reset,
  input  load,
  input  inc,
  input  clk,
  output [15:0] out
);

  wire adder_1_cout, adder_2_cout, adder_3_cout, adder_4_cout, adder_5_cout, adder_6_cout, adder_7_cout,
       adder_8_cout, adder_9_cout, adder_10_cout, adder_11_cout, adder_12_cout, adder_13_cout, adder_14_cout,
       adder_15_cout, or_1_out, or_2_out;
  wire [3:0] adder_13_out, multiplexer_4_out, multiplexer_8_out, multiplexer_12_out, multiplexer_16_out,
       multiplexer_20_out, multiplexer_24_out, multiplexer_28_out, multiplexer_32_out;
  wire [11:0] adder_1_out;
  wire [15:0] pull_resistor_1_node, pull_resistor_3_node;

  Pull_Resistor #(.pull(1)) pull_resistor_1 (.node(pull_resistor_1_node[0]));
  Pull_Resistor pull_resistor_2 (.node(pull_resistor_1_node[15]));
  Adder #(.width(1)) adder_1 (
    .a(out[0]), .b(pull_resistor_1_node[0]), .out(adder_1_out[0]), .cout(adder_1_cout));  // open: cin
  Adder #(.width(1)) adder_2 (
    .a(out[1]), .b(pull_resistor_1_node[15]), .out(adder_1_out[1]), .cin(adder_1_cout), .cout(adder_2_cout));
  Adder #(.width(1)) adder_3 (
    .a(out[2]), .b(pull_resistor_1_node[15]), .out(adder_1_out[2]), .cin(adder_2_cout), .cout(adder_3_cout));
  Adder #(.width(1)) adder_4 (
    .a(out[3]), .b(pull_resistor_1_node[15]), .out(adder_1_out[3]), .cin(adder_3_cout), .cout(adder_4_cout));
  Adder #(.width(1)) adder_5 (
    .a(out[4]), .b(pull_resistor_1_node[15]), .out(adder_1_out[4]), .cin(adder_4_cout), .cout(adder_5_cout));
  Adder #(.width(1)) adder_6 (
    .a(out[5]), .b(pull_resistor_1_node[15]), .out(adder_1_out[5]), .cin(adder_5_cout), .cout(adder_6_cout));
  Adder #(.width(1)) adder_7 (
    .a(out[6]), .b(pull_resistor_1_node[15]), .out(adder_1_out[6]), .cin(adder_6_cout), .cout(adder_7_cout));
  Adder #(.width(1)) adder_8 (
    .a(out[7]), .b(pull_resistor_1_node[15]), .out(adder_1_out[7]), .cin(adder_7_cout), .cout(adder_8_cout));
  Adder #(.width(1)) adder_9 (
    .a(out[8]), .b(pull_resistor_1_node[15]), .out(adder_1_out[8]), .cin(adder_8_cout), .cout(adder_9_cout));
  Adder #(.width(1)) adder_10 (
    .a(out[9]), .b(pull_resistor_1_node[15]), .out(adder_1_out[9]), .cin(adder_9_cout), .cout(adder_10_cout));
  Adder #(.width(1)) adder_11 (
    .a(out[10]), .b(pull_resistor_1_node[15]), .out(adder_1_out[10]), .cin(adder_10_cout),
    .cout(adder_11_cout));
  Adder #(.width(1)) adder_12 (
    .a(out[11]), .b(pull_resistor_1_node[15]), .out(adder_1_out[11]), .cin(adder_11_cout),
    .cout(adder_12_cout));
  Adder #(.width(1)) adder_13 (
    .a(out[12]), .b(pull_resistor_1_node[15]), .out(adder_13_out[0]), .cin(adder_12_cout),
    .cout(adder_13_cout));
  Adder #(.width(1)) adder_14 (
    .a(out[13]), .b(pull_resistor_1_node[15]), .out(adder_13_out[1]), .cin(adder_13_cout),
    .cout(adder_14_cout));
  Adder #(.width(1)) adder_15 (
    .a(out[14]), .b(pull_resistor_1_node[15]), .out(adder_13_out[2]), .cin(adder_14_cout),
    .cout(adder_15_cout));
  Adder #(.width(1)) adder_16 (
    .a(out[15]), .b(pull_resistor_1_node[15]), .out(adder_13_out[3]), .cin(adder_15_cout));  // open: cout
  Multiplexer #(.enable("false")) multiplexer_1 (
    .in0(adder_1_out[3]), .in1(in[3]), .out(multiplexer_4_out[3]), .sel(load));
  Multiplexer #(.enable("false")) multiplexer_2 (
    .in0(adder_1_out[2]), .in1(in[2]), .out(multiplexer_4_out[2]), .sel(load));
  Multiplexer #(.enable("false")) multiplexer_3 (
    .in0(adder_1_out[1]), .in1(in[1]), .out(multiplexer_4_out[1]), .sel(load));
  Multiplexer #(.enable("false")) multiplexer_4 (
    .in0(adder_1_out[0]), .in1(in[0]), .out(multiplexer_4_out[0]), .sel(load));
  Multiplexer #(.enable("false")) multiplexer_5 (
    .in0(adder_1_out[7]), .in1(in[7]), .out(multiplexer_8_out[3]), .sel(load));
  Multiplexer #(.enable("false")) multiplexer_6 (
    .in0(adder_1_out[6]), .in1(in[6]), .out(multiplexer_8_out[2]), .sel(load));
  Multiplexer #(.enable("false")) multiplexer_7 (
    .in0(adder_1_out[5]), .in1(in[5]), .out(multiplexer_8_out[1]), .sel(load));
  Multiplexer #(.enable("false")) multiplexer_8 (
    .in0(adder_1_out[4]), .in1(in[4]), .out(multiplexer_8_out[0]), .sel(load));
  Multiplexer #(.enable("false")) multiplexer_9 (
    .in0(adder_1_out[11]), .in1(in[11]), .out(multiplexer_12_out[3]), .sel(load));
  Multiplexer #(.enable("false")) multiplexer_10 (
    .in0(adder_1_out[10]), .in1(in[10]), .out(multiplexer_12_out[2]), .sel(load));
  Multiplexer #(.enable("false")) multiplexer_11 (
    .in0(adder_1_out[9]), .in1(in[9]), .out(multiplexer_12_out[1]), .sel(load));
  Multiplexer #(.enable("false")) multiplexer_12 (
    .in0(adder_1_out[8]), .in1(in[8]), .out(multiplexer_12_out[0]), .sel(load));
  Multiplexer #(.enable("false")) multiplexer_13 (
    .in0(adder_13_out[3]), .in1(in[15]), .out(multiplexer_16_out[3]), .sel(load));
  Multiplexer #(.enable("false")) multiplexer_14 (
    .in0(adder_13_out[2]), .in1(in[14]), .out(multiplexer_16_out[2]), .sel(load));
  Multiplexer #(.enable("false")) multiplexer_15 (
    .in0(adder_13_out[1]), .in1(in[13]), .out(multiplexer_16_out[1]), .sel(load));
  Multiplexer #(.enable("false")) multiplexer_16 (
    .in0(adder_13_out[0]), .in1(in[12]), .out(multiplexer_16_out[0]), .sel(load));
  Pull_Resistor pull_resistor_3 (.node(pull_resistor_3_node));
  Multiplexer #(.enable("false")) multiplexer_17 (
    .in0(multiplexer_4_out[3]), .in1(pull_resistor_3_node[3]), .out(multiplexer_20_out[3]), .sel(reset));
  Multiplexer #(.enable("false")) multiplexer_18 (
    .in0(multiplexer_4_out[2]), .in1(pull_resistor_3_node[2]), .out(multiplexer_20_out[2]), .sel(reset));
  Multiplexer #(.enable("false")) multiplexer_19 (
    .in0(multiplexer_4_out[1]), .in1(pull_resistor_3_node[1]), .out(multiplexer_20_out[1]), .sel(reset));
  Multiplexer #(.enable("false")) multiplexer_20 (
    .in0(multiplexer_4_out[0]), .in1(pull_resistor_3_node[0]), .out(multiplexer_20_out[0]), .sel(reset));
  or or_1 (or_1_out, load, inc);
  Multiplexer #(.enable("false")) multiplexer_21 (
    .in0(multiplexer_8_out[3]), .in1(pull_resistor_3_node[7]), .out(multiplexer_24_out[3]), .sel(reset));
  Multiplexer #(.enable("false")) multiplexer_22 (
    .in0(multiplexer_8_out[2]), .in1(pull_resistor_3_node[6]), .out(multiplexer_24_out[2]), .sel(reset));
  Multiplexer #(.enable("false")) multiplexer_23 (
    .in0(multiplexer_8_out[1]), .in1(pull_resistor_3_node[5]), .out(multiplexer_24_out[1]), .sel(reset));
  Multiplexer #(.enable("false")) multiplexer_24 (
    .in0(multiplexer_8_out[0]), .in1(pull_resistor_3_node[4]), .out(multiplexer_24_out[0]), .sel(reset));
  or or_2 (or_2_out, reset, or_1_out);
  Multiplexer #(.enable("false")) multiplexer_25 (
    .in0(multiplexer_12_out[3]), .in1(pull_resistor_3_node[11]), .out(multiplexer_28_out[3]), .sel(reset));
  Multiplexer #(.enable("false")) multiplexer_26 (
    .in0(multiplexer_12_out[2]), .in1(pull_resistor_3_node[10]), .out(multiplexer_28_out[2]), .sel(reset));
  Multiplexer #(.enable("false")) multiplexer_27 (
    .in0(multiplexer_12_out[1]), .in1(pull_resistor_3_node[9]), .out(multiplexer_28_out[1]), .sel(reset));
  Multiplexer #(.enable("false")) multiplexer_28 (
    .in0(multiplexer_12_out[0]), .in1(pull_resistor_3_node[8]), .out(multiplexer_28_out[0]), .sel(reset));
  Multiplexer #(.enable("false")) multiplexer_29 (
    .in0(multiplexer_16_out[3]), .in1(pull_resistor_3_node[15]), .out(multiplexer_32_out[3]), .sel(reset));
  Multiplexer #(.enable("false")) multiplexer_30 (
    .in0(multiplexer_16_out[2]), .in1(pull_resistor_3_node[14]), .out(multiplexer_32_out[2]), .sel(reset));
  Multiplexer #(.enable("false")) multiplexer_31 (
    .in0(multiplexer_16_out[1]), .in1(pull_resistor_3_node[13]), .out(multiplexer_32_out[1]), .sel(reset));
  Multiplexer #(.enable("false")) multiplexer_32 (
    .in0(multiplexer_16_out[0]), .in1(pull_resistor_3_node[12]), .out(multiplexer_32_out[0]), .sel(reset));
  Register #(.width(1)) register_1 (.D(multiplexer_20_out[3]), .en(or_2_out), .Q(out[3]), .clk(clk));  // open: clr
  Register #(.width(1)) register_2 (.D(multiplexer_20_out[2]), .en(or_2_out), .Q(out[2]), .clk(clk));  // open: clr
  Register #(.width(1)) register_3 (.D(multiplexer_20_out[1]), .en(or_2_out), .Q(out[1]), .clk(clk));  // open: clr
  Register #(.width(1)) register_4 (.D(multiplexer_20_out[0]), .en(or_2_out), .Q(out[0]), .clk(clk));  // open: clr
  Register #(.width(1)) register_5 (.D(multiplexer_24_out[3]), .en(or_2_out), .Q(out[7]), .clk(clk));  // open: clr
  Register #(.width(1)) register_6 (.D(multiplexer_24_out[2]), .en(or_2_out), .Q(out[6]), .clk(clk));  // open: clr
  Register #(.width(1)) register_7 (.D(multiplexer_24_out[1]), .en(or_2_out), .Q(out[5]), .clk(clk));  // open: clr
  Register #(.width(1)) register_8 (.D(multiplexer_24_out[0]), .en(or_2_out), .Q(out[4]), .clk(clk));  // open: clr
  Register #(.width(1)) register_9 (.D(multiplexer_28_out[3]), .en(or_2_out), .Q(out[11]), .clk(clk));  // open: clr
  Register #(.width(1)) register_10 (.D(multiplexer_28_out[2]), .en(or_2_out), .Q(out[10]), .clk(clk));  // open: clr
  Register #(.width(1)) register_11 (.D(multiplexer_28_out[1]), .en(or_2_out), .Q(out[9]), .clk(clk));  // open: clr
  Register #(.width(1)) register_12 (.D(multiplexer_28_out[0]), .en(or_2_out), .Q(out[8]), .clk(clk));  // open: clr
  Register #(.width(1)) register_13 (.D(multiplexer_32_out[3]), .en(or_2_out), .Q(out[15]), .clk(clk));  // open: clr
  Register #(.width(1)) register_14 (.D(multiplexer_32_out[2]), .en(or_2_out), .Q(out[14]), .clk(clk));  // open: clr
  Register #(.width(1)) register_15 (.D(multiplexer_32_out[1]), .en(or_2_out), .Q(out[13]), .clk(clk));  // open: clr
  Register #(.width(1)) register_16 (.D(multiplexer_32_out[0]), .en(or_2_out), .Q(out[12]), .clk(clk));  // open: clr
endmodule

module MEMORY (
  input  [14:0] address,
  input  CLK,
  input  [15:0] in,
  input  load,
  output [15:0] out
);

  wire demultiplexer_1_out0, demultiplexer_1_out1, demultiplexer_2_out0, demultiplexer_2_out1,
       demultiplexer_3_out0, demultiplexer_3_out1, not_1_out, not_2_out, or_1_out;
  wire [15:0] multiplexer_1_out, multiplexer_2_out, pull_resistor_2_node, ram_1_data, ram_2_data;

  Demultiplexer #(.enable("false")) demultiplexer_1 (
    .out0(demultiplexer_1_out0), .out1(demultiplexer_1_out1), .in(demultiplexer_2_out0), .sel(address[14]));
  Demultiplexer #(.enable("false")) demultiplexer_2 (
    .out0(demultiplexer_2_out0), .out1(demultiplexer_2_out1), .in(load), .sel(address[13]));
  Demultiplexer #(.enable("false")) demultiplexer_3 (
    .out0(demultiplexer_3_out0), .out1(demultiplexer_3_out1), .in(demultiplexer_2_out1), .sel(address[14]));
  Pull_Resistor pull_resistor_1 (.node(demultiplexer_3_out1));
  or or_1 (or_1_out, demultiplexer_1_out0, demultiplexer_3_out0);
  not not_1 (not_1_out, or_1_out);
  not not_2 (not_2_out, demultiplexer_1_out1);
  RAM #(.addrWidth(14), .dataWidth(16), .bus("separate")) ram_1 (
    .addr(address[13:0]), .din(in), .data(ram_1_data), .str(or_1_out), .clk(CLK), .ld(not_1_out));  // open: sel, clr
  RAM #(.addrWidth(13), .dataWidth(16), .bus("separate")) ram_2 (
    .addr(address[12:0]), .din(in), .data(ram_2_data), .str(demultiplexer_1_out1), .clk(CLK), .ld(not_2_out));  // open: sel, clr
  Multiplexer #(.width(16), .enable("false")) multiplexer_1 (
    .in0(ram_1_data), .in1(ram_1_data), .out(multiplexer_1_out), .sel(address[13]));
  Multiplexer #(.width(16), .enable("false")) multiplexer_2 (
    .in0(ram_2_data), .in1(pull_resistor_2_node), .out(multiplexer_2_out), .sel(address[13]));
  Pull_Resistor pull_resistor_2 (.node(pull_resistor_2_node));
  Multiplexer #(.width(16), .enable("false")) multiplexer_3 (
    .in0(multiplexer_1_out), .in1(multiplexer_2_out), .out(out), .sel(address[14]));

  // Notes on the sheet:
  //   Main Memory 16K RAM
  //   Screen 8K RAM
endmodule

module mux16 (
  input  sel
);

  wire [3:0] multiplexer_4_out, multiplexer_8_out, multiplexer_12_out, multiplexer_16_out;
  wire [15:0] undriven, undriven_2;

  Multiplexer #(.enable("false")) multiplexer_1 (
    .in0(undriven[3]), .in1(undriven_2[3]), .out(multiplexer_4_out[3]), .sel(sel));
  Multiplexer #(.enable("false")) multiplexer_2 (
    .in0(undriven[2]), .in1(undriven_2[2]), .out(multiplexer_4_out[2]), .sel(sel));
  Multiplexer #(.enable("false")) multiplexer_3 (
    .in0(undriven[1]), .in1(undriven_2[1]), .out(multiplexer_4_out[1]), .sel(sel));
  Multiplexer #(.enable("false")) multiplexer_4 (
    .in0(undriven[0]), .in1(undriven_2[0]), .out(multiplexer_4_out[0]), .sel(sel));
  Multiplexer #(.enable("false")) multiplexer_5 (
    .in0(undriven[7]), .in1(undriven_2[7]), .out(multiplexer_8_out[3]), .sel(sel));
  Multiplexer #(.enable("false")) multiplexer_6 (
    .in0(undriven[6]), .in1(undriven_2[6]), .out(multiplexer_8_out[2]), .sel(sel));
  Multiplexer #(.enable("false")) multiplexer_7 (
    .in0(undriven[5]), .in1(undriven_2[5]), .out(multiplexer_8_out[1]), .sel(sel));
  Multiplexer #(.enable("false")) multiplexer_8 (
    .in0(undriven[4]), .in1(undriven_2[4]), .out(multiplexer_8_out[0]), .sel(sel));
  Multiplexer #(.enable("false")) multiplexer_9 (
    .in0(undriven[11]), .in1(undriven_2[11]), .out(multiplexer_12_out[3]), .sel(sel));
  Multiplexer #(.enable("false")) multiplexer_10 (
    .in0(undriven[10]), .in1(undriven_2[10]), .out(multiplexer_12_out[2]), .sel(sel));
  Multiplexer #(.enable("false")) multiplexer_11 (
    .in0(undriven[9]), .in1(undriven_2[9]), .out(multiplexer_12_out[1]), .sel(sel));
  Multiplexer #(.enable("false")) multiplexer_12 (
    .in0(undriven[8]), .in1(undriven_2[8]), .out(multiplexer_12_out[0]), .sel(sel));
  Multiplexer #(.enable("false")) multiplexer_13 (
    .in0(undriven[15]), .in1(undriven_2[15]), .out(multiplexer_16_out[3]), .sel(sel));
  Multiplexer #(.enable("false")) multiplexer_14 (
    .in0(undriven[14]), .in1(undriven_2[14]), .out(multiplexer_16_out[2]), .sel(sel));
  Multiplexer #(.enable("false")) multiplexer_15 (
    .in0(undriven[13]), .in1(undriven_2[13]), .out(multiplexer_16_out[1]), .sel(sel));
  Multiplexer #(.enable("false")) multiplexer_16 (
    .in0(undriven[12]), .in1(undriven_2[12]), .out(multiplexer_16_out[0]), .sel(sel));
endmodule

module register_16 (
  input  en,
  input  clk
);

  wire [15:0] register_4_q, undriven;

  Register #(.width(1)) register_1 (.D(undriven[3]), .en(en), .Q(register_4_q[3]), .clk(clk));  // open: clr
  Register #(.width(1)) register_2 (.D(undriven[2]), .en(en), .Q(register_4_q[2]), .clk(clk));  // open: clr
  Register #(.width(1)) register_3 (.D(undriven[1]), .en(en), .Q(register_4_q[1]), .clk(clk));  // open: clr
  Register #(.width(1)) register_4 (.D(undriven[0]), .en(en), .Q(register_4_q[0]), .clk(clk));  // open: clr
  Register #(.width(1)) register_5 (.D(undriven[7]), .en(en), .Q(register_4_q[7]), .clk(clk));  // open: clr
  Register #(.width(1)) register_6 (.D(undriven[6]), .en(en), .Q(register_4_q[6]), .clk(clk));  // open: clr
  Register #(.width(1)) register_7 (.D(undriven[5]), .en(en), .Q(register_4_q[5]), .clk(clk));  // open: clr
  Register #(.width(1)) register_8 (.D(undriven[4]), .en(en), .Q(register_4_q[4]), .clk(clk));  // open: clr
  Register #(.width(1)) register_9 (.D(undriven[11]), .en(en), .Q(register_4_q[11]), .clk(clk));  // open: clr
  Register #(.width(1)) register_10 (.D(undriven[10]), .en(en), .Q(register_4_q[10]), .clk(clk));  // open: clr
  Register #(.width(1)) register_11 (.D(undriven[9]), .en(en), .Q(register_4_q[9]), .clk(clk));  // open: clr
  Register #(.width(1)) register_12 (.D(undriven[8]), .en(en), .Q(register_4_q[8]), .clk(clk));  // open: clr
  Register #(.width(1)) register_13 (.D(undriven[15]), .en(en), .Q(register_4_q[15]), .clk(clk));  // open: clr
  Register #(.width(1)) register_14 (.D(undriven[14]), .en(en), .Q(register_4_q[14]), .clk(clk));  // open: clr
  Register #(.width(1)) register_15 (.D(undriven[13]), .en(en), .Q(register_4_q[13]), .clk(clk));  // open: clr
  Register #(.width(1)) register_16 (.D(undriven[12]), .en(en), .Q(register_4_q[12]), .clk(clk));  // open: clr
endmodule

module and_16 (
);

  wire [3:0] and_4_out, and_8_out, and_12_out, and_16_out;
  wire [15:0] undriven, undriven_2;

  and and_1 (and_4_out[3], undriven[3], undriven_2[3]);
  and and_2 (and_4_out[2], undriven[2], undriven_2[2]);
  and and_3 (and_4_out[1], undriven[1], undriven_2[1]);
  and and_4 (and_4_out[0], undriven[0], undriven_2[0]);
  and and_5 (and_8_out[3], undriven[7], undriven_2[7]);
  and and_6 (and_8_out[2], undriven[6], undriven_2[6]);
  and and_7 (and_8_out[1], undriven[5], undriven_2[5]);
  and and_8 (and_8_out[0], undriven[4], undriven_2[4]);
  and and_9 (and_12_out[3], undriven[11], undriven_2[11]);
  and and_10 (and_12_out[2], undriven[10], undriven_2[10]);
  and and_11 (and_12_out[1], undriven[9], undriven_2[9]);
  and and_12 (and_12_out[0], undriven[8], undriven_2[8]);
  and and_13 (and_16_out[3], undriven[15], undriven_2[15]);
  and and_14 (and_16_out[2], undriven[14], undriven_2[14]);
  and and_15 (and_16_out[1], undriven[13], undriven_2[13]);
  and and_16 (and_16_out[0], undriven[12], undriven_2[12]);
endmodule

module add_16 (
);

  wire adder_1_cout, adder_2_cout, adder_3_cout, adder_4_cout, adder_5_cout, adder_6_cout, adder_7_cout,
       adder_8_cout, adder_9_cout, adder_10_cout, adder_11_cout, adder_12_cout, adder_13_cout, adder_14_cout,
       adder_15_cout;
  wire [3:0] adder_1_out, adder_5_out, adder_9_out, adder_13_out;
  wire [15:0] undriven, undriven_2;

  Adder #(.width(1)) adder_1 (
    .a(undriven[0]), .b(undriven_2[0]), .out(adder_1_out[0]), .cout(adder_1_cout));  // open: cin
  Adder #(.width(1)) adder_2 (
    .a(undriven[1]), .b(undriven_2[1]), .out(adder_1_out[1]), .cin(adder_1_cout), .cout(adder_2_cout));
  Adder #(.width(1)) adder_3 (
    .a(undriven[2]), .b(undriven_2[2]), .out(adder_1_out[2]), .cin(adder_2_cout), .cout(adder_3_cout));
  Adder #(.width(1)) adder_4 (
    .a(undriven[3]), .b(undriven_2[3]), .out(adder_1_out[3]), .cin(adder_3_cout), .cout(adder_4_cout));
  Adder #(.width(1)) adder_5 (
    .a(undriven[4]), .b(undriven_2[4]), .out(adder_5_out[0]), .cin(adder_4_cout), .cout(adder_5_cout));
  Adder #(.width(1)) adder_6 (
    .a(undriven[5]), .b(undriven_2[5]), .out(adder_5_out[1]), .cin(adder_5_cout), .cout(adder_6_cout));
  Adder #(.width(1)) adder_7 (
    .a(undriven[6]), .b(undriven_2[6]), .out(adder_5_out[2]), .cin(adder_6_cout), .cout(adder_7_cout));
  Adder #(.width(1)) adder_8 (
    .a(undriven[7]), .b(undriven_2[7]), .out(adder_5_out[3]), .cin(adder_7_cout), .cout(adder_8_cout));
  Adder #(.width(1)) adder_9 (
    .a(undriven[8]), .b(undriven_2[8]), .out(adder_9_out[0]), .cin(adder_8_cout), .cout(adder_9_cout));
  Adder #(.width(1)) adder_10 (
    .a(undriven[9]), .b(undriven_2[9]), .out(adder_9_out[1]), .cin(adder_9_cout), .cout(adder_10_cout));
  Adder #(.width(1)) adder_11 (
    .a(undriven[10]), .b(undriven_2[10]), .out(adder_9_out[2]), .cin(adder_10_cout), .cout(adder_11_cout));
  Adder #(.width(1)) adder_12 (
    .a(undriven[11]), .b(undriven_2[11]), .out(adder_9_out[3]), .cin(adder_11_cout), .cout(adder_12_cout));
  Adder #(.width(1)) adder_13 (
    .a(undriven[12]), .b(undriven_2[12]), .out(adder_13_out[0]), .cin(adder_12_cout), .cout(adder_13_cout));
  Adder #(.width(1)) adder_14 (
    .a(undriven[13]), .b(undriven_2[13]), .out(adder_13_out[1]), .cin(adder_13_cout), .cout(adder_14_cout));
  Adder #(.width(1)) adder_15 (
    .a(undriven[14]), .b(undriven_2[14]), .out(adder_13_out[2]), .cin(adder_14_cout), .cout(adder_15_cout));
  Adder #(.width(1)) adder_16 (
    .a(undriven[15]), .b(undriven_2[15]), .out(adder_13_out[3]), .cin(adder_15_cout));  // open: cout
endmodule
